// Logisim project CH016M01.circ as structural Verilog: 19 circuits, main circuit CH016M01
module CH016M01 (
  input  INT,
  input  [15:0] FROM_RAM,
  input  resume,
  input  CLR,
  output STEP_1,
  output STEP_2,
  output STEP_3,
  output STEP_4,
  output [15:0] TO_RAM,
  output RAM_WE,
  output RAM_RE,
  output [15:0] TO_ADDR
);

  wire control_unit_1_alu_abs, control_unit_1_alu_add, control_unit_1_alu_and, control_unit_1_alu_carry,
       control_unit_1_alu_i_flags, control_unit_1_alu_inc, control_unit_1_alu_neg, control_unit_1_alu_not,
       control_unit_1_alu_or, control_unit_1_alu_rotate, control_unit_1_alu_shift,
       control_unit_1_alu_shift_a, control_unit_1_alu_shift_left, control_unit_1_alu_sub,
       control_unit_1_alu_x_passthrough, control_unit_1_alu_xor, control_unit_1_alu_y_embeded,
       control_unit_1_flags_load, control_unit_1_flags_load_bus, control_unit_1_flags_re,
       control_unit_1_flags_we, control_unit_1_gpr_re, control_unit_1_gpr_we, control_unit_1_imm_we,
       control_unit_1_int_disable, control_unit_1_int_enable, control_unit_1_iss_we, control_unit_1_pc_load,
       control_unit_1_pc_re, control_unit_1_pc_we, control_unit_1_ram_re, control_unit_1_ram_we,
       control_unit_1_sp_dec, control_unit_1_sp_inc, control_unit_1_step_1, control_unit_1_step_2,
       control_unit_1_step_3, control_unit_1_step_4, interrupt_service_system_1_int_out, xor_1_out;
  wire [1:0] arithmetic_logic_unit_1_flags_write, control_unit_1_ram_addr_mode,
       control_unit_1_ram_addr_mode_2, flags_register_1_alu_in;
  wire [2:0] control_unit_1_gpr_addr_mode;
  wire [3:0] control_unit_1_x_op, control_unit_1_y_op;
  wire [15:0] adder_1_out, arithmetic_logic_unit_1_result, bit_extender_1_out, flags_register_1_data_out,
       immediate_register_1_data_out, interrupt_service_system_1_data_out, multiplexer_1_out,
       multiplexer_3_out, multiplexer_4_out, multiplexer_5_out, or_1_out, program_counter_1_addr_out,
       program_counter_1_data_out, register_file_1_data_out, register_file_1_x_out, register_file_1_y_out;

  Control_Unit control_unit_1 (
    .FLAGS_WE(control_unit_1_flags_we), .FLAGS_LOAD(control_unit_1_flags_load),
    .FLAGS_LOAD_BUS(control_unit_1_flags_load_bus), .IMM_WE(control_unit_1_imm_we),
    .FLAGS_RE(control_unit_1_flags_re), .Y_OP(control_unit_1_y_op), .ALU_ADD(control_unit_1_alu_add),
    .ALU_CARRY(control_unit_1_alu_carry), .ALU_SUB(control_unit_1_alu_sub), .ALU_INC(control_unit_1_alu_inc),
    .ALU_ABS(control_unit_1_alu_abs), .ALU_NEG(control_unit_1_alu_neg),
    .ALU_I_FLAGS(control_unit_1_alu_i_flags), .ALU_SHIFT(control_unit_1_alu_shift),
    .ALU_SHIFT_LEFT(control_unit_1_alu_shift_left), .ALU_SHIFT_A(control_unit_1_alu_shift_a),
    .ALU_ROTATE(control_unit_1_alu_rotate), .ALU_Y_EMBEDED(control_unit_1_alu_y_embeded),
    .ALU_AND(control_unit_1_alu_and), .ALU_OR(control_unit_1_alu_or), .ALU_XOR(control_unit_1_alu_xor),
    .ALU_NOT(control_unit_1_alu_not), .ALU_X_PASSTHROUGH(control_unit_1_alu_x_passthrough),
    .PC_LOAD(control_unit_1_pc_load), .RAM_RE(control_unit_1_ram_re), .PC_WE(control_unit_1_pc_we),
    .GPR_WE(control_unit_1_gpr_we), .RAM_ADDR_MODE(control_unit_1_ram_addr_mode),
    .RAM_WE(control_unit_1_ram_we), .GPR_RE(control_unit_1_gpr_re), .SP_INC(control_unit_1_sp_inc),
    .SP_DEC(control_unit_1_sp_dec), .RAM_ADDR_MODE_2(control_unit_1_ram_addr_mode_2),
    .PC_RE(control_unit_1_pc_re), .INT_DISABLE(control_unit_1_int_disable),
    .INT_ENABLE(control_unit_1_int_enable), .ISS_WE(control_unit_1_iss_we), .X_OP(control_unit_1_x_op),
    .STEP_1(control_unit_1_step_1), .INSTRUCTION(FROM_RAM), .CLR(CLR), .RESUME(resume),
    .EXT_INT(interrupt_service_system_1_int_out), .FLAGS_IN(flags_register_1_alu_in),
    .STEP_2(control_unit_1_step_2), .STEP_3(control_unit_1_step_3), .STEP_4(control_unit_1_step_4),
    .GPR_ADDR_MODE(control_unit_1_gpr_addr_mode));
  buf buffer_1 (STEP_1, control_unit_1_step_1);
  buf buffer_2 (STEP_2, control_unit_1_step_2);
  buf buffer_3 (STEP_3, control_unit_1_step_3);
  buf buffer_4 (STEP_4, control_unit_1_step_4);
  Multiplexer #(.enable("false"), .width(16)) multiplexer_1 (
    .in0(register_file_1_y_out), .in1(bit_extender_1_out), .out(multiplexer_1_out),
    .sel(control_unit_1_alu_y_embeded));
  assign bit_extender_1_out = {{12{1'b0}}, control_unit_1_y_op};  // Bit_Extender bit_extender_1
  Multiplexer #(.enable("false"), .select(2), .width(16)) multiplexer_2 (
    .in0(program_counter_1_addr_out), .in1(immediate_register_1_data_out), .in2(register_file_1_y_out),
    .in3(adder_1_out), .out(TO_ADDR), .sel(control_unit_1_ram_addr_mode));
  Multiplexer #(.enable("false"), .select(2), .width(16)) multiplexer_3 (
    .in0(FROM_RAM), .in1(immediate_register_1_data_out), .in2(register_file_1_x_out),
    .in3(interrupt_service_system_1_data_out), .out(multiplexer_3_out), .sel(control_unit_1_ram_addr_mode_2));
  Adder #(.width(16)) adder_1 (
    .a(register_file_1_y_out), .b(immediate_register_1_data_out), .out(adder_1_out));  // open: cin, cout
  Program_Counter program_counter_1 (
    .ADDR_OUT(program_counter_1_addr_out), .DATA_OUT(program_counter_1_data_out),
    .DATA_IN(multiplexer_3_out), .LOAD(control_unit_1_pc_load), .WE(control_unit_1_pc_we), .CLR(CLR),
    .RE(control_unit_1_pc_re));
  Interrupt_Service_System interrupt_service_system_1 (
    .DATA_OUT(interrupt_service_system_1_data_out), .INT_OUT(interrupt_service_system_1_int_out),
    .ENABLE(control_unit_1_int_enable), .DISABLE(control_unit_1_int_disable), .WE(control_unit_1_iss_we),
    .INT_IN(INT), .CLR(CLR), .DATA_IN(FROM_RAM));
  Register_File register_file_1 (
    .DATA_OUT(register_file_1_data_out), .Y_OUT(register_file_1_y_out), .X_OUT(register_file_1_x_out),
    .DATA_IN(multiplexer_4_out), .WE(control_unit_1_gpr_we), .XOP(control_unit_1_x_op),
    .YOP(control_unit_1_y_op), .SP_INC(control_unit_1_sp_inc), .SP_DEC(control_unit_1_sp_dec), .CLR(CLR),
    .RE(control_unit_1_gpr_re));
  Multiplexer #(.enable("false"), .select(3), .width(16)) multiplexer_4 (
    .in0(FROM_RAM), .in1(flags_register_1_data_out), .in2(arithmetic_logic_unit_1_result),
    .in3(register_file_1_y_out), .in4(16'h200), .in5({16{1'b1}}), .in6({16{1'b1}}), .in7({16{1'b1}}),
    .out(multiplexer_4_out), .sel(control_unit_1_gpr_addr_mode));
  Arithmetic_Logic_Unit arithmetic_logic_unit_1 (
    .FLAGS_WRITE(arithmetic_logic_unit_1_flags_write), .RESULT(arithmetic_logic_unit_1_result),
    .NEG(control_unit_1_alu_abs), .ABS(control_unit_1_alu_neg), .INC(control_unit_1_alu_inc),
    .X_OPERAND(register_file_1_x_out), .Y_OPERAND(multiplexer_1_out), .I_FLAGS(control_unit_1_alu_i_flags),
    .ADD(control_unit_1_alu_add), .SHIFT(control_unit_1_alu_shift), .LEFT(control_unit_1_alu_shift_left),
    .FLAGS_READ(flags_register_1_alu_in), .ROTATE(control_unit_1_alu_rotate),
    .A_SHIFT(control_unit_1_alu_shift_a), .CARRY(control_unit_1_alu_carry), .AND(control_unit_1_alu_and),
    .OR(control_unit_1_alu_or), .XOR(control_unit_1_alu_xor), .NOT(control_unit_1_alu_not),
    .SUB(control_unit_1_alu_sub), .X_PASS_THROUGH(control_unit_1_alu_x_passthrough));
  Flags_Register flags_register_1 (
    .ALU_IN(flags_register_1_alu_in), .DATA_OUT(flags_register_1_data_out),
    .ALU_OUT(arithmetic_logic_unit_1_flags_write), .DATA_IN(multiplexer_5_out),
    .LOAD(control_unit_1_flags_load), .WE(control_unit_1_flags_we), .CLR(CLR), .RE(control_unit_1_flags_re));
  Multiplexer #(.enable("false"), .width(16)) multiplexer_5 (
    .in0(register_file_1_x_out), .in1(FROM_RAM), .out(multiplexer_5_out), .sel(control_unit_1_flags_load_bus));
  Immediate_Register immediate_register_1 (
    .DATA_OUT(immediate_register_1_data_out), .DATA_IN(FROM_RAM), .WE(control_unit_1_imm_we), .CLR(CLR));
  assign or_1_out = program_counter_1_data_out | register_file_1_data_out | flags_register_1_data_out;  // OR_Gate or_1, 16 bits wide
  and and_1 (RAM_WE, control_unit_1_ram_we, xor_1_out);
  xor xor_1 (xor_1_out, control_unit_1_ram_we, control_unit_1_ram_re);
  and and_2 (RAM_RE, xor_1_out, control_unit_1_ram_re);
  assign TO_RAM = RAM_WE ? or_1_out : 16'bz;  // Controlled_Buffer controlled_buffer_1
endmodule

module CH016M01_S (
  input  INT,
  input  [15:0] FROM_RAM,
  input  resume,
  input  CLR,
  output STEP_1,
  output STEP_2,
  output STEP_3,
  output STEP_4,
  output [15:0] TO_RAM,
  output RAM_WE,
  output RAM_RE,
  output [15:0] TO_ADDR
);

  wire control_unit_s_1_alu_abs, control_unit_s_1_alu_add, control_unit_s_1_alu_and,
       control_unit_s_1_alu_carry, control_unit_s_1_alu_i_flags, control_unit_s_1_alu_inc,
       control_unit_s_1_alu_neg, control_unit_s_1_alu_not, control_unit_s_1_alu_or,
       control_unit_s_1_alu_rotate, control_unit_s_1_alu_shift, control_unit_s_1_alu_shift_a,
       control_unit_s_1_alu_shift_left, control_unit_s_1_alu_sub, control_unit_s_1_alu_x_passthrough,
       control_unit_s_1_alu_xor, control_unit_s_1_alu_y_embeded, control_unit_s_1_flags_load,
       control_unit_s_1_flags_load_bus, control_unit_s_1_flags_re, control_unit_s_1_flags_we,
       control_unit_s_1_gpr_re, control_unit_s_1_gpr_we, control_unit_s_1_imm_we,
       control_unit_s_1_int_disable, control_unit_s_1_int_enable, control_unit_s_1_iss_we,
       control_unit_s_1_pc_load, control_unit_s_1_pc_re, control_unit_s_1_pc_we, control_unit_s_1_ram_re,
       control_unit_s_1_ram_we, control_unit_s_1_sp_dec, control_unit_s_1_sp_inc, control_unit_s_1_step_1,
       control_unit_s_1_step_2, control_unit_s_1_step_3, control_unit_s_1_step_4,
       interrupt_service_system_1_int_out, xor_1_out;
  wire [1:0] arithmetic_logic_unit_1_flags_write, control_unit_s_1_ram_addr_mode,
       control_unit_s_1_ram_addr_mode_2, flags_register_1_alu_in;
  wire [2:0] control_unit_s_1_gpr_addr_mode;
  wire [3:0] control_unit_s_1_x_op, control_unit_s_1_y_op;
  wire [15:0] adder_1_out, arithmetic_logic_unit_1_result, bit_extender_1_out, flags_register_1_data_out,
       immediate_register_1_data_out, interrupt_service_system_1_data_out, multiplexer_1_out,
       multiplexer_3_out, multiplexer_4_out, multiplexer_5_out, or_1_out, program_counter_1_addr_out,
       program_counter_1_data_out, register_file_1_data_out, register_file_1_x_out, register_file_1_y_out;

  Control_Unit__S control_unit_s_1 (
    .FLAGS_WE(control_unit_s_1_flags_we), .FLAGS_LOAD(control_unit_s_1_flags_load),
    .FLAGS_LOAD_BUS(control_unit_s_1_flags_load_bus), .IMM_WE(control_unit_s_1_imm_we),
    .FLAGS_RE(control_unit_s_1_flags_re), .Y_OP(control_unit_s_1_y_op), .ALU_ADD(control_unit_s_1_alu_add),
    .ALU_CARRY(control_unit_s_1_alu_carry), .ALU_SUB(control_unit_s_1_alu_sub),
    .ALU_INC(control_unit_s_1_alu_inc), .ALU_ABS(control_unit_s_1_alu_abs),
    .ALU_NEG(control_unit_s_1_alu_neg), .ALU_I_FLAGS(control_unit_s_1_alu_i_flags),
    .ALU_SHIFT(control_unit_s_1_alu_shift), .ALU_SHIFT_LEFT(control_unit_s_1_alu_shift_left),
    .ALU_SHIFT_A(control_unit_s_1_alu_shift_a), .ALU_ROTATE(control_unit_s_1_alu_rotate),
    .ALU_Y_EMBEDED(control_unit_s_1_alu_y_embeded), .ALU_AND(control_unit_s_1_alu_and),
    .ALU_OR(control_unit_s_1_alu_or), .ALU_XOR(control_unit_s_1_alu_xor), .ALU_NOT(control_unit_s_1_alu_not),
    .ALU_X_PASSTHROUGH(control_unit_s_1_alu_x_passthrough), .PC_LOAD(control_unit_s_1_pc_load),
    .RAM_RE(control_unit_s_1_ram_re), .PC_WE(control_unit_s_1_pc_we), .GPR_WE(control_unit_s_1_gpr_we),
    .RAM_ADDR_MODE(control_unit_s_1_ram_addr_mode), .RAM_WE(control_unit_s_1_ram_we),
    .GPR_RE(control_unit_s_1_gpr_re), .SP_INC(control_unit_s_1_sp_inc), .SP_DEC(control_unit_s_1_sp_dec),
    .RAM_ADDR_MODE_2(control_unit_s_1_ram_addr_mode_2), .GPR_ADDR_MODE(control_unit_s_1_gpr_addr_mode),
    .PC_RE(control_unit_s_1_pc_re), .INT_DISABLE(control_unit_s_1_int_disable),
    .INT_ENABLE(control_unit_s_1_int_enable), .ISS_WE(control_unit_s_1_iss_we), .X_OP(control_unit_s_1_x_op),
    .STEP_1(control_unit_s_1_step_1), .INSTRUCTION(FROM_RAM), .CLR(CLR), .RESUME(resume),
    .EXT_INT(interrupt_service_system_1_int_out), .FLAGS_IN(flags_register_1_alu_in),
    .STEP_2(control_unit_s_1_step_2), .STEP_3(control_unit_s_1_step_3), .STEP_4(control_unit_s_1_step_4));
  buf buffer_1 (STEP_1, control_unit_s_1_step_1);
  buf buffer_2 (STEP_2, control_unit_s_1_step_2);
  buf buffer_3 (STEP_3, control_unit_s_1_step_3);
  buf buffer_4 (STEP_4, control_unit_s_1_step_4);
  Multiplexer #(.enable("false"), .width(16)) multiplexer_1 (
    .in0(register_file_1_y_out), .in1(bit_extender_1_out), .out(multiplexer_1_out),
    .sel(control_unit_s_1_alu_y_embeded));
  assign bit_extender_1_out = {{12{1'b0}}, control_unit_s_1_y_op};  // Bit_Extender bit_extender_1
  Multiplexer #(.enable("false"), .select(2), .width(16)) multiplexer_2 (
    .in0(program_counter_1_addr_out), .in1(immediate_register_1_data_out), .in2(register_file_1_y_out),
    .in3(adder_1_out), .out(TO_ADDR), .sel(control_unit_s_1_ram_addr_mode));
  Multiplexer #(.enable("false"), .select(2), .width(16)) multiplexer_3 (
    .in0(FROM_RAM), .in1(immediate_register_1_data_out), .in2(register_file_1_x_out),
    .in3(interrupt_service_system_1_data_out), .out(multiplexer_3_out), .sel(control_unit_s_1_ram_addr_mode_2));
  Adder #(.width(16)) adder_1 (
    .a(register_file_1_y_out), .b(immediate_register_1_data_out), .out(adder_1_out));  // open: cin, cout
  Program_Counter program_counter_1 (
    .ADDR_OUT(program_counter_1_addr_out), .DATA_OUT(program_counter_1_data_out),
    .DATA_IN(multiplexer_3_out), .LOAD(control_unit_s_1_pc_load), .WE(control_unit_s_1_pc_we), .CLR(CLR),
    .RE(control_unit_s_1_pc_re));
  Interrupt_Service_System interrupt_service_system_1 (
    .DATA_OUT(interrupt_service_system_1_data_out), .INT_OUT(interrupt_service_system_1_int_out),
    .ENABLE(control_unit_s_1_int_enable), .DISABLE(control_unit_s_1_int_disable),
    .WE(control_unit_s_1_iss_we), .INT_IN(INT), .CLR(CLR), .DATA_IN(FROM_RAM));
  Register_File register_file_1 (
    .DATA_OUT(register_file_1_data_out), .Y_OUT(register_file_1_y_out), .X_OUT(register_file_1_x_out),
    .DATA_IN(multiplexer_4_out), .WE(control_unit_s_1_gpr_we), .XOP(control_unit_s_1_x_op),
    .YOP(control_unit_s_1_y_op), .SP_INC(control_unit_s_1_sp_inc), .SP_DEC(control_unit_s_1_sp_dec),
    .CLR(CLR), .RE(control_unit_s_1_gpr_re));
  Multiplexer #(.enable("false"), .select(3), .width(16)) multiplexer_4 (
    .in0(FROM_RAM), .in1(flags_register_1_data_out), .in2(arithmetic_logic_unit_1_result),
    .in3(register_file_1_y_out), .in4(16'h280), .in5({16{1'b1}}), .in6({16{1'b1}}), .in7({16{1'b1}}),
    .out(multiplexer_4_out), .sel(control_unit_s_1_gpr_addr_mode));
  Arithmetic_Logic_Unit arithmetic_logic_unit_1 (
    .FLAGS_WRITE(arithmetic_logic_unit_1_flags_write), .RESULT(arithmetic_logic_unit_1_result),
    .NEG(control_unit_s_1_alu_abs), .ABS(control_unit_s_1_alu_neg), .INC(control_unit_s_1_alu_inc),
    .X_OPERAND(register_file_1_x_out), .Y_OPERAND(multiplexer_1_out), .I_FLAGS(control_unit_s_1_alu_i_flags),
    .ADD(control_unit_s_1_alu_add), .SHIFT(control_unit_s_1_alu_shift),
    .LEFT(control_unit_s_1_alu_shift_left), .FLAGS_READ(flags_register_1_alu_in),
    .ROTATE(control_unit_s_1_alu_rotate), .A_SHIFT(control_unit_s_1_alu_shift_a),
    .CARRY(control_unit_s_1_alu_carry), .AND(control_unit_s_1_alu_and), .OR(control_unit_s_1_alu_or),
    .XOR(control_unit_s_1_alu_xor), .NOT(control_unit_s_1_alu_not), .SUB(control_unit_s_1_alu_sub),
    .X_PASS_THROUGH(control_unit_s_1_alu_x_passthrough));
  Flags_Register flags_register_1 (
    .ALU_IN(flags_register_1_alu_in), .DATA_OUT(flags_register_1_data_out),
    .ALU_OUT(arithmetic_logic_unit_1_flags_write), .DATA_IN(multiplexer_5_out),
    .LOAD(control_unit_s_1_flags_load), .WE(control_unit_s_1_flags_we), .CLR(CLR),
    .RE(control_unit_s_1_flags_re));
  Multiplexer #(.enable("false"), .width(16)) multiplexer_5 (
    .in0(register_file_1_x_out), .in1(FROM_RAM), .out(multiplexer_5_out),
    .sel(control_unit_s_1_flags_load_bus));
  Immediate_Register immediate_register_1 (
    .DATA_OUT(immediate_register_1_data_out), .DATA_IN(FROM_RAM), .WE(control_unit_s_1_imm_we), .CLR(CLR));
  assign or_1_out = program_counter_1_data_out | register_file_1_data_out | flags_register_1_data_out;  // OR_Gate or_1, 16 bits wide
  and and_1 (RAM_WE, control_unit_s_1_ram_we, xor_1_out);
  xor xor_1 (xor_1_out, control_unit_s_1_ram_we, control_unit_s_1_ram_re);
  and and_2 (RAM_RE, xor_1_out, control_unit_s_1_ram_re);
  assign TO_RAM = RAM_WE ? or_1_out : 16'bz;  // Controlled_Buffer controlled_buffer_1
endmodule

module CH016M01_SE (
  input  INT,
  input  [15:0] FROM_RAM,
  input  resume,
  input  CLR,
  output STEP_1,
  output STEP_2,
  output STEP_3,
  output STEP_4,
  output [15:0] TO_RAM,
  output RAM_WE,
  output RAM_RE,
  output [15:0] TO_ADDR
);

  wire control_unit_se_1_alu_abs, control_unit_se_1_alu_add, control_unit_se_1_alu_and,
       control_unit_se_1_alu_carry, control_unit_se_1_alu_i_flags, control_unit_se_1_alu_inc,
       control_unit_se_1_alu_neg, control_unit_se_1_alu_not, control_unit_se_1_alu_or,
       control_unit_se_1_alu_rotate, control_unit_se_1_alu_shift, control_unit_se_1_alu_shift_a,
       control_unit_se_1_alu_shift_left, control_unit_se_1_alu_sub, control_unit_se_1_alu_x_passthrough,
       control_unit_se_1_alu_xor, control_unit_se_1_flags_load, control_unit_se_1_flags_load_bus,
       control_unit_se_1_flags_re, control_unit_se_1_flags_we, control_unit_se_1_gpr_re,
       control_unit_se_1_gpr_we, control_unit_se_1_imm_we, control_unit_se_1_int_disable,
       control_unit_se_1_int_enable, control_unit_se_1_iss_we, control_unit_se_1_pc_load,
       control_unit_se_1_pc_re, control_unit_se_1_pc_we, control_unit_se_1_ram_re, control_unit_se_1_ram_we,
       control_unit_se_1_sp_dec, control_unit_se_1_sp_inc, control_unit_se_1_step_1,
       control_unit_se_1_step_2, control_unit_se_1_step_3, control_unit_se_1_step_4,
       interrupt_service_system_1_int_out, xor_1_out;
  wire [1:0] arithmetic_logic_unit_1_flags_write, control_unit_se_1_alu_y_embeded,
       control_unit_se_1_ram_addr_mode, control_unit_se_1_ram_addr_mode_2, flags_register_1_alu_in;
  wire [2:0] control_unit_se_1_gpr_addr_mode;
  wire [3:0] control_unit_se_1_x_op, control_unit_se_1_y_op;
  wire [15:0] adder_1_out, arithmetic_logic_unit_1_result, bit_extender_1_out, flags_register_1_data_out,
       immediate_register_1_data_out, interrupt_service_system_1_data_out, multiplexer_1_out,
       multiplexer_3_out, multiplexer_4_out, multiplexer_5_out, or_1_out, program_counter_1_addr_out,
       program_counter_1_data_out, register_file_1_data_out, register_file_1_x_out, register_file_1_y_out;

  Control_Unit__SE control_unit_se_1 (
    .FLAGS_WE(control_unit_se_1_flags_we), .FLAGS_LOAD(control_unit_se_1_flags_load),
    .FLAGS_LOAD_BUS(control_unit_se_1_flags_load_bus), .IMM_WE(control_unit_se_1_imm_we),
    .FLAGS_RE(control_unit_se_1_flags_re), .Y_OP(control_unit_se_1_y_op),
    .ALU_ADD(control_unit_se_1_alu_add), .ALU_CARRY(control_unit_se_1_alu_carry),
    .ALU_SUB(control_unit_se_1_alu_sub), .ALU_INC(control_unit_se_1_alu_inc),
    .ALU_ABS(control_unit_se_1_alu_abs), .ALU_NEG(control_unit_se_1_alu_neg),
    .ALU_I_FLAGS(control_unit_se_1_alu_i_flags), .ALU_SHIFT(control_unit_se_1_alu_shift),
    .ALU_SHIFT_LEFT(control_unit_se_1_alu_shift_left), .ALU_SHIFT_A(control_unit_se_1_alu_shift_a),
    .ALU_ROTATE(control_unit_se_1_alu_rotate), .ALU_Y_EMBEDED(control_unit_se_1_alu_y_embeded[0]),
    .ALU_AND(control_unit_se_1_alu_and), .ALU_OR(control_unit_se_1_alu_or),
    .ALU_XOR(control_unit_se_1_alu_xor), .ALU_NOT(control_unit_se_1_alu_not),
    .ALU_X_PASSTHROUGH(control_unit_se_1_alu_x_passthrough), .PC_LOAD(control_unit_se_1_pc_load),
    .RAM_RE(control_unit_se_1_ram_re), .PC_WE(control_unit_se_1_pc_we), .GPR_WE(control_unit_se_1_gpr_we),
    .RAM_ADDR_MODE(control_unit_se_1_ram_addr_mode), .RAM_WE(control_unit_se_1_ram_we),
    .GPR_RE(control_unit_se_1_gpr_re), .SP_INC(control_unit_se_1_sp_inc), .SP_DEC(control_unit_se_1_sp_dec),
    .RAM_ADDR_MODE_2(control_unit_se_1_ram_addr_mode_2), .GPR_ADDR_MODE(control_unit_se_1_gpr_addr_mode),
    .PC_RE(control_unit_se_1_pc_re), .INT_DISABLE(control_unit_se_1_int_disable),
    .INT_ENABLE(control_unit_se_1_int_enable), .ISS_WE(control_unit_se_1_iss_we),
    .X_OP(control_unit_se_1_x_op), .STEP_1(control_unit_se_1_step_1), .INSTRUCTION(FROM_RAM), .CLR(CLR),
    .RESUME(resume), .EXT_INT(interrupt_service_system_1_int_out), .FLAGS_IN(flags_register_1_alu_in),
    .STEP_2(control_unit_se_1_step_2), .STEP_3(control_unit_se_1_step_3), .STEP_4(control_unit_se_1_step_4),
    .ALU_IMM_EMBEDED(control_unit_se_1_alu_y_embeded[1]));
  buf buffer_1 (STEP_1, control_unit_se_1_step_1);
  buf buffer_2 (STEP_2, control_unit_se_1_step_2);
  buf buffer_3 (STEP_3, control_unit_se_1_step_3);
  buf buffer_4 (STEP_4, control_unit_se_1_step_4);
  assign bit_extender_1_out = {{12{1'b0}}, control_unit_se_1_y_op};  // Bit_Extender bit_extender_1
  Multiplexer #(.enable("false"), .select(2), .width(16)) multiplexer_1 (
    .in0(register_file_1_y_out), .in1(bit_extender_1_out), .in2(immediate_register_1_data_out),
    .in3(immediate_register_1_data_out), .out(multiplexer_1_out), .sel(control_unit_se_1_alu_y_embeded));
  Multiplexer #(.enable("false"), .select(2), .width(16)) multiplexer_2 (
    .in0(program_counter_1_addr_out), .in1(immediate_register_1_data_out), .in2(register_file_1_y_out),
    .in3(adder_1_out), .out(TO_ADDR), .sel(control_unit_se_1_ram_addr_mode));
  Multiplexer #(.enable("false"), .select(2), .width(16)) multiplexer_3 (
    .in0(FROM_RAM), .in1(immediate_register_1_data_out), .in2(register_file_1_x_out),
    .in3(interrupt_service_system_1_data_out), .out(multiplexer_3_out),
    .sel(control_unit_se_1_ram_addr_mode_2));
  Adder #(.width(16)) adder_1 (
    .a(register_file_1_y_out), .b(immediate_register_1_data_out), .out(adder_1_out));  // open: cin, cout
  Program_Counter program_counter_1 (
    .ADDR_OUT(program_counter_1_addr_out), .DATA_OUT(program_counter_1_data_out),
    .DATA_IN(multiplexer_3_out), .LOAD(control_unit_se_1_pc_load), .WE(control_unit_se_1_pc_we), .CLR(CLR),
    .RE(control_unit_se_1_pc_re));
  Interrupt_Service_System interrupt_service_system_1 (
    .DATA_OUT(interrupt_service_system_1_data_out), .INT_OUT(interrupt_service_system_1_int_out),
    .ENABLE(control_unit_se_1_int_enable), .DISABLE(control_unit_se_1_int_disable),
    .WE(control_unit_se_1_iss_we), .INT_IN(INT), .CLR(CLR), .DATA_IN(FROM_RAM));
  Register_File register_file_1 (
    .DATA_OUT(register_file_1_data_out), .Y_OUT(register_file_1_y_out), .X_OUT(register_file_1_x_out),
    .DATA_IN(multiplexer_4_out), .WE(control_unit_se_1_gpr_we), .XOP(control_unit_se_1_x_op),
    .YOP(control_unit_se_1_y_op), .SP_INC(control_unit_se_1_sp_inc), .SP_DEC(control_unit_se_1_sp_dec),
    .CLR(CLR), .RE(control_unit_se_1_gpr_re));
  Multiplexer #(.enable("false"), .select(3), .width(16)) multiplexer_4 (
    .in0(FROM_RAM), .in1(flags_register_1_data_out), .in2(arithmetic_logic_unit_1_result),
    .in3(register_file_1_y_out), .in4(16'h2c0), .in5({16{1'b1}}), .in6({16{1'b1}}), .in7({16{1'b1}}),
    .out(multiplexer_4_out), .sel(control_unit_se_1_gpr_addr_mode));
  Arithmetic_Logic_Unit arithmetic_logic_unit_1 (
    .FLAGS_WRITE(arithmetic_logic_unit_1_flags_write), .RESULT(arithmetic_logic_unit_1_result),
    .NEG(control_unit_se_1_alu_abs), .ABS(control_unit_se_1_alu_neg), .INC(control_unit_se_1_alu_inc),
    .X_OPERAND(register_file_1_x_out), .Y_OPERAND(multiplexer_1_out),
    .I_FLAGS(control_unit_se_1_alu_i_flags), .ADD(control_unit_se_1_alu_add),
    .SHIFT(control_unit_se_1_alu_shift), .LEFT(control_unit_se_1_alu_shift_left),
    .FLAGS_READ(flags_register_1_alu_in), .ROTATE(control_unit_se_1_alu_rotate),
    .A_SHIFT(control_unit_se_1_alu_shift_a), .CARRY(control_unit_se_1_alu_carry),
    .AND(control_unit_se_1_alu_and), .OR(control_unit_se_1_alu_or), .XOR(control_unit_se_1_alu_xor),
    .NOT(control_unit_se_1_alu_not), .SUB(control_unit_se_1_alu_sub),
    .X_PASS_THROUGH(control_unit_se_1_alu_x_passthrough));
  Flags_Register flags_register_1 (
    .ALU_IN(flags_register_1_alu_in), .DATA_OUT(flags_register_1_data_out),
    .ALU_OUT(arithmetic_logic_unit_1_flags_write), .DATA_IN(multiplexer_5_out),
    .LOAD(control_unit_se_1_flags_load), .WE(control_unit_se_1_flags_we), .CLR(CLR),
    .RE(control_unit_se_1_flags_re));
  Multiplexer #(.enable("false"), .width(16)) multiplexer_5 (
    .in0(register_file_1_x_out), .in1(FROM_RAM), .out(multiplexer_5_out),
    .sel(control_unit_se_1_flags_load_bus));
  Immediate_Register immediate_register_1 (
    .DATA_OUT(immediate_register_1_data_out), .DATA_IN(FROM_RAM), .WE(control_unit_se_1_imm_we), .CLR(CLR));
  assign or_1_out = program_counter_1_data_out | register_file_1_data_out | flags_register_1_data_out;  // OR_Gate or_1, 16 bits wide
  and and_1 (RAM_WE, control_unit_se_1_ram_we, xor_1_out);
  xor xor_1 (xor_1_out, control_unit_se_1_ram_we, control_unit_se_1_ram_re);
  and and_2 (RAM_RE, xor_1_out, control_unit_se_1_ram_re);
  assign TO_RAM = RAM_WE ? or_1_out : 16'bz;  // Controlled_Buffer controlled_buffer_1
endmodule

module Instruction_Register (
  input  [15:0] DATA_IN,
  input  WE,
  input  CLR,
  output [4:0] ALU_OPERATION,
  output [7:0] INSTRUCTION_OUT,
  output [3:0] X_OPERAND,
  output [3:0] Y_OPERAND
);

  wire clock_1_out;

  Register #(.width(16)) Instruction (
    .D(DATA_IN), .en(WE), .clk(clock_1_out), .Q({INSTRUCTION_OUT[7:5], ALU_OPERATION, Y_OPERAND, X_OPERAND}),
    .clr(CLR));
  Clock clock_1 (.out(clock_1_out));

  assign INSTRUCTION_OUT[4:0] = ALU_OPERATION;
endmodule

module Control_Unit (
  input  EXT_INT,
  input  [15:0] INSTRUCTION,
  input  CLR,
  input  RESUME,
  input  [1:0] FLAGS_IN,
  output [3:0] X_OP,
  output STEP_1,
  output STEP_2,
  output STEP_3,
  output STEP_4,
  output IMM_WE,
  output INT_DISABLE,
  output INT_ENABLE,
  output ISS_WE,
  output FLAGS_RE,
  output FLAGS_WE,
  output RAM_RE,
  output FLAGS_LOAD,
  output FLAGS_LOAD_BUS,
  output RAM_WE,
  output ALU_ADD,
  output ALU_CARRY,
  output ALU_SUB,
  output [1:0] RAM_ADDR_MODE,
  output ALU_INC,
  output ALU_ABS,
  output ALU_NEG,
  output ALU_I_FLAGS,
  output ALU_SHIFT,
  output ALU_SHIFT_LEFT,
  output ALU_SHIFT_A,
  output ALU_ROTATE,
  output ALU_Y_EMBEDED,
  output ALU_AND,
  output ALU_OR,
  output ALU_XOR,
  output ALU_NOT,
  output ALU_X_PASSTHROUGH,
  output PC_RE,
  output [3:0] Y_OP,
  output PC_WE,
  output PC_LOAD,
  output [1:0] RAM_ADDR_MODE_2,
  output GPR_RE,
  output GPR_WE,
  output SP_INC,
  output SP_DEC,
  output [2:0] GPR_ADDR_MODE
);

  wire and_1_out, and_2_out, and_3_out, and_4_out, and_5_out, and_6_out, and_7_out, and_8_out, and_9_out,
       and_10_out, and_11_out, and_12_out, and_13_out, and_14_out, and_15_out, and_16_out, and_17_out,
       and_19_out, and_20_out, and_21_out, and_22_out, and_23_out, and_24_out, and_25_out, and_26_out,
       and_27_out, and_28_out, and_29_out, and_30_out, and_31_out, and_32_out, and_33_out, and_34_out,
       and_35_out, and_36_out, and_37_out, and_38_out, and_39_out, and_40_out, and_41_out, and_42_out,
       and_43_out, and_44_out, and_45_out, and_46_out, and_47_out, and_48_out, and_49_out, and_50_out,
       and_51_out, and_52_out, and_53_out, and_54_out, demultiplexer_1_out0, demultiplexer_1_out1,
       demultiplexer_1_out2, demultiplexer_1_out4, demultiplexer_1_out5, demultiplexer_1_out6,
       demultiplexer_1_out8, demultiplexer_1_out9, demultiplexer_1_out10, demultiplexer_1_out11,
       demultiplexer_1_out12, demultiplexer_1_out13, demultiplexer_1_out14, demultiplexer_1_out15,
       demultiplexer_1_out16, demultiplexer_1_out17, demultiplexer_1_out18, demultiplexer_1_out19,
       demultiplexer_1_out20, demultiplexer_1_out24, demultiplexer_1_out26,
       instruction_decoder_1_alu_operation, instruction_decoder_1_brk, instruction_decoder_1_call_direct,
       instruction_decoder_1_call_indirect, instruction_decoder_1_cpuid, instruction_decoder_1_hlt,
       instruction_decoder_1_int_call, instruction_decoder_1_int_disable, instruction_decoder_1_int_enable,
       instruction_decoder_1_isr, instruction_decoder_1_jmp_direct, instruction_decoder_1_jmp_indirect,
       instruction_decoder_1_ld, instruction_decoder_1_ld_imm, instruction_decoder_1_ld_st_imm_ptr,
       instruction_decoder_1_ld_st_indirect, instruction_decoder_1_ld_st_indirect_offset,
       instruction_decoder_1_mov_flags_reg, instruction_decoder_1_mov_reg_flags,
       instruction_decoder_1_mov_reg_reg, instruction_decoder_1_pop_flags, instruction_decoder_1_pop_reg,
       instruction_decoder_1_push_flags, instruction_decoder_1_push_reg, instruction_decoder_1_ret,
       instruction_decoder_1_rti, instruction_decoder_1_st, nand_1_out, not_1_out, not_2_out, not_3_out,
       not_4_out, not_5_out, not_6_out, not_7_out, or_2_out, or_6_out, or_7_out, or_10_out, or_11_out,
       or_12_out, or_13_out, or_14_out, or_15_out, or_16_out, or_17_out, or_18_out, or_19_out, or_20_out,
       or_25_out, or_26_out, or_27_out, or_28_out, or_29_out, or_30_out, or_31_out, or_32_out, or_33_out,
       or_34_out, or_35_out, or_38_out, or_42_out, or_43_out, or_44_out, or_45_out, or_48_out, or_49_out,
       or_50_out, or_55_out, or_56_out, or_57_out, or_59_out, or_60_out, or_61_out, or_63_out, or_65_out,
       or_67_out, or_69_out, or_70_out, or_72_out, or_73_out, or_75_out, or_78_out, or_80_out;
  wire [3:0] Y_OP_t;
  wire [4:0] ALU_Operation;
  wire [7:0] instruction_register_1_instruction_out;
  wire [15:0] multiplexer_1_out;

  not not_1 (not_1_out, EXT_INT);
  Multiplexer #(.enable("false"), .width(16)) multiplexer_1 (
    .in0(INSTRUCTION), .in1(16'h300), .out(multiplexer_1_out), .sel(EXT_INT));
  Instruction_Register instruction_register_1 (
    .ALU_OPERATION(ALU_Operation), .INSTRUCTION_OUT(instruction_register_1_instruction_out),
    .X_OPERAND(X_OP), .Y_OPERAND(Y_OP_t), .DATA_IN(multiplexer_1_out), .WE(STEP_1), .CLR(CLR));
  not not_2 (not_2_out, RESUME);
  not not_3 (not_3_out, Y_OP_t[2]);
  not not_4 (not_4_out, Y_OP_t[1]);
  not not_5 (not_5_out, Y_OP_t[0]);
  not not_6 (not_6_out, FLAGS_IN[0]);
  not not_7 (not_7_out, FLAGS_IN[1]);
  Instruction_Decoder instruction_decoder_1 (
    .MOV_FLAGS_REG(instruction_decoder_1_mov_flags_reg), .MOV_REG_REG(instruction_decoder_1_mov_reg_reg),
    .CPUID(instruction_decoder_1_cpuid), .ALU_OPERATION(instruction_decoder_1_alu_operation),
    .BRK(instruction_decoder_1_brk), .ISR(instruction_decoder_1_isr), .HLT(instruction_decoder_1_hlt),
    .INT_DISABLE(instruction_decoder_1_int_disable), .INT_ENABLE(instruction_decoder_1_int_enable),
    .INT_CALL(instruction_decoder_1_int_call), .CALL_DIRECT(instruction_decoder_1_call_direct),
    .CALL_INDIRECT(instruction_decoder_1_call_indirect), .RET(instruction_decoder_1_ret),
    .RTI(instruction_decoder_1_rti), .LD_IMM(instruction_decoder_1_ld_imm), .LD(instruction_decoder_1_ld),
    .ST(instruction_decoder_1_st), .LD_ST_IMM_PTR(instruction_decoder_1_ld_st_imm_ptr),
    .LD_ST_INDIRECT(instruction_decoder_1_ld_st_indirect),
    .LD_ST_INDIRECT_OFFSET(instruction_decoder_1_ld_st_indirect_offset),
    .PUSH_REG(instruction_decoder_1_push_reg), .PUSH_FLAGS(instruction_decoder_1_push_flags),
    .POP_REG(instruction_decoder_1_pop_reg), .POP_FLAGS(instruction_decoder_1_pop_flags),
    .JMP_DIRECT(instruction_decoder_1_jmp_direct), .JMP_INDIRECT(instruction_decoder_1_jmp_indirect),
    .MOV_REG_FLAGS(instruction_decoder_1_mov_reg_flags), .Y_OPERAND(Y_OP_t),
    .INSTRUCTION_IN(instruction_register_1_instruction_out));
  Stepper stepper_1 (
    .STEP_1(STEP_1), .STEP_2(STEP_2), .STEP_3(STEP_3), .STEP_4(STEP_4), .RESET(1'b0), .CLR(CLR),
    ._WE(or_6_out));
  or or_1 (RAM_RE, or_7_out, and_14_out);
  and and_1 (and_1_out, not_5_out, not_4_out, not_3_out);
  and and_2 (and_2_out, FLAGS_IN[1], Y_OP_t[0], not_4_out, not_3_out);
  and and_3 (and_3_out, not_7_out, not_5_out, Y_OP_t[1], not_3_out);
  and and_4 (and_4_out, FLAGS_IN[0], Y_OP_t[0], Y_OP_t[1], not_3_out);
  and and_5 (and_5_out, not_6_out, not_5_out, not_4_out, Y_OP_t[2]);
  and and_6 (and_6_out, not_7_out, not_6_out);
  and and_7 (and_7_out, and_6_out, and_8_out);
  and and_8 (and_8_out, Y_OP_t[0], not_4_out, Y_OP_t[2]);
  or or_2 (or_2_out, FLAGS_IN[1], FLAGS_IN[0]);
  and and_9 (and_9_out, or_2_out, and_10_out);
  and and_10 (and_10_out, not_5_out, Y_OP_t[1], Y_OP_t[2]);
  or or_3 (PC_WE, or_13_out, or_14_out, or_15_out, or_16_out);
  or or_4 (PC_LOAD, or_17_out, or_18_out);
  or or_5 (GPR_WE, or_19_out, GPR_ADDR_MODE[2], or_20_out);
  and and_11 (and_11_out, STEP_2, not_2_out, instruction_decoder_1_brk);
  and and_12 (and_12_out, STEP_2, instruction_decoder_1_hlt);
  or or_6 (or_6_out, and_11_out, and_12_out);
  or or_7 (or_7_out, or_25_out, or_26_out, or_27_out, or_28_out);
  or or_8 (RAM_WE, or_29_out, or_30_out, or_31_out);
  or or_9 (RAM_ADDR_MODE[1], or_32_out, or_33_out, or_34_out, or_35_out);
  or or_10 (or_10_out, and_1_out, and_2_out, and_3_out, and_4_out);
  or or_11 (or_11_out, or_10_out, or_12_out);
  or or_12 (or_12_out, and_5_out, and_7_out, and_9_out);
  or or_13 (or_13_out, and_24_out, and_25_out, and_26_out, and_28_out);
  or or_14 (or_14_out, and_17_out, ISS_WE, and_33_out, and_32_out);
  or or_15 (or_15_out, and_36_out, and_38_out, and_41_out);
  or or_16 (or_16_out, and_29_out, and_30_out, and_49_out, and_15_out);
  or or_17 (or_17_out, and_24_out, and_26_out, and_28_out);
  or or_18 (or_18_out, and_29_out, and_30_out, and_13_out);
  and and_13 (and_13_out, or_11_out, or_38_out);
  or or_19 (or_19_out, and_32_out, and_34_out, and_35_out, and_37_out);
  or or_20 (or_20_out, and_47_out, and_51_out, and_53_out, and_16_out);
  or or_21 (SP_INC, or_42_out, or_43_out);
  or or_22 (SP_DEC, or_44_out, or_45_out);
  or or_23 (INT_DISABLE, and_21_out, and_22_out);
  or or_24 (INT_ENABLE, and_20_out, and_30_out);
  or or_25 (or_25_out, and_17_out, ISS_WE, and_25_out, and_29_out);
  or or_26 (or_26_out, and_30_out, and_31_out, and_32_out, and_33_out);
  or or_27 (or_27_out, and_34_out, and_35_out, and_36_out, and_37_out);
  or or_28 (or_28_out, and_38_out, and_41_out, and_47_out, and_48_out);
  and and_14 (and_14_out, and_49_out, or_11_out);
  or or_29 (or_29_out, and_23_out, and_24_out, and_26_out);
  or or_30 (or_30_out, and_28_out, and_39_out, and_40_out);
  or or_31 (or_31_out, and_42_out, and_44_out, and_46_out);
  or or_32 (or_32_out, and_23_out, and_24_out, and_26_out, and_28_out);
  or or_33 (or_33_out, and_29_out, and_30_out, and_31_out);
  or or_34 (or_34_out, and_47_out, and_35_out, and_37_out, and_40_out);
  or or_35 (or_35_out, and_48_out, and_42_out, and_44_out, and_46_out);
  or or_36 (RAM_ADDR_MODE[0], and_34_out, and_37_out, and_39_out, and_42_out);
  or or_37 (PC_RE, and_24_out, and_26_out, and_28_out);
  and and_15 (and_15_out, or_11_out, and_50_out);
  or or_38 (or_38_out, and_49_out, and_50_out);
  or or_39 (RAM_ADDR_MODE_2[1], and_24_out, and_28_out, and_50_out);
  or or_40 (RAM_ADDR_MODE_2[0], and_24_out, and_26_out);
  or or_41 (GPR_RE, and_39_out, and_40_out, and_42_out, and_44_out);
  and and_16 (and_16_out, and_54_out, nand_1_out);
  or or_42 (or_42_out, and_29_out, and_30_out, and_31_out);
  or or_43 (or_43_out, and_47_out, and_48_out);
  or or_44 (or_44_out, and_22_out, and_23_out, and_25_out);
  or or_45 (or_45_out, and_27_out, and_43_out, and_45_out);
  or or_46 (GPR_ADDR_MODE[0], and_16_out, and_53_out);
  or or_47 (GPR_ADDR_MODE[1], and_51_out, and_53_out, and_19_out);
  and and_17 (and_17_out, STEP_1, not_1_out);
  and and_18 (ISS_WE, STEP_2, instruction_decoder_1_isr);
  or or_48 (or_48_out, Y_OP_t[0], Y_OP_t[1], Y_OP_t[2], Y_OP_t[3]);
  and and_19 (and_19_out, or_48_out, GPR_ADDR_MODE[2]);
  and and_20 (and_20_out, STEP_2, instruction_decoder_1_int_enable);
  and and_21 (and_21_out, STEP_2, instruction_decoder_1_int_disable);
  and and_22 (and_22_out, STEP_2, instruction_decoder_1_int_call);
  and and_23 (and_23_out, STEP_3, instruction_decoder_1_int_call);
  and and_24 (and_24_out, STEP_4, instruction_decoder_1_int_call);
  and and_25 (and_25_out, STEP_2, instruction_decoder_1_call_direct);
  and and_26 (and_26_out, STEP_3, instruction_decoder_1_call_direct);
  and and_27 (and_27_out, STEP_2, instruction_decoder_1_call_indirect);
  and and_28 (and_28_out, STEP_3, instruction_decoder_1_call_indirect);
  and and_29 (and_29_out, STEP_2, instruction_decoder_1_ret);
  and and_30 (and_30_out, STEP_2, instruction_decoder_1_rti);
  and and_31 (and_31_out, STEP_3, instruction_decoder_1_rti);
  and and_32 (and_32_out, STEP_2, instruction_decoder_1_ld, instruction_decoder_1_ld_imm);
  and and_33 (and_33_out, STEP_2, instruction_decoder_1_ld_st_imm_ptr, instruction_decoder_1_ld);
  and and_34 (and_34_out, STEP_3, instruction_decoder_1_ld_st_imm_ptr, instruction_decoder_1_ld);
  and and_35 (and_35_out, STEP_2, instruction_decoder_1_ld_st_indirect, instruction_decoder_1_ld);
  and and_36 (and_36_out, STEP_2, instruction_decoder_1_ld_st_indirect_offset, instruction_decoder_1_ld);
  and and_37 (and_37_out, STEP_3, instruction_decoder_1_ld_st_indirect_offset, instruction_decoder_1_ld);
  and and_38 (and_38_out, STEP_2, instruction_decoder_1_ld_st_imm_ptr, instruction_decoder_1_st);
  and and_39 (and_39_out, STEP_3, instruction_decoder_1_ld_st_imm_ptr, instruction_decoder_1_st);
  and and_40 (and_40_out, STEP_2, instruction_decoder_1_ld_st_indirect, instruction_decoder_1_st);
  and and_41 (and_41_out, STEP_2, instruction_decoder_1_ld_st_indirect_offset, instruction_decoder_1_st);
  and and_42 (and_42_out, STEP_3, instruction_decoder_1_ld_st_indirect_offset, instruction_decoder_1_st);
  and and_43 (and_43_out, STEP_2, instruction_decoder_1_push_reg);
  and and_44 (and_44_out, STEP_3, instruction_decoder_1_push_reg);
  and and_45 (and_45_out, STEP_2, instruction_decoder_1_push_flags);
  and and_46 (and_46_out, STEP_3, instruction_decoder_1_push_flags);
  and and_47 (and_47_out, STEP_2, instruction_decoder_1_pop_reg);
  and and_48 (and_48_out, STEP_2, instruction_decoder_1_pop_flags);
  and and_49 (and_49_out, STEP_2, instruction_decoder_1_jmp_direct);
  and and_50 (and_50_out, STEP_2, instruction_decoder_1_jmp_indirect);
  and and_51 (and_51_out, STEP_2, instruction_decoder_1_mov_reg_flags);
  and and_52 (and_52_out, STEP_2, instruction_decoder_1_mov_flags_reg);
  and and_53 (and_53_out, STEP_2, instruction_decoder_1_mov_reg_reg);
  and and_54 (and_54_out, STEP_2, instruction_decoder_1_alu_operation);
  nand nand_1 (nand_1_out, ALU_Operation[4], ALU_Operation[3]);
  and and_55 (GPR_ADDR_MODE[2], STEP_2, instruction_decoder_1_cpuid);
  or or_49 (or_49_out, ISS_WE, and_25_out, and_33_out);
  or or_50 (or_50_out, and_36_out, and_38_out, and_41_out);
  or or_51 (FLAGS_RE, and_23_out, and_51_out, and_46_out);
  or or_52 (FLAGS_WE, and_31_out, and_48_out, and_52_out, and_54_out);
  or or_53 (FLAGS_LOAD, and_31_out, and_48_out, and_52_out);
  or or_54 (FLAGS_LOAD_BUS, and_31_out, and_48_out);
  or or_55 (or_55_out, and_23_out, and_24_out, and_26_out, and_28_out);
  or or_56 (or_56_out, and_29_out, and_30_out, and_31_out);
  or or_57 (or_57_out, and_44_out, and_46_out, and_47_out, and_48_out);
  or or_58 (IMM_WE, or_49_out, or_50_out);
  or or_59 (or_59_out, or_55_out, or_56_out, or_57_out);
  Multiplexer #(.enable("false"), .width(4)) multiplexer_2 (.in0(Y_OP_t), .in1(4'b1111), .out(Y_OP), .sel(or_59_out));
  Demultiplexer #(.enable("false"), .select(5)) demultiplexer_1 (
    .out0(demultiplexer_1_out0), .out1(demultiplexer_1_out1), .out2(demultiplexer_1_out2), .out3(ALU_ABS),
    .out4(demultiplexer_1_out4), .out5(demultiplexer_1_out5), .out6(demultiplexer_1_out6), .out7(ALU_NEG),
    .out8(demultiplexer_1_out8), .out9(demultiplexer_1_out9), .out10(demultiplexer_1_out10),
    .out11(demultiplexer_1_out11), .out12(demultiplexer_1_out12), .out13(demultiplexer_1_out13),
    .out14(demultiplexer_1_out14), .out15(demultiplexer_1_out15), .out16(demultiplexer_1_out16),
    .out17(demultiplexer_1_out17), .out18(demultiplexer_1_out18), .out19(demultiplexer_1_out19),
    .out20(demultiplexer_1_out20), .out21(ALU_OR), .out22(ALU_XOR), .out23(ALU_NOT),
    .out24(demultiplexer_1_out24), .out25(ALU_I_FLAGS), .out26(demultiplexer_1_out26),
    .out27(ALU_X_PASSTHROUGH), .in(and_54_out), .sel(ALU_Operation));  // open: out28, out29, out30, out31
  or or_60 (or_60_out, demultiplexer_1_out0, demultiplexer_1_out1, demultiplexer_1_out2);
  or or_61 (or_61_out, ALU_ABS, demultiplexer_1_out4, demultiplexer_1_out5, demultiplexer_1_out6);
  or or_62 (ALU_ADD, or_60_out, or_61_out, or_63_out);
  or or_63 (or_63_out, ALU_NEG, demultiplexer_1_out24, ALU_I_FLAGS);
  or or_64 (ALU_CARRY, demultiplexer_1_out1, demultiplexer_1_out5);
  or or_65 (or_65_out, demultiplexer_1_out4, demultiplexer_1_out5, demultiplexer_1_out6);
  or or_66 (ALU_SUB, or_65_out, or_67_out);
  or or_67 (or_67_out, demultiplexer_1_out24, ALU_I_FLAGS);
  or or_68 (ALU_INC, demultiplexer_1_out2, demultiplexer_1_out6);
  or or_69 (or_69_out, demultiplexer_1_out8, demultiplexer_1_out9, demultiplexer_1_out10, demultiplexer_1_out11);
  or or_70 (or_70_out, demultiplexer_1_out12, demultiplexer_1_out13, demultiplexer_1_out14, demultiplexer_1_out15);
  or or_71 (ALU_SHIFT, or_69_out, or_70_out, or_72_out);
  or or_72 (or_72_out, demultiplexer_1_out16, demultiplexer_1_out17, demultiplexer_1_out18, demultiplexer_1_out19);
  or or_73 (or_73_out, demultiplexer_1_out8, demultiplexer_1_out9, demultiplexer_1_out10);
  or or_74 (ALU_SHIFT_LEFT, or_73_out, or_75_out);
  or or_75 (or_75_out, demultiplexer_1_out11, demultiplexer_1_out16, demultiplexer_1_out17);
  or or_76 (ALU_SHIFT_A, demultiplexer_1_out10, demultiplexer_1_out11, demultiplexer_1_out14, demultiplexer_1_out15);
  or or_77 (ALU_ROTATE, demultiplexer_1_out16, demultiplexer_1_out17, demultiplexer_1_out18, demultiplexer_1_out19);
  or or_78 (or_78_out, demultiplexer_1_out9, demultiplexer_1_out11, demultiplexer_1_out13);
  or or_79 (ALU_Y_EMBEDED, or_78_out, or_80_out);
  or or_80 (or_80_out, demultiplexer_1_out15, demultiplexer_1_out17, demultiplexer_1_out19);
  or or_81 (ALU_AND, demultiplexer_1_out20, demultiplexer_1_out26);

  // Other names for the same wires on the sheet: Y_OPERAND[3:0] = Y_OP_t

  // Notes on the sheet:
  //   Jump Control Logic
  //   Immediate Register
  //   RAM Addressing Mode Logic
  //   PC Read Logic
  //   PC Write Logic
  //   PC Load Logic
  //   PC Addressing Mode
  //   GPR Read Logic
  //   GPR Write Logic
  //   Stack Pointer Logic
  //   GPR Addressing Mode
  //   Internal Signals
  //   Interrupt Control Logic
  //   RAM Read Logic
  //   RAM Write Logic
  //   Register File
  //   IMM Write Logic
  //   Flags Read Logic
  //   Flags Write Logic
  //   Flags Load Logic
  //   Y Operand Addressing Mode
  //   ALU Operations Logic
endmodule

module Control_Unit__S (
  input  EXT_INT,
  input  [15:0] INSTRUCTION,
  input  CLR,
  input  RESUME,
  input  [1:0] FLAGS_IN,
  output [3:0] X_OP,
  output STEP_1,
  output STEP_2,
  output STEP_3,
  output STEP_4,
  output IMM_WE,
  output INT_DISABLE,
  output INT_ENABLE,
  output ISS_WE,
  output FLAGS_RE,
  output FLAGS_WE,
  output RAM_RE,
  output FLAGS_LOAD,
  output FLAGS_LOAD_BUS,
  output RAM_WE,
  output ALU_ADD,
  output ALU_CARRY,
  output ALU_SUB,
  output [1:0] RAM_ADDR_MODE,
  output ALU_INC,
  output ALU_ABS,
  output ALU_NEG,
  output ALU_I_FLAGS,
  output ALU_SHIFT,
  output ALU_SHIFT_LEFT,
  output ALU_SHIFT_A,
  output ALU_ROTATE,
  output ALU_Y_EMBEDED,
  output ALU_AND,
  output ALU_OR,
  output ALU_XOR,
  output ALU_NOT,
  output ALU_X_PASSTHROUGH,
  output PC_RE,
  output [3:0] Y_OP,
  output PC_WE,
  output PC_LOAD,
  output [1:0] RAM_ADDR_MODE_2,
  output GPR_RE,
  output GPR_WE,
  output SP_INC,
  output SP_DEC,
  output [2:0] GPR_ADDR_MODE
);

  wire and_1_out, and_2_out, and_3_out, and_4_out, and_5_out, and_6_out, and_7_out, and_8_out, and_9_out,
       and_10_out, and_11_out, and_12_out, and_13_out, and_14_out, and_15_out, and_16_out, and_17_out,
       and_18_out, and_20_out, and_21_out, and_22_out, and_23_out, and_24_out, and_25_out, and_26_out,
       and_27_out, and_28_out, and_29_out, and_30_out, and_31_out, and_32_out, and_33_out, and_34_out,
       and_35_out, and_36_out, and_37_out, and_38_out, and_39_out, and_40_out, and_41_out, and_42_out,
       and_43_out, and_44_out, and_45_out, and_46_out, and_47_out, and_48_out, and_49_out, and_50_out,
       and_51_out, and_52_out, and_53_out, and_54_out, and_55_out, demultiplexer_1_out0,
       demultiplexer_1_out1, demultiplexer_1_out2, demultiplexer_1_out4, demultiplexer_1_out5,
       demultiplexer_1_out6, demultiplexer_1_out8, demultiplexer_1_out9, demultiplexer_1_out10,
       demultiplexer_1_out11, demultiplexer_1_out12, demultiplexer_1_out13, demultiplexer_1_out14,
       demultiplexer_1_out15, demultiplexer_1_out16, demultiplexer_1_out17, demultiplexer_1_out18,
       demultiplexer_1_out19, demultiplexer_1_out20, demultiplexer_1_out24, demultiplexer_1_out26,
       instruction_decoder_1_alu_operation, instruction_decoder_1_brk, instruction_decoder_1_call_direct,
       instruction_decoder_1_call_indirect, instruction_decoder_1_cpuid, instruction_decoder_1_hlt,
       instruction_decoder_1_int_call, instruction_decoder_1_int_disable, instruction_decoder_1_int_enable,
       instruction_decoder_1_isr, instruction_decoder_1_jmp_direct, instruction_decoder_1_jmp_indirect,
       instruction_decoder_1_ld, instruction_decoder_1_ld_imm, instruction_decoder_1_ld_st_imm_ptr,
       instruction_decoder_1_ld_st_indirect, instruction_decoder_1_ld_st_indirect_offset,
       instruction_decoder_1_mov_flags_reg, instruction_decoder_1_mov_reg_flags,
       instruction_decoder_1_mov_reg_reg, instruction_decoder_1_pop_flags, instruction_decoder_1_pop_reg,
       instruction_decoder_1_push_flags, instruction_decoder_1_push_reg, instruction_decoder_1_ret,
       instruction_decoder_1_rti, instruction_decoder_1_st, nand_1_out, not_1_out, not_2_out, not_3_out,
       not_4_out, not_5_out, not_6_out, not_7_out, or_2_out, or_6_out, or_7_out, or_8_out, or_11_out,
       or_12_out, or_13_out, or_14_out, or_15_out, or_16_out, or_17_out, or_18_out, or_19_out, or_20_out,
       or_21_out, or_24_out, or_25_out, or_26_out, or_27_out, or_30_out, or_31_out, or_32_out, or_33_out,
       or_34_out, or_35_out, or_36_out, or_37_out, or_38_out, or_39_out, or_40_out, or_43_out, or_47_out,
       or_48_out, or_49_out, or_50_out, or_53_out, or_54_out, or_56_out, or_61_out, or_62_out, or_63_out,
       or_64_out, or_65_out, or_66_out, or_67_out, or_69_out, or_70_out, or_72_out, or_73_out, or_74_out,
       or_75_out, or_76_out, or_79_out, or_80_out;
  wire [3:0] Y_OP_t;
  wire [4:0] ALU_Operation;
  wire [7:0] instruction_register_1_instruction_out;
  wire [15:0] multiplexer_1_out;

  not not_1 (not_1_out, EXT_INT);
  Multiplexer #(.enable("false"), .width(16)) multiplexer_1 (
    .in0(INSTRUCTION), .in1(16'h300), .out(multiplexer_1_out), .sel(EXT_INT));
  Instruction_Register instruction_register_1 (
    .ALU_OPERATION(ALU_Operation), .INSTRUCTION_OUT(instruction_register_1_instruction_out),
    .X_OPERAND(X_OP), .Y_OPERAND(Y_OP_t), .DATA_IN(multiplexer_1_out), .WE(STEP_1), .CLR(CLR));
  not not_2 (not_2_out, RESUME);
  not not_3 (not_3_out, Y_OP_t[2]);
  not not_4 (not_4_out, Y_OP_t[1]);
  not not_5 (not_5_out, Y_OP_t[0]);
  not not_6 (not_6_out, FLAGS_IN[0]);
  not not_7 (not_7_out, FLAGS_IN[1]);
  Instruction_Decoder instruction_decoder_1 (
    .MOV_FLAGS_REG(instruction_decoder_1_mov_flags_reg), .MOV_REG_REG(instruction_decoder_1_mov_reg_reg),
    .CPUID(instruction_decoder_1_cpuid), .ALU_OPERATION(instruction_decoder_1_alu_operation),
    .BRK(instruction_decoder_1_brk), .ISR(instruction_decoder_1_isr), .HLT(instruction_decoder_1_hlt),
    .INT_DISABLE(instruction_decoder_1_int_disable), .INT_ENABLE(instruction_decoder_1_int_enable),
    .INT_CALL(instruction_decoder_1_int_call), .CALL_DIRECT(instruction_decoder_1_call_direct),
    .CALL_INDIRECT(instruction_decoder_1_call_indirect), .RET(instruction_decoder_1_ret),
    .RTI(instruction_decoder_1_rti), .LD_IMM(instruction_decoder_1_ld_imm), .LD(instruction_decoder_1_ld),
    .ST(instruction_decoder_1_st), .LD_ST_IMM_PTR(instruction_decoder_1_ld_st_imm_ptr),
    .LD_ST_INDIRECT(instruction_decoder_1_ld_st_indirect),
    .LD_ST_INDIRECT_OFFSET(instruction_decoder_1_ld_st_indirect_offset),
    .PUSH_REG(instruction_decoder_1_push_reg), .PUSH_FLAGS(instruction_decoder_1_push_flags),
    .POP_REG(instruction_decoder_1_pop_reg), .POP_FLAGS(instruction_decoder_1_pop_flags),
    .JMP_DIRECT(instruction_decoder_1_jmp_direct), .JMP_INDIRECT(instruction_decoder_1_jmp_indirect),
    .MOV_REG_FLAGS(instruction_decoder_1_mov_reg_flags), .Y_OPERAND(Y_OP_t),
    .INSTRUCTION_IN(instruction_register_1_instruction_out));
  Stepper stepper_1 (
    .STEP_1(STEP_1), .STEP_2(STEP_2), .STEP_3(STEP_3), .STEP_4(STEP_4), .RESET(and_1_out), .CLR(CLR),
    ._WE(or_6_out));
  and and_1 (and_1_out, or_24_out, ~or_7_out);  // AND_Gate
  or or_1 (RAM_RE, or_8_out, and_15_out);
  and and_2 (and_2_out, not_5_out, not_4_out, not_3_out);
  and and_3 (and_3_out, FLAGS_IN[1], Y_OP_t[0], not_4_out, not_3_out);
  and and_4 (and_4_out, not_7_out, not_5_out, Y_OP_t[1], not_3_out);
  and and_5 (and_5_out, FLAGS_IN[0], Y_OP_t[0], Y_OP_t[1], not_3_out);
  and and_6 (and_6_out, not_6_out, not_5_out, not_4_out, Y_OP_t[2]);
  and and_7 (and_7_out, not_7_out, not_6_out);
  and and_8 (and_8_out, and_7_out, and_9_out);
  and and_9 (and_9_out, Y_OP_t[0], not_4_out, Y_OP_t[2]);
  or or_2 (or_2_out, FLAGS_IN[1], FLAGS_IN[0]);
  and and_10 (and_10_out, or_2_out, and_11_out);
  and and_11 (and_11_out, not_5_out, Y_OP_t[1], Y_OP_t[2]);
  or or_3 (PC_WE, or_14_out, or_15_out, or_16_out, or_17_out);
  or or_4 (PC_LOAD, or_18_out, or_19_out);
  or or_5 (GPR_WE, or_20_out, GPR_ADDR_MODE[2], or_21_out);
  and and_12 (and_12_out, STEP_2, not_2_out, instruction_decoder_1_brk);
  and and_13 (and_13_out, STEP_2, instruction_decoder_1_hlt);
  or or_6 (or_6_out, and_12_out, and_13_out);
  or or_7 (or_7_out, or_25_out, or_26_out, or_27_out);
  or or_8 (or_8_out, or_30_out, or_31_out, or_32_out, or_33_out);
  or or_9 (RAM_WE, or_34_out, or_35_out, or_36_out);
  or or_10 (RAM_ADDR_MODE[1], or_37_out, or_38_out, or_39_out, or_40_out);
  or or_11 (or_11_out, and_2_out, and_3_out, and_4_out, and_5_out);
  or or_12 (or_12_out, or_11_out, or_13_out);
  or or_13 (or_13_out, and_6_out, and_8_out, and_10_out);
  or or_14 (or_14_out, and_25_out, and_26_out, and_27_out, and_29_out);
  or or_15 (or_15_out, and_18_out, ISS_WE, and_34_out, and_33_out);
  or or_16 (or_16_out, and_37_out, and_39_out, and_42_out);
  or or_17 (or_17_out, and_30_out, and_31_out, and_50_out, and_16_out);
  or or_18 (or_18_out, and_25_out, and_27_out, and_29_out);
  or or_19 (or_19_out, and_30_out, and_31_out, and_14_out);
  and and_14 (and_14_out, or_12_out, or_43_out);
  or or_20 (or_20_out, and_33_out, and_35_out, and_36_out, and_38_out);
  or or_21 (or_21_out, and_48_out, and_52_out, and_54_out, and_17_out);
  or or_22 (SP_INC, or_47_out, or_48_out);
  or or_23 (SP_DEC, or_49_out, or_50_out);
  or or_24 (or_24_out, STEP_2, STEP_3);
  or or_25 (or_25_out, and_23_out, and_24_out, and_26_out, and_28_out);
  or or_26 (or_26_out, and_31_out, and_34_out, and_37_out, and_39_out);
  or or_27 (or_27_out, and_42_out, and_44_out, and_46_out, GPR_ADDR_MODE[2]);
  or or_28 (INT_DISABLE, and_22_out, and_23_out);
  or or_29 (INT_ENABLE, and_21_out, and_31_out);
  or or_30 (or_30_out, and_18_out, ISS_WE, and_26_out, and_30_out);
  or or_31 (or_31_out, and_31_out, and_32_out, and_33_out, and_34_out);
  or or_32 (or_32_out, and_35_out, and_36_out, and_37_out, and_38_out);
  or or_33 (or_33_out, and_39_out, and_42_out, and_48_out, and_49_out);
  and and_15 (and_15_out, and_50_out, or_12_out);
  or or_34 (or_34_out, and_24_out, and_25_out, and_27_out);
  or or_35 (or_35_out, and_29_out, and_40_out, and_41_out);
  or or_36 (or_36_out, and_43_out, and_45_out, and_47_out);
  or or_37 (or_37_out, and_24_out, and_25_out, and_27_out, and_29_out);
  or or_38 (or_38_out, and_30_out, and_31_out, and_32_out);
  or or_39 (or_39_out, and_48_out, and_36_out, and_38_out, and_41_out);
  or or_40 (or_40_out, and_49_out, and_43_out, and_45_out, and_47_out);
  or or_41 (RAM_ADDR_MODE[0], and_35_out, and_38_out, and_40_out, and_43_out);
  or or_42 (PC_RE, and_25_out, and_27_out, and_29_out);
  and and_16 (and_16_out, or_12_out, and_51_out);
  or or_43 (or_43_out, and_50_out, and_51_out);
  or or_44 (RAM_ADDR_MODE_2[1], and_25_out, and_29_out, and_51_out);
  or or_45 (RAM_ADDR_MODE_2[0], and_25_out, and_27_out);
  or or_46 (GPR_RE, and_40_out, and_41_out, and_43_out, and_45_out);
  and and_17 (and_17_out, and_55_out, nand_1_out);
  or or_47 (or_47_out, and_30_out, and_31_out, and_32_out);
  or or_48 (or_48_out, and_48_out, and_49_out);
  or or_49 (or_49_out, and_23_out, and_24_out, and_26_out);
  or or_50 (or_50_out, and_28_out, and_44_out, and_46_out);
  or or_51 (GPR_ADDR_MODE[1], and_17_out, and_54_out);
  or or_52 (GPR_ADDR_MODE[0], and_52_out, and_54_out, and_20_out);
  and and_18 (and_18_out, STEP_1, not_1_out);
  and and_19 (ISS_WE, STEP_2, instruction_decoder_1_isr);
  or or_53 (or_53_out, Y_OP_t[0], Y_OP_t[1], Y_OP_t[2], Y_OP_t[3]);
  and and_20 (and_20_out, or_53_out, GPR_ADDR_MODE[2]);
  and and_21 (and_21_out, STEP_2, instruction_decoder_1_int_enable);
  and and_22 (and_22_out, STEP_2, instruction_decoder_1_int_disable);
  and and_23 (and_23_out, STEP_2, instruction_decoder_1_int_call);
  and and_24 (and_24_out, STEP_3, instruction_decoder_1_int_call);
  and and_25 (and_25_out, STEP_4, instruction_decoder_1_int_call);
  and and_26 (and_26_out, STEP_2, instruction_decoder_1_call_direct);
  and and_27 (and_27_out, STEP_3, instruction_decoder_1_call_direct);
  and and_28 (and_28_out, STEP_2, instruction_decoder_1_call_indirect);
  and and_29 (and_29_out, STEP_3, instruction_decoder_1_call_indirect);
  and and_30 (and_30_out, STEP_2, instruction_decoder_1_ret);
  and and_31 (and_31_out, STEP_2, instruction_decoder_1_rti);
  and and_32 (and_32_out, STEP_3, instruction_decoder_1_rti);
  and and_33 (and_33_out, STEP_2, instruction_decoder_1_ld, instruction_decoder_1_ld_imm);
  and and_34 (and_34_out, STEP_2, instruction_decoder_1_ld_st_imm_ptr, instruction_decoder_1_ld);
  and and_35 (and_35_out, STEP_3, instruction_decoder_1_ld_st_imm_ptr, instruction_decoder_1_ld);
  and and_36 (and_36_out, STEP_2, instruction_decoder_1_ld_st_indirect, instruction_decoder_1_ld);
  and and_37 (and_37_out, STEP_2, instruction_decoder_1_ld_st_indirect_offset, instruction_decoder_1_ld);
  and and_38 (and_38_out, STEP_3, instruction_decoder_1_ld_st_indirect_offset, instruction_decoder_1_ld);
  and and_39 (and_39_out, STEP_2, instruction_decoder_1_ld_st_imm_ptr, instruction_decoder_1_st);
  and and_40 (and_40_out, STEP_3, instruction_decoder_1_ld_st_imm_ptr, instruction_decoder_1_st);
  and and_41 (and_41_out, STEP_2, instruction_decoder_1_ld_st_indirect, instruction_decoder_1_st);
  and and_42 (and_42_out, STEP_2, instruction_decoder_1_ld_st_indirect_offset, instruction_decoder_1_st);
  and and_43 (and_43_out, STEP_3, instruction_decoder_1_ld_st_indirect_offset, instruction_decoder_1_st);
  and and_44 (and_44_out, STEP_2, instruction_decoder_1_push_reg);
  and and_45 (and_45_out, STEP_3, instruction_decoder_1_push_reg);
  and and_46 (and_46_out, STEP_2, instruction_decoder_1_push_flags);
  and and_47 (and_47_out, STEP_3, instruction_decoder_1_push_flags);
  and and_48 (and_48_out, STEP_2, instruction_decoder_1_pop_reg);
  and and_49 (and_49_out, STEP_2, instruction_decoder_1_pop_flags);
  and and_50 (and_50_out, STEP_2, instruction_decoder_1_jmp_direct);
  and and_51 (and_51_out, STEP_2, instruction_decoder_1_jmp_indirect);
  and and_52 (and_52_out, STEP_2, instruction_decoder_1_mov_reg_flags);
  and and_53 (and_53_out, STEP_2, instruction_decoder_1_mov_flags_reg);
  and and_54 (and_54_out, STEP_2, instruction_decoder_1_mov_reg_reg);
  and and_55 (and_55_out, STEP_2, instruction_decoder_1_alu_operation);
  nand nand_1 (nand_1_out, ALU_Operation[4], ALU_Operation[3]);
  and and_56 (GPR_ADDR_MODE[2], STEP_2, instruction_decoder_1_cpuid);
  or or_54 (or_54_out, ISS_WE, and_26_out, and_34_out);
  or or_55 (IMM_WE, or_54_out, or_56_out);
  or or_56 (or_56_out, and_37_out, and_39_out, and_42_out);
  or or_57 (FLAGS_RE, and_24_out, and_52_out, and_47_out);
  or or_58 (FLAGS_WE, and_32_out, and_49_out, and_53_out, and_55_out);
  or or_59 (FLAGS_LOAD, and_32_out, and_49_out, and_53_out);
  or or_60 (FLAGS_LOAD_BUS, and_32_out, and_49_out);
  or or_61 (or_61_out, and_24_out, and_25_out, and_27_out, and_29_out);
  or or_62 (or_62_out, and_30_out, and_31_out, and_32_out);
  or or_63 (or_63_out, or_61_out, or_62_out, or_64_out);
  or or_64 (or_64_out, and_45_out, and_47_out, and_48_out, and_49_out);
  Demultiplexer #(.enable("false"), .select(5)) demultiplexer_1 (
    .out0(demultiplexer_1_out0), .out1(demultiplexer_1_out1), .out2(demultiplexer_1_out2), .out3(ALU_ABS),
    .out4(demultiplexer_1_out4), .out5(demultiplexer_1_out5), .out6(demultiplexer_1_out6), .out7(ALU_NEG),
    .out8(demultiplexer_1_out8), .out9(demultiplexer_1_out9), .out10(demultiplexer_1_out10),
    .out11(demultiplexer_1_out11), .out12(demultiplexer_1_out12), .out13(demultiplexer_1_out13),
    .out14(demultiplexer_1_out14), .out15(demultiplexer_1_out15), .out16(demultiplexer_1_out16),
    .out17(demultiplexer_1_out17), .out18(demultiplexer_1_out18), .out19(demultiplexer_1_out19),
    .out20(demultiplexer_1_out20), .out21(ALU_OR), .out22(ALU_XOR), .out23(ALU_NOT),
    .out24(demultiplexer_1_out24), .out25(ALU_I_FLAGS), .out26(demultiplexer_1_out26),
    .out27(ALU_X_PASSTHROUGH), .in(and_55_out), .sel(ALU_Operation));  // open: out28, out29, out30, out31
  Multiplexer #(.enable("false"), .width(4)) multiplexer_2 (.in0(Y_OP_t), .in1(4'b1111), .out(Y_OP), .sel(or_63_out));
  or or_65 (or_65_out, demultiplexer_1_out0, demultiplexer_1_out1, demultiplexer_1_out2);
  or or_66 (or_66_out, ALU_ABS, demultiplexer_1_out4, demultiplexer_1_out5, demultiplexer_1_out6);
  or or_67 (or_67_out, ALU_NEG, demultiplexer_1_out24, ALU_I_FLAGS);
  or or_68 (ALU_CARRY, demultiplexer_1_out1, demultiplexer_1_out5);
  or or_69 (or_69_out, demultiplexer_1_out4, demultiplexer_1_out5, demultiplexer_1_out6);
  or or_70 (or_70_out, demultiplexer_1_out24, ALU_I_FLAGS);
  or or_71 (ALU_INC, demultiplexer_1_out2, demultiplexer_1_out6);
  or or_72 (or_72_out, demultiplexer_1_out8, demultiplexer_1_out9, demultiplexer_1_out10, demultiplexer_1_out11);
  or or_73 (or_73_out, demultiplexer_1_out12, demultiplexer_1_out13, demultiplexer_1_out14, demultiplexer_1_out15);
  or or_74 (or_74_out, demultiplexer_1_out16, demultiplexer_1_out17, demultiplexer_1_out18, demultiplexer_1_out19);
  or or_75 (or_75_out, demultiplexer_1_out8, demultiplexer_1_out9, demultiplexer_1_out10);
  or or_76 (or_76_out, demultiplexer_1_out11, demultiplexer_1_out16, demultiplexer_1_out17);
  or or_77 (ALU_SHIFT_A, demultiplexer_1_out10, demultiplexer_1_out11, demultiplexer_1_out14, demultiplexer_1_out15);
  or or_78 (ALU_ROTATE, demultiplexer_1_out16, demultiplexer_1_out17, demultiplexer_1_out18, demultiplexer_1_out19);
  or or_79 (or_79_out, demultiplexer_1_out9, demultiplexer_1_out11, demultiplexer_1_out13);
  or or_80 (or_80_out, demultiplexer_1_out15, demultiplexer_1_out17, demultiplexer_1_out19);
  or or_81 (ALU_AND, demultiplexer_1_out20, demultiplexer_1_out26);
  or or_82 (ALU_ADD, or_65_out, or_66_out, or_67_out);
  or or_83 (ALU_SUB, or_69_out, or_70_out);
  or or_84 (ALU_SHIFT, or_72_out, or_73_out, or_74_out);
  or or_85 (ALU_SHIFT_LEFT, or_75_out, or_76_out);
  or or_86 (ALU_Y_EMBEDED, or_79_out, or_80_out);

  // Notes on the sheet:
  //   Jump Control Logic
  //   Stepper Reset
  //   Immediate Register
  //   RAM Addressing Mode Logic
  //   PC Read Logic
  //   PC Write Logic
  //   PC Load Logic
  //   PC Addressing Mode
  //   GPR Read Logic
  //   GPR Write Logic
  //   Stack Pointer Logic
  //   GPR Addressing Mode
  //   Internal Signals
  //   Interrupt Control Logic
  //   RAM Read Logic
  //   RAM Write Logic
  //   Register File
  //   Flags Read Logic
  //   Flags Write Logic
  //   Flags Load Logic
  //   IMM Write Logic
  //   Y Operand Addressing Mode
  //   ALU Operations Logic
endmodule

module Control_Unit__SE (
  input  EXT_INT,
  input  [15:0] INSTRUCTION,
  input  CLR,
  input  RESUME,
  input  [1:0] FLAGS_IN,
  output [3:0] X_OP,
  output STEP_1,
  output STEP_2,
  output STEP_3,
  output STEP_4,
  output IMM_WE,
  output INT_DISABLE,
  output INT_ENABLE,
  output ISS_WE,
  output FLAGS_RE,
  output FLAGS_WE,
  output RAM_RE,
  output FLAGS_LOAD,
  output FLAGS_LOAD_BUS,
  output RAM_WE,
  output ALU_ADD,
  output ALU_CARRY,
  output ALU_SUB,
  output [1:0] RAM_ADDR_MODE,
  output ALU_INC,
  output ALU_ABS,
  output ALU_NEG,
  output ALU_I_FLAGS,
  output ALU_SHIFT,
  output ALU_SHIFT_LEFT,
  output ALU_SHIFT_A,
  output ALU_ROTATE,
  output ALU_Y_EMBEDED,
  output ALU_AND,
  output ALU_OR,
  output ALU_XOR,
  output ALU_NOT,
  output ALU_X_PASSTHROUGH,
  output PC_RE,
  output [3:0] Y_OP,
  output PC_WE,
  output ALU_IMM_EMBEDED,
  output PC_LOAD,
  output [1:0] RAM_ADDR_MODE_2,
  output GPR_RE,
  output GPR_WE,
  output SP_INC,
  output SP_DEC,
  output [2:0] GPR_ADDR_MODE
);

  wire and_1_out, and_2_out, and_3_out, and_4_out, and_5_out, and_6_out, and_7_out, and_8_out, and_9_out,
       and_10_out, and_11_out, and_12_out, and_13_out, and_14_out, and_15_out, and_16_out, and_17_out,
       and_18_out, and_20_out, and_21_out, and_22_out, and_23_out, and_24_out, and_25_out, and_26_out,
       and_27_out, and_28_out, and_29_out, and_30_out, and_31_out, and_32_out, and_33_out, and_34_out,
       and_35_out, and_36_out, and_37_out, and_38_out, and_39_out, and_40_out, and_41_out, and_42_out,
       and_43_out, and_44_out, and_45_out, and_46_out, and_47_out, and_48_out, and_49_out, and_50_out,
       and_51_out, and_52_out, and_53_out, and_54_out, and_55_out, and_57_out, demultiplexer_1_out0,
       demultiplexer_1_out1, demultiplexer_1_out2, demultiplexer_1_out4, demultiplexer_1_out5,
       demultiplexer_1_out6, demultiplexer_1_out8, demultiplexer_1_out9, demultiplexer_1_out10,
       demultiplexer_1_out11, demultiplexer_1_out12, demultiplexer_1_out13, demultiplexer_1_out14,
       demultiplexer_1_out15, demultiplexer_1_out16, demultiplexer_1_out17, demultiplexer_1_out18,
       demultiplexer_1_out19, demultiplexer_1_out20, demultiplexer_1_out24, demultiplexer_1_out26,
       instruction_decoder_e_1_alu_imm_operation, instruction_decoder_e_1_alu_operation,
       instruction_decoder_e_1_brk, instruction_decoder_e_1_call_direct,
       instruction_decoder_e_1_call_indirect, instruction_decoder_e_1_cpuid, instruction_decoder_e_1_hlt,
       instruction_decoder_e_1_int_call, instruction_decoder_e_1_int_disable,
       instruction_decoder_e_1_int_enable, instruction_decoder_e_1_isr, instruction_decoder_e_1_jmp_direct,
       instruction_decoder_e_1_jmp_indirect, instruction_decoder_e_1_ld, instruction_decoder_e_1_ld_imm,
       instruction_decoder_e_1_ld_st_imm_ptr, instruction_decoder_e_1_ld_st_indirect,
       instruction_decoder_e_1_ld_st_indirect_offset, instruction_decoder_e_1_mov_flags_reg,
       instruction_decoder_e_1_mov_reg_flags, instruction_decoder_e_1_mov_reg_reg,
       instruction_decoder_e_1_pop_flags, instruction_decoder_e_1_pop_reg,
       instruction_decoder_e_1_push_flags, instruction_decoder_e_1_push_reg, instruction_decoder_e_1_ret,
       instruction_decoder_e_1_rti, instruction_decoder_e_1_st, nand_1_out, not_1_out, not_2_out, not_3_out,
       not_4_out, not_5_out, not_6_out, not_7_out, or_2_out, or_6_out, or_7_out, or_8_out, or_11_out,
       or_12_out, or_13_out, or_14_out, or_15_out, or_16_out, or_17_out, or_18_out, or_19_out, or_20_out,
       or_21_out, or_24_out, or_25_out, or_26_out, or_27_out, or_30_out, or_31_out, or_32_out, or_33_out,
       or_34_out, or_35_out, or_36_out, or_37_out, or_38_out, or_39_out, or_40_out, or_43_out, or_47_out,
       or_48_out, or_49_out, or_50_out, or_53_out, or_54_out, or_55_out, or_57_out, or_58_out, or_61_out,
       or_62_out, or_63_out, or_64_out, or_67_out, or_68_out, or_69_out, or_71_out, or_73_out, or_75_out,
       or_77_out, or_78_out, or_80_out, or_81_out, or_83_out, or_86_out, or_88_out;
  wire [3:0] Y_OP_t;
  wire [4:0] ALU_Operation;
  wire [7:0] instruction_register_1_instruction_out;
  wire [15:0] multiplexer_1_out;

  not not_1 (not_1_out, EXT_INT);
  Multiplexer #(.enable("false"), .width(16)) multiplexer_1 (
    .in0(INSTRUCTION), .in1(16'h300), .out(multiplexer_1_out), .sel(EXT_INT));
  Instruction_Register instruction_register_1 (
    .ALU_OPERATION(ALU_Operation), .INSTRUCTION_OUT(instruction_register_1_instruction_out),
    .X_OPERAND(X_OP), .Y_OPERAND(Y_OP_t), .DATA_IN(multiplexer_1_out), .WE(STEP_1), .CLR(CLR));
  not not_2 (not_2_out, RESUME);
  not not_3 (not_3_out, Y_OP_t[2]);
  not not_4 (not_4_out, Y_OP_t[1]);
  not not_5 (not_5_out, Y_OP_t[0]);
  not not_6 (not_6_out, FLAGS_IN[0]);
  not not_7 (not_7_out, FLAGS_IN[1]);
  Instruction_Decoder__E instruction_decoder_e_1 (
    .MOV_FLAGS_REG(instruction_decoder_e_1_mov_flags_reg), .MOV_REG_REG(instruction_decoder_e_1_mov_reg_reg),
    .CPUID(instruction_decoder_e_1_cpuid), .ALU_OPERATION(instruction_decoder_e_1_alu_operation),
    .BRK(instruction_decoder_e_1_brk), .ISR(instruction_decoder_e_1_isr), .HLT(instruction_decoder_e_1_hlt),
    .INT_DISABLE(instruction_decoder_e_1_int_disable), .INT_ENABLE(instruction_decoder_e_1_int_enable),
    .INT_CALL(instruction_decoder_e_1_int_call), .CALL_DIRECT(instruction_decoder_e_1_call_direct),
    .CALL_INDIRECT(instruction_decoder_e_1_call_indirect), .RET(instruction_decoder_e_1_ret),
    .RTI(instruction_decoder_e_1_rti), .LD_IMM(instruction_decoder_e_1_ld_imm),
    .LD(instruction_decoder_e_1_ld), .ST(instruction_decoder_e_1_st),
    .LD_ST_IMM_PTR(instruction_decoder_e_1_ld_st_imm_ptr),
    .LD_ST_INDIRECT(instruction_decoder_e_1_ld_st_indirect),
    .LD_ST_INDIRECT_OFFSET(instruction_decoder_e_1_ld_st_indirect_offset),
    .PUSH_REG(instruction_decoder_e_1_push_reg), .PUSH_FLAGS(instruction_decoder_e_1_push_flags),
    .POP_REG(instruction_decoder_e_1_pop_reg), .POP_FLAGS(instruction_decoder_e_1_pop_flags),
    .JMP_DIRECT(instruction_decoder_e_1_jmp_direct), .JMP_INDIRECT(instruction_decoder_e_1_jmp_indirect),
    .MOV_REG_FLAGS(instruction_decoder_e_1_mov_reg_flags), .Y_OPERAND(Y_OP_t),
    .INSTRUCTION_IN(instruction_register_1_instruction_out),
    .ALU_IMM_OPERATION(instruction_decoder_e_1_alu_imm_operation));
  Stepper stepper_1 (
    .STEP_1(STEP_1), .STEP_2(STEP_2), .STEP_3(STEP_3), .STEP_4(STEP_4), .RESET(and_1_out), .CLR(CLR),
    ._WE(or_6_out));
  and and_1 (and_1_out, or_24_out, ~or_7_out);  // AND_Gate
  or or_1 (RAM_RE, or_8_out, and_57_out, and_15_out);
  and and_2 (and_2_out, not_5_out, not_4_out, not_3_out);
  and and_3 (and_3_out, FLAGS_IN[1], Y_OP_t[0], not_4_out, not_3_out);
  and and_4 (and_4_out, not_7_out, not_5_out, Y_OP_t[1], not_3_out);
  and and_5 (and_5_out, FLAGS_IN[0], Y_OP_t[0], Y_OP_t[1], not_3_out);
  and and_6 (and_6_out, not_6_out, not_5_out, not_4_out, Y_OP_t[2]);
  and and_7 (and_7_out, not_7_out, not_6_out);
  and and_8 (and_8_out, and_7_out, and_9_out);
  and and_9 (and_9_out, Y_OP_t[0], not_4_out, Y_OP_t[2]);
  or or_2 (or_2_out, FLAGS_IN[1], FLAGS_IN[0]);
  and and_10 (and_10_out, or_2_out, and_11_out);
  and and_11 (and_11_out, not_5_out, Y_OP_t[1], Y_OP_t[2]);
  or or_3 (PC_WE, or_14_out, or_15_out, or_16_out, or_17_out);
  or or_4 (PC_LOAD, or_18_out, or_19_out);
  or or_5 (GPR_WE, or_20_out, ALU_IMM_EMBEDED, GPR_ADDR_MODE[2], or_21_out);
  and and_12 (and_12_out, STEP_2, not_2_out, instruction_decoder_e_1_brk);
  and and_13 (and_13_out, STEP_2, instruction_decoder_e_1_hlt);
  or or_6 (or_6_out, and_12_out, and_13_out);
  or or_7 (or_7_out, or_25_out, or_26_out, and_57_out, or_27_out);
  or or_8 (or_8_out, or_30_out, or_31_out, or_32_out, or_33_out);
  or or_9 (RAM_WE, or_34_out, or_35_out, or_36_out);
  or or_10 (RAM_ADDR_MODE[1], or_37_out, or_38_out, or_39_out, or_40_out);
  or or_11 (or_11_out, and_2_out, and_3_out, and_4_out, and_5_out);
  or or_12 (or_12_out, or_11_out, or_13_out);
  or or_13 (or_13_out, and_6_out, and_8_out, and_10_out);
  or or_14 (or_14_out, and_25_out, and_26_out, and_27_out, and_29_out);
  or or_15 (or_15_out, and_18_out, ISS_WE, and_34_out, and_33_out);
  or or_16 (or_16_out, and_37_out, and_39_out, and_42_out, and_57_out);
  or or_17 (or_17_out, and_30_out, and_31_out, and_50_out, and_16_out);
  or or_18 (or_18_out, and_25_out, and_27_out, and_29_out);
  or or_19 (or_19_out, and_30_out, and_31_out, and_14_out);
  and and_14 (and_14_out, or_12_out, or_43_out);
  or or_20 (or_20_out, and_33_out, and_35_out, and_36_out, and_38_out);
  or or_21 (or_21_out, and_48_out, and_52_out, and_54_out, and_17_out);
  or or_22 (SP_INC, or_47_out, or_48_out);
  or or_23 (SP_DEC, or_49_out, or_50_out);
  or or_24 (or_24_out, STEP_2, STEP_3);
  or or_25 (or_25_out, and_23_out, and_24_out, and_26_out, and_28_out);
  or or_26 (or_26_out, and_31_out, and_34_out, and_37_out, and_39_out);
  or or_27 (or_27_out, and_42_out, and_44_out, and_46_out, GPR_ADDR_MODE[2]);
  or or_28 (INT_DISABLE, and_22_out, and_23_out);
  or or_29 (INT_ENABLE, and_21_out, and_31_out);
  or or_30 (or_30_out, and_18_out, ISS_WE, and_26_out, and_30_out);
  or or_31 (or_31_out, and_31_out, and_32_out, and_33_out, and_34_out);
  or or_32 (or_32_out, and_35_out, and_36_out, and_37_out, and_38_out);
  or or_33 (or_33_out, and_39_out, and_42_out, and_48_out, and_49_out);
  and and_15 (and_15_out, and_50_out, or_12_out);
  or or_34 (or_34_out, and_24_out, and_25_out, and_27_out);
  or or_35 (or_35_out, and_29_out, and_40_out, and_41_out);
  or or_36 (or_36_out, and_43_out, and_45_out, and_47_out);
  or or_37 (or_37_out, and_24_out, and_25_out, and_27_out, and_29_out);
  or or_38 (or_38_out, and_30_out, and_31_out, and_32_out);
  or or_39 (or_39_out, and_48_out, and_36_out, and_38_out, and_41_out);
  or or_40 (or_40_out, and_49_out, and_43_out, and_45_out, and_47_out);
  or or_41 (RAM_ADDR_MODE[0], and_35_out, and_38_out, and_40_out, and_43_out);
  or or_42 (PC_RE, and_25_out, and_27_out, and_29_out);
  and and_16 (and_16_out, or_12_out, and_51_out);
  or or_43 (or_43_out, and_50_out, and_51_out);
  or or_44 (RAM_ADDR_MODE_2[1], and_25_out, and_29_out, and_51_out);
  or or_45 (RAM_ADDR_MODE_2[0], and_25_out, and_27_out);
  or or_46 (GPR_RE, and_40_out, and_41_out, and_43_out, and_45_out);
  and and_17 (and_17_out, and_55_out, nand_1_out);
  or or_47 (or_47_out, and_30_out, and_31_out, and_32_out);
  or or_48 (or_48_out, and_48_out, and_49_out);
  or or_49 (or_49_out, and_23_out, and_24_out, and_26_out);
  or or_50 (or_50_out, and_28_out, and_44_out, and_46_out);
  or or_51 (GPR_ADDR_MODE[1], and_17_out, ALU_IMM_EMBEDED, and_54_out);
  or or_52 (GPR_ADDR_MODE[0], and_52_out, and_54_out, and_20_out);
  and and_18 (and_18_out, STEP_1, not_1_out);
  and and_19 (ISS_WE, STEP_2, instruction_decoder_e_1_isr);
  or or_53 (or_53_out, Y_OP_t[0], Y_OP_t[1], Y_OP_t[2], Y_OP_t[3]);
  and and_20 (and_20_out, or_53_out, GPR_ADDR_MODE[2]);
  and and_21 (and_21_out, STEP_2, instruction_decoder_e_1_int_enable);
  and and_22 (and_22_out, STEP_2, instruction_decoder_e_1_int_disable);
  and and_23 (and_23_out, STEP_2, instruction_decoder_e_1_int_call);
  and and_24 (and_24_out, STEP_3, instruction_decoder_e_1_int_call);
  and and_25 (and_25_out, STEP_4, instruction_decoder_e_1_int_call);
  and and_26 (and_26_out, STEP_2, instruction_decoder_e_1_call_direct);
  and and_27 (and_27_out, STEP_3, instruction_decoder_e_1_call_direct);
  and and_28 (and_28_out, STEP_2, instruction_decoder_e_1_call_indirect);
  and and_29 (and_29_out, STEP_3, instruction_decoder_e_1_call_indirect);
  and and_30 (and_30_out, STEP_2, instruction_decoder_e_1_ret);
  and and_31 (and_31_out, STEP_2, instruction_decoder_e_1_rti);
  and and_32 (and_32_out, STEP_3, instruction_decoder_e_1_rti);
  and and_33 (and_33_out, STEP_2, instruction_decoder_e_1_ld, instruction_decoder_e_1_ld_imm);
  and and_34 (and_34_out, STEP_2, instruction_decoder_e_1_ld_st_imm_ptr, instruction_decoder_e_1_ld);
  and and_35 (and_35_out, STEP_3, instruction_decoder_e_1_ld_st_imm_ptr, instruction_decoder_e_1_ld);
  and and_36 (and_36_out, STEP_2, instruction_decoder_e_1_ld_st_indirect, instruction_decoder_e_1_ld);
  and and_37 (and_37_out, STEP_2, instruction_decoder_e_1_ld_st_indirect_offset, instruction_decoder_e_1_ld);
  and and_38 (and_38_out, STEP_3, instruction_decoder_e_1_ld_st_indirect_offset, instruction_decoder_e_1_ld);
  and and_39 (and_39_out, STEP_2, instruction_decoder_e_1_ld_st_imm_ptr, instruction_decoder_e_1_st);
  and and_40 (and_40_out, STEP_3, instruction_decoder_e_1_ld_st_imm_ptr, instruction_decoder_e_1_st);
  and and_41 (and_41_out, STEP_2, instruction_decoder_e_1_ld_st_indirect, instruction_decoder_e_1_st);
  and and_42 (and_42_out, STEP_2, instruction_decoder_e_1_ld_st_indirect_offset, instruction_decoder_e_1_st);
  and and_43 (and_43_out, STEP_3, instruction_decoder_e_1_ld_st_indirect_offset, instruction_decoder_e_1_st);
  and and_44 (and_44_out, STEP_2, instruction_decoder_e_1_push_reg);
  and and_45 (and_45_out, STEP_3, instruction_decoder_e_1_push_reg);
  and and_46 (and_46_out, STEP_2, instruction_decoder_e_1_push_flags);
  and and_47 (and_47_out, STEP_3, instruction_decoder_e_1_push_flags);
  and and_48 (and_48_out, STEP_2, instruction_decoder_e_1_pop_reg);
  and and_49 (and_49_out, STEP_2, instruction_decoder_e_1_pop_flags);
  and and_50 (and_50_out, STEP_2, instruction_decoder_e_1_jmp_direct);
  and and_51 (and_51_out, STEP_2, instruction_decoder_e_1_jmp_indirect);
  and and_52 (and_52_out, STEP_2, instruction_decoder_e_1_mov_reg_flags);
  and and_53 (and_53_out, STEP_2, instruction_decoder_e_1_mov_flags_reg);
  and and_54 (and_54_out, STEP_2, instruction_decoder_e_1_mov_reg_reg);
  and and_55 (and_55_out, STEP_2, instruction_decoder_e_1_alu_operation);
  nand nand_1 (nand_1_out, ALU_Operation[4], ALU_Operation[3]);
  and and_56 (GPR_ADDR_MODE[2], STEP_2, instruction_decoder_e_1_cpuid);
  and and_57 (and_57_out, STEP_2, instruction_decoder_e_1_alu_imm_operation);
  and and_58 (ALU_IMM_EMBEDED, STEP_3, instruction_decoder_e_1_alu_imm_operation);
  or or_54 (or_54_out, ISS_WE, and_26_out, and_34_out);
  or or_55 (or_55_out, and_37_out, and_39_out, and_42_out);
  or or_56 (FLAGS_RE, and_24_out, and_52_out, and_47_out);
  or or_57 (or_57_out, ALU_IMM_EMBEDED, and_32_out, and_49_out);
  or or_58 (or_58_out, and_53_out, and_55_out);
  or or_59 (FLAGS_LOAD, and_32_out, and_49_out, and_53_out);
  or or_60 (FLAGS_LOAD_BUS, and_32_out, and_49_out);
  or or_61 (or_61_out, ALU_IMM_EMBEDED, and_55_out);
  or or_62 (or_62_out, and_24_out, and_25_out, and_27_out, and_29_out);
  or or_63 (or_63_out, and_30_out, and_31_out, and_32_out);
  or or_64 (or_64_out, and_45_out, and_47_out, and_48_out, and_49_out);
  or or_65 (IMM_WE, or_54_out, and_57_out, or_55_out);
  or or_66 (FLAGS_WE, or_57_out, or_58_out);
  or or_67 (or_67_out, or_62_out, or_63_out, or_64_out);
  Multiplexer #(.enable("false"), .width(4)) multiplexer_2 (.in0(Y_OP_t), .in1(4'b1111), .out(Y_OP), .sel(or_67_out));
  Demultiplexer #(.enable("false"), .select(5)) demultiplexer_1 (
    .out0(demultiplexer_1_out0), .out1(demultiplexer_1_out1), .out2(demultiplexer_1_out2), .out3(ALU_ABS),
    .out4(demultiplexer_1_out4), .out5(demultiplexer_1_out5), .out6(demultiplexer_1_out6), .out7(ALU_NEG),
    .out8(demultiplexer_1_out8), .out9(demultiplexer_1_out9), .out10(demultiplexer_1_out10),
    .out11(demultiplexer_1_out11), .out12(demultiplexer_1_out12), .out13(demultiplexer_1_out13),
    .out14(demultiplexer_1_out14), .out15(demultiplexer_1_out15), .out16(demultiplexer_1_out16),
    .out17(demultiplexer_1_out17), .out18(demultiplexer_1_out18), .out19(demultiplexer_1_out19),
    .out20(demultiplexer_1_out20), .out21(ALU_OR), .out22(ALU_XOR), .out23(ALU_NOT),
    .out24(demultiplexer_1_out24), .out25(ALU_I_FLAGS), .out26(demultiplexer_1_out26),
    .out27(ALU_X_PASSTHROUGH), .in(or_61_out), .sel(ALU_Operation));  // open: out28, out29, out30, out31
  or or_68 (or_68_out, demultiplexer_1_out0, demultiplexer_1_out1, demultiplexer_1_out2);
  or or_69 (or_69_out, ALU_ABS, demultiplexer_1_out4, demultiplexer_1_out5, demultiplexer_1_out6);
  or or_70 (ALU_ADD, or_68_out, or_69_out, or_71_out);
  or or_71 (or_71_out, ALU_NEG, demultiplexer_1_out24, ALU_I_FLAGS);
  or or_72 (ALU_CARRY, demultiplexer_1_out1, demultiplexer_1_out5);
  or or_73 (or_73_out, demultiplexer_1_out4, demultiplexer_1_out5, demultiplexer_1_out6);
  or or_74 (ALU_SUB, or_73_out, or_75_out);
  or or_75 (or_75_out, demultiplexer_1_out24, ALU_I_FLAGS);
  or or_76 (ALU_INC, demultiplexer_1_out2, demultiplexer_1_out6);
  or or_77 (or_77_out, demultiplexer_1_out8, demultiplexer_1_out9, demultiplexer_1_out10, demultiplexer_1_out11);
  or or_78 (or_78_out, demultiplexer_1_out12, demultiplexer_1_out13, demultiplexer_1_out14, demultiplexer_1_out15);
  or or_79 (ALU_SHIFT, or_77_out, or_78_out, or_80_out);
  or or_80 (or_80_out, demultiplexer_1_out16, demultiplexer_1_out17, demultiplexer_1_out18, demultiplexer_1_out19);
  or or_81 (or_81_out, demultiplexer_1_out8, demultiplexer_1_out9, demultiplexer_1_out10);
  or or_82 (ALU_SHIFT_LEFT, or_81_out, or_83_out);
  or or_83 (or_83_out, demultiplexer_1_out11, demultiplexer_1_out16, demultiplexer_1_out17);
  or or_84 (ALU_SHIFT_A, demultiplexer_1_out10, demultiplexer_1_out11, demultiplexer_1_out14, demultiplexer_1_out15);
  or or_85 (ALU_ROTATE, demultiplexer_1_out16, demultiplexer_1_out17, demultiplexer_1_out18, demultiplexer_1_out19);
  or or_86 (or_86_out, demultiplexer_1_out9, demultiplexer_1_out11, demultiplexer_1_out13);
  or or_87 (ALU_Y_EMBEDED, or_86_out, or_88_out);
  or or_88 (or_88_out, demultiplexer_1_out15, demultiplexer_1_out17, demultiplexer_1_out19);
  or or_89 (ALU_AND, demultiplexer_1_out20, demultiplexer_1_out26);

  // Notes on the sheet:
  //   Jump Control Logic
  //   Stepper Reset
  //   Immediate Register
  //   RAM Addressing Mode Logic
  //   PC Read Logic
  //   PC Write Logic
  //   PC Load Logic
  //   PC Addressing Mode
  //   GPR Read Logic
  //   GPR Write Logic
  //   Stack Pointer Logic
  //   GPR Addressing Mode
  //   Internal Signals
  //   Interrupt Control Logic
  //   RAM Read Logic
  //   RAM Write Logic
  //   Register File
  //   IMM Write Logic
  //   Flags Read Logic
  //   Flags Write Logic
  //   Flags Load Logic
  //   Y Operand Addressing Mode
  //   ALU Operations Logic
endmodule

module Stepper (
  input  RESET,
  input  CLR,
  input  _WE,
  output STEP_1,
  output STEP_2,
  output STEP_3,
  output STEP_4
);

  wire and_1_out, and_2_out, and_3_out, clock_1_out, multiplexer_1_out, multiplexer_2_out, multiplexer_3_out,
       multiplexer_4_out, nor_1_out, not_1_out, or_1_out, or_2_out;

  or or_1 (or_1_out, nor_1_out, RESET);
  or or_2 (or_2_out, or_1_out, STEP_4);
  nor nor_1 (nor_1_out, STEP_4, STEP_3, STEP_2, STEP_1);
  D_Flip_Flop d_ff_1 (.D(multiplexer_1_out), .clk(clock_1_out), .Q(STEP_1), .reset(CLR));  // open: Qn, preset
  Multiplexer #(.enable("false")) multiplexer_1 (.in0(or_2_out), .in1(STEP_1), .out(multiplexer_1_out), .sel(_WE));
  not not_1 (not_1_out, or_1_out);
  and and_1 (and_1_out, STEP_1, not_1_out);
  D_Flip_Flop d_ff_2 (.D(multiplexer_2_out), .clk(clock_1_out), .Q(STEP_2), .reset(CLR));  // open: Qn, preset
  Multiplexer #(.enable("false")) multiplexer_2 (.in0(and_1_out), .in1(STEP_2), .out(multiplexer_2_out), .sel(_WE));
  and and_2 (and_2_out, STEP_2, not_1_out);
  D_Flip_Flop d_ff_3 (.D(multiplexer_3_out), .clk(clock_1_out), .Q(STEP_3), .reset(CLR));  // open: Qn, preset
  Multiplexer #(.enable("false")) multiplexer_3 (.in0(and_2_out), .in1(STEP_3), .out(multiplexer_3_out), .sel(_WE));
  and and_3 (and_3_out, STEP_3, not_1_out);
  Multiplexer #(.enable("false")) multiplexer_4 (.in0(and_3_out), .in1(STEP_4), .out(multiplexer_4_out), .sel(_WE));
  Clock clock_1 (.out(clock_1_out));
  D_Flip_Flop d_ff_4 (.D(multiplexer_4_out), .clk(clock_1_out), .Q(STEP_4), .reset(CLR));  // open: Qn, preset
endmodule

module Instruction_Decoder (
  input  [3:0] Y_OPERAND,
  input  [7:0] INSTRUCTION_IN,
  output ISR,
  output INT_DISABLE,
  output INT_ENABLE,
  output INT_CALL,
  output CALL_DIRECT,
  output CALL_INDIRECT,
  output RET,
  output RTI,
  output LD_IMM,
  output LD,
  output ST,
  output LD_ST_IMM_PTR,
  output LD_ST_INDIRECT,
  output LD_ST_INDIRECT_OFFSET,
  output PUSH_REG,
  output PUSH_FLAGS,
  output POP_REG,
  output POP_FLAGS,
  output JMP_DIRECT,
  output JMP_INDIRECT,
  output MOV_REG_FLAGS,
  output MOV_FLAGS_REG,
  output MOV_REG_REG,
  output CPUID,
  output ALU_OPERATION,
  output BRK,
  output HLT
);

  wire and_3_out, and_7_out, and_10_out, and_13_out, and_14_out, and_15_out, and_16_out, and_17_out,
       and_18_out, and_20_out, and_23_out, decoder_1_out0, decoder_1_out7, decoder_2_out1, decoder_2_out2,
       decoder_2_out3, decoder_2_out4, decoder_2_out5, decoder_2_out6, decoder_2_out8, decoder_2_out9,
       decoder_2_out10, decoder_2_out11, decoder_2_out13, decoder_2_out14, decoder_2_out15, decoder_2_out16,
       decoder_2_out17, decoder_2_out18, decoder_2_out19, decoder_2_out20, decoder_2_out21, decoder_2_out22,
       decoder_2_out30, decoder_2_out31, decoder_3_out0, decoder_3_out1;

  Decoder #(.enable("false"), .select(3)) decoder_1 (
    .out0(decoder_1_out0), .out1(ALU_OPERATION), .out7(decoder_1_out7), .sel(INSTRUCTION_IN[7:5]));  // open: out2, out3, out4, out5, out6
  Decoder #(.enable("false"), .select(5)) decoder_2 (
    .out1(decoder_2_out1), .out2(decoder_2_out2), .out3(decoder_2_out3), .out4(decoder_2_out4),
    .out5(decoder_2_out5), .out6(decoder_2_out6), .out8(decoder_2_out8), .out9(decoder_2_out9),
    .out10(decoder_2_out10), .out11(decoder_2_out11), .out13(decoder_2_out13), .out14(decoder_2_out14),
    .out15(decoder_2_out15), .out16(decoder_2_out16), .out17(decoder_2_out17), .out18(decoder_2_out18),
    .out19(decoder_2_out19), .out20(decoder_2_out20), .out21(decoder_2_out21), .out22(decoder_2_out22),
    .out30(decoder_2_out30), .out31(decoder_2_out31), .sel(INSTRUCTION_IN[4:0]));  // open: out0, out7, out12, out23, out24, out25, out26, out27, out28, out29
  Decoder #(.enable("false")) decoder_3 (.out0(decoder_3_out0), .out1(decoder_3_out1), .sel(Y_OPERAND[0]));
  and and_1 (ISR, decoder_2_out1, decoder_1_out0);
  and and_2 (INT_DISABLE, decoder_3_out0, and_3_out);
  and and_3 (and_3_out, decoder_2_out2, decoder_1_out0);
  and and_4 (INT_ENABLE, and_3_out, decoder_3_out1);
  and and_5 (INT_CALL, decoder_2_out3, decoder_1_out0);
  and and_6 (CALL_DIRECT, decoder_3_out0, and_7_out);
  and and_7 (and_7_out, decoder_2_out4, decoder_1_out0);
  and and_8 (CALL_INDIRECT, and_7_out, decoder_3_out1);
  and and_9 (RET, decoder_3_out0, and_10_out);
  and and_10 (and_10_out, decoder_2_out5, decoder_1_out0);
  and and_11 (RTI, and_10_out, decoder_3_out1);
  and and_12 (LD_IMM, decoder_2_out8, decoder_1_out0);
  and and_13 (and_13_out, decoder_2_out9, decoder_1_out0);
  and and_14 (and_14_out, decoder_2_out10, decoder_1_out0);
  and and_15 (and_15_out, decoder_2_out11, decoder_1_out0);
  and and_16 (and_16_out, decoder_2_out13, decoder_1_out0);
  and and_17 (and_17_out, decoder_2_out14, decoder_1_out0);
  and and_18 (and_18_out, decoder_2_out15, decoder_1_out0);
  and and_19 (PUSH_REG, decoder_3_out0, and_20_out);
  and and_20 (and_20_out, decoder_2_out16, decoder_1_out0);
  and and_21 (PUSH_FLAGS, and_20_out, decoder_3_out1);
  and and_22 (POP_REG, decoder_3_out0, and_23_out);
  and and_23 (and_23_out, decoder_2_out17, decoder_1_out0);
  and and_24 (POP_FLAGS, and_23_out, decoder_3_out1);
  and and_25 (JMP_DIRECT, decoder_2_out18, decoder_1_out0);
  and and_26 (JMP_INDIRECT, decoder_2_out19, decoder_1_out0);
  and and_27 (MOV_REG_FLAGS, decoder_2_out20, decoder_1_out0);
  and and_28 (MOV_FLAGS_REG, decoder_2_out21, decoder_1_out0);
  and and_29 (MOV_REG_REG, decoder_2_out22, decoder_1_out0);
  and and_30 (CPUID, decoder_2_out6, decoder_1_out0);
  and and_31 (BRK, decoder_2_out30, decoder_1_out7);
  and and_32 (HLT, decoder_2_out31, decoder_1_out7);
  or or_1 (LD, LD_IMM, and_13_out, and_14_out, and_15_out);
  or or_2 (ST, and_16_out, and_17_out, and_18_out);
  or or_3 (LD_ST_IMM_PTR, and_13_out, and_16_out);
  or or_4 (LD_ST_INDIRECT, and_14_out, and_17_out);
  or or_5 (LD_ST_INDIRECT_OFFSET, and_15_out, and_18_out);
endmodule

module Instruction_Decoder__E (
  input  [3:0] Y_OPERAND,
  input  [7:0] INSTRUCTION_IN,
  output ISR,
  output INT_ENABLE,
  output INT_CALL,
  output CALL_INDIRECT,
  output RTI,
  output CPUID,
  output INT_DISABLE,
  output CALL_DIRECT,
  output RET,
  output PUSH_FLAGS,
  output POP_FLAGS,
  output JMP_DIRECT,
  output JMP_INDIRECT,
  output MOV_REG_FLAGS,
  output MOV_FLAGS_REG,
  output MOV_REG_REG,
  output PUSH_REG,
  output POP_REG,
  output BRK,
  output HLT,
  output LD_IMM,
  output LD,
  output ALU_IMM_OPERATION,
  output ST,
  output LD_ST_IMM_PTR,
  output LD_ST_INDIRECT,
  output LD_ST_INDIRECT_OFFSET,
  output ALU_OPERATION
);

  wire ABS, ADC_IMM, ADC_REG, ADD_IMM, ADD_REG, AND_IMM, AND_REG, CMP_IMM, CMP_REG, CMPS_IMM, CMPS_REG, DEC,
       decoder_1_out0, decoder_1_out1, decoder_2_out0, decoder_2_out1, decoder_2_out2, decoder_2_out3,
       decoder_2_out4, decoder_2_out5, decoder_2_out6, decoder_2_out7, decoder_2_out8, decoder_2_out9,
       decoder_2_out10, decoder_2_out11, decoder_2_out12, decoder_2_out13, decoder_2_out14, decoder_2_out15,
       decoder_3_out0, decoder_3_out1, decoder_3_out2, decoder_3_out3, decoder_3_out4, decoder_3_out5,
       decoder_3_out6, decoder_3_out7, decoder_3_out8, decoder_3_out9, decoder_3_out10, decoder_3_out11,
       decoder_3_out12, decoder_3_out13, decoder_3_out14, decoder_3_out15, INC, LD_IMM_ADDR, LD_IND,
       LD_IND_OFF, NEG, NOT, or_1_out, or_2_out, or_3_out, or_4_out, or_5_out, or_6_out, or_7_out, or_8_out,
       or_9_out, or_11_out, or_12_out, or_13_out, OR_IMM, OR_REG, ROL_IMM, ROL_REG, ROR_IMM, ROR_REG,
       SAL_IMM, SAL_REG, SAR_IMM, SAR_REG, SBB_IMM, SBB_REG, SHL_IMM, SHL_REG, SHR_IMM, SHR_REG, ST_IMM_ADDR,
       ST_IND, ST_IND_OFF, SUB_IMM, SUB_REG, TEST, TEST_IMM, TEST_REG, XOR_IMM, XOR_REG;

  Decoder #(.enable("false")) decoder_1 (.out0(decoder_1_out0), .out1(decoder_1_out1), .sel(Y_OPERAND[0]));
  Decoder #(.enable("false"), .select(4)) decoder_2 (
    .out0(decoder_2_out0), .out1(decoder_2_out1), .out2(decoder_2_out2), .out3(decoder_2_out3),
    .out4(decoder_2_out4), .out5(decoder_2_out5), .out6(decoder_2_out6), .out7(decoder_2_out7),
    .out8(decoder_2_out8), .out9(decoder_2_out9), .out10(decoder_2_out10), .out11(decoder_2_out11),
    .out12(decoder_2_out12), .out13(decoder_2_out13), .out14(decoder_2_out14), .out15(decoder_2_out15),
    .sel(INSTRUCTION_IN[3:0]));
  Decoder #(.enable("false"), .select(4)) decoder_3 (
    .out0(decoder_3_out0), .out1(decoder_3_out1), .out2(decoder_3_out2), .out3(decoder_3_out3),
    .out4(decoder_3_out4), .out5(decoder_3_out5), .out6(decoder_3_out6), .out7(decoder_3_out7),
    .out8(decoder_3_out8), .out9(decoder_3_out9), .out10(decoder_3_out10), .out11(decoder_3_out11),
    .out12(decoder_3_out12), .out13(decoder_3_out13), .out14(decoder_3_out14), .out15(decoder_3_out15),
    .sel(INSTRUCTION_IN[7:4]));
  and and_1 (PUSH_FLAGS, decoder_3_out1, decoder_2_out0, decoder_1_out1);
  and and_2 (PUSH_REG, decoder_3_out1, decoder_2_out0, decoder_1_out0);
  and and_3 (ADD_REG, decoder_3_out2, decoder_2_out0);
  and and_4 (ROL_REG, decoder_3_out3, decoder_2_out0);
  and and_5 (ADD_IMM, decoder_3_out4, decoder_2_out0);
  and and_6 (ISR, decoder_3_out0, decoder_2_out1);
  and and_7 (POP_FLAGS, decoder_3_out1, decoder_2_out1, decoder_1_out1);
  and and_8 (POP_REG, decoder_3_out1, decoder_2_out1, decoder_1_out0);
  and and_9 (ADC_REG, decoder_3_out2, decoder_2_out1);
  and and_10 (ROL_IMM, decoder_3_out3, decoder_2_out1);
  and and_11 (ADC_IMM, decoder_3_out4, decoder_2_out1);
  and and_12 (INT_ENABLE, decoder_3_out0, decoder_2_out2, decoder_1_out1);
  and and_13 (INT_DISABLE, decoder_3_out0, decoder_2_out2, decoder_1_out0);
  and and_14 (JMP_DIRECT, decoder_3_out1, decoder_2_out2);
  and and_15 (INC, decoder_3_out2, decoder_2_out2);
  and and_16 (ROR_REG, decoder_3_out3, decoder_2_out2);
  or or_1 (or_1_out, ADD_REG, ADC_REG, INC, ABS);
  or or_2 (or_2_out, SUB_REG, SBB_REG, DEC, NEG);
  or or_3 (or_3_out, SHL_REG, SHL_IMM, SAL_REG, SAL_IMM);
  or or_4 (or_4_out, SHR_REG, SHR_IMM, SAR_REG, SAR_IMM);
  or or_5 (or_5_out, ROL_REG, ROL_IMM, ROR_REG, ROR_IMM);
  or or_6 (or_6_out, AND_REG, OR_REG, XOR_REG, NOT);
  or or_7 (or_7_out, CMP_REG, CMPS_REG, TEST_REG, TEST);
  and and_17 (INT_CALL, decoder_3_out0, decoder_2_out3);
  and and_18 (JMP_INDIRECT, decoder_3_out1, decoder_2_out3);
  and and_19 (ABS, decoder_3_out2, decoder_2_out3);
  and and_20 (ROR_IMM, decoder_3_out3, decoder_2_out3);
  or or_8 (or_8_out, or_1_out, or_2_out, or_3_out, or_4_out);
  or or_9 (or_9_out, or_5_out, or_6_out, or_7_out);
  or or_10 (ALU_OPERATION, or_8_out, or_9_out);
  and and_21 (CALL_INDIRECT, decoder_3_out0, decoder_2_out4, decoder_1_out1);
  and and_22 (CALL_DIRECT, decoder_3_out0, decoder_2_out4, decoder_1_out0);
  and and_23 (MOV_REG_FLAGS, decoder_3_out1, decoder_2_out4);
  and and_24 (SUB_REG, decoder_3_out2, decoder_2_out4);
  and and_25 (AND_REG, decoder_3_out3, decoder_2_out4);
  and and_26 (SUB_IMM, decoder_3_out4, decoder_2_out4);
  and and_27 (AND_IMM, decoder_3_out5, decoder_2_out4);
  or or_11 (or_11_out, ADD_IMM, ADC_IMM, SUB_IMM, SBB_IMM);
  or or_12 (or_12_out, AND_IMM, OR_IMM, XOR_IMM);
  or or_13 (or_13_out, CMP_IMM, CMPS_IMM, TEST_IMM);
  and and_28 (RTI, decoder_3_out0, decoder_2_out5, decoder_1_out1);
  and and_29 (RET, decoder_3_out0, decoder_2_out5, decoder_1_out0);
  and and_30 (MOV_FLAGS_REG, decoder_3_out1, decoder_2_out5);
  and and_31 (SBB_REG, decoder_3_out2, decoder_2_out5);
  and and_32 (OR_REG, decoder_3_out3, decoder_2_out5);
  and and_33 (SBB_IMM, decoder_3_out4, decoder_2_out5);
  and and_34 (OR_IMM, decoder_3_out5, decoder_2_out5);
  or or_14 (ALU_IMM_OPERATION, or_11_out, or_12_out, or_13_out);
  and and_35 (CPUID, decoder_3_out0, decoder_2_out6);
  and and_36 (MOV_REG_REG, decoder_3_out1, decoder_2_out6);
  and and_37 (DEC, decoder_3_out2, decoder_2_out6);
  and and_38 (XOR_REG, decoder_3_out3, decoder_2_out6);
  and and_39 (XOR_IMM, decoder_3_out5, decoder_2_out6);
  and and_40 (NEG, decoder_3_out2, decoder_2_out7);
  and and_41 (NOT, decoder_3_out3, decoder_2_out7);
  and and_42 (LD_IMM, decoder_3_out0, decoder_2_out8);
  and and_43 (SHL_REG, decoder_3_out2, decoder_2_out8);
  and and_44 (CMP_REG, decoder_3_out3, decoder_2_out8);
  and and_45 (CMP_IMM, decoder_3_out5, decoder_2_out8);
  and and_46 (LD_IMM_ADDR, decoder_3_out0, decoder_2_out9);
  and and_47 (SHL_IMM, decoder_3_out2, decoder_2_out9);
  and and_48 (CMPS_REG, decoder_3_out3, decoder_2_out9);
  and and_49 (CMPS_IMM, decoder_3_out5, decoder_2_out9);
  and and_50 (LD_IND, decoder_3_out0, decoder_2_out10);
  and and_51 (SAL_REG, decoder_3_out2, decoder_2_out10);
  and and_52 (TEST_REG, decoder_3_out3, decoder_2_out10);
  and and_53 (TEST_IMM, decoder_3_out5, decoder_2_out10);
  and and_54 (LD_IND_OFF, decoder_3_out0, decoder_2_out11);
  and and_55 (SAL_IMM, decoder_3_out2, decoder_2_out11);
  and and_56 (TEST, decoder_3_out3, decoder_2_out11);
  or or_15 (LD, LD_IMM, LD_IMM_ADDR, LD_IND, LD_IND_OFF);
  or or_16 (ST, ST_IMM_ADDR, ST_IND, ST_IND_OFF);
  or or_17 (LD_ST_IMM_PTR, LD_IMM_ADDR, ST_IMM_ADDR);
  or or_18 (LD_ST_INDIRECT, LD_IND, ST_IND);
  or or_19 (LD_ST_INDIRECT_OFFSET, LD_IND_OFF, ST_IND_OFF);
  and and_57 (SHR_REG, decoder_3_out2, decoder_2_out12);
  and and_58 (ST_IMM_ADDR, decoder_3_out0, decoder_2_out13);
  and and_59 (SHR_IMM, decoder_3_out2, decoder_2_out13);
  and and_60 (ST_IND, decoder_3_out0, decoder_2_out14);
  and and_61 (SAR_REG, decoder_3_out2, decoder_2_out14);
  and and_62 (BRK, decoder_3_out15, decoder_2_out14);
  and and_63 (ST_IND_OFF, decoder_3_out0, decoder_2_out15);
  and and_64 (SAR_IMM, decoder_3_out2, decoder_2_out15);
  and and_65 (HLT, decoder_3_out15, decoder_2_out15);
endmodule

module Program_Counter (
  input  [15:0] DATA_IN,
  input  WE,
  input  LOAD,
  input  CLR,
  input  RE,
  output [15:0] ADDR_OUT,
  output [15:0] DATA_OUT
);

  wire clock_1_out;
  wire [15:0] adder_1_out, bit_extender_1_out, multiplexer_1_out;

  Adder #(.width(16)) adder_1 (.a(ADDR_OUT), .b(16'h1), .out(adder_1_out), .cin(1'b0));  // open: cout
  Multiplexer #(.enable("false"), .width(16)) multiplexer_1 (
    .in0(adder_1_out), .in1(DATA_IN), .out(multiplexer_1_out), .sel(LOAD));
  Register #(.width(16)) PC (.D(multiplexer_1_out), .en(WE), .clk(clock_1_out), .Q(ADDR_OUT), .clr(CLR));
  Clock clock_1 (.out(clock_1_out));
  assign bit_extender_1_out = {{15{RE}}, RE};  // Bit_Extender bit_extender_1
  assign DATA_OUT = ADDR_OUT & bit_extender_1_out;  // AND_Gate and_1, 16 bits wide
endmodule

module Interrupt_Service_System (
  input  [15:0] DATA_IN,
  input  WE,
  input  INT_IN,
  input  ENABLE,
  input  DISABLE,
  input  CLR,
  output [15:0] DATA_OUT,
  output INT_OUT
);

  wire clock_1_out, ENABLED_q, or_1_out, TRIGGERED_q;

  Register #(.width(16)) ISR (.D(DATA_IN), .en(WE), .clk(clock_1_out), .Q(DATA_OUT), .clr(CLR));
  Clock clock_1 (.out(clock_1_out));
  Register #(.width(1)) TRIGGERED (.D(INT_IN), .en(1'b1), .clk(clock_1_out), .Q(TRIGGERED_q), .clr(CLR));
  Register #(.width(1)) ENABLED (.D(ENABLE), .en(or_1_out), .clk(clock_1_out), .Q(ENABLED_q), .clr(CLR));
  or or_1 (or_1_out, ENABLE, DISABLE);
  and and_1 (INT_OUT, TRIGGERED_q, ENABLED_q);
endmodule

module Register_File (
  input  [15:0] DATA_IN,
  input  WE,
  input  [3:0] XOP,
  input  [3:0] YOP,
  input  SP_INC,
  input  SP_DEC,
  input  CLR,
  input  RE,
  output [15:0] Y_OUT,
  output [15:0] X_OUT,
  output [15:0] DATA_OUT
);

  wire clock_1_out, demultiplexer_1_out0, demultiplexer_1_out1, demultiplexer_1_out2, demultiplexer_1_out3,
       demultiplexer_1_out4, demultiplexer_1_out5, demultiplexer_1_out6, demultiplexer_1_out7,
       demultiplexer_1_out8, demultiplexer_1_out9, demultiplexer_1_out10, demultiplexer_1_out11,
       demultiplexer_1_out12, demultiplexer_1_out13, demultiplexer_1_out14, demultiplexer_1_out15, or_1_out,
       or_2_out;
  wire [15:0] adder_1_out, bit_extender_1_out, bit_extender_2_out, multiplexer_1_out, r0_q, r1_q, r2_q, r3_q,
       r4_q, r5_q, r6_q, r7_q, r8_q, r9_q, r10_q, r11_q, r12_q, r13_q, r14_q, r15_q;

  Demultiplexer #(.enable("false"), .select(4)) demultiplexer_1 (
    .out0(demultiplexer_1_out0), .out1(demultiplexer_1_out1), .out2(demultiplexer_1_out2),
    .out3(demultiplexer_1_out3), .out4(demultiplexer_1_out4), .out5(demultiplexer_1_out5),
    .out6(demultiplexer_1_out6), .out7(demultiplexer_1_out7), .out8(demultiplexer_1_out8),
    .out9(demultiplexer_1_out9), .out10(demultiplexer_1_out10), .out11(demultiplexer_1_out11),
    .out12(demultiplexer_1_out12), .out13(demultiplexer_1_out13), .out14(demultiplexer_1_out14),
    .out15(demultiplexer_1_out15), .in(WE), .sel(XOP));
  assign bit_extender_1_out = {{15{SP_DEC}}, SP_DEC};  // Bit_Extender bit_extender_1
  Adder #(.width(16)) adder_1 (.a(r15_q), .b(bit_extender_1_out), .out(adder_1_out), .cin(SP_INC));  // open: cout
  or or_1 (or_1_out, SP_INC, SP_DEC);
  Multiplexer #(.enable("false"), .width(16)) multiplexer_1 (
    .in0(DATA_IN), .in1(adder_1_out), .out(multiplexer_1_out), .sel(or_1_out));
  or or_2 (or_2_out, demultiplexer_1_out15, SP_INC, SP_DEC);
  Clock clock_1 (.out(clock_1_out));
  Register #(.width(16)) r0 (.D(DATA_IN), .en(demultiplexer_1_out0), .clk(clock_1_out), .Q(r0_q), .clr(CLR));
  Register #(.width(16)) r1 (.D(DATA_IN), .en(demultiplexer_1_out1), .clk(clock_1_out), .Q(r1_q), .clr(CLR));
  Register #(.width(16)) r2 (.D(DATA_IN), .en(demultiplexer_1_out2), .clk(clock_1_out), .Q(r2_q), .clr(CLR));
  Register #(.width(16)) r3 (.D(DATA_IN), .en(demultiplexer_1_out3), .clk(clock_1_out), .Q(r3_q), .clr(CLR));
  Register #(.width(16)) r4 (.D(DATA_IN), .en(demultiplexer_1_out4), .clk(clock_1_out), .Q(r4_q), .clr(CLR));
  Register #(.width(16)) r5 (.D(DATA_IN), .en(demultiplexer_1_out5), .clk(clock_1_out), .Q(r5_q), .clr(CLR));
  Register #(.width(16)) r6 (.D(DATA_IN), .en(demultiplexer_1_out6), .clk(clock_1_out), .Q(r6_q), .clr(CLR));
  Register #(.width(16)) r7 (.D(DATA_IN), .en(demultiplexer_1_out7), .clk(clock_1_out), .Q(r7_q), .clr(CLR));
  Register #(.width(16)) r8 (.D(DATA_IN), .en(demultiplexer_1_out8), .clk(clock_1_out), .Q(r8_q), .clr(CLR));
  Register #(.width(16)) r9 (.D(DATA_IN), .en(demultiplexer_1_out9), .clk(clock_1_out), .Q(r9_q), .clr(CLR));
  Register #(.width(16)) r10 (.D(DATA_IN), .en(demultiplexer_1_out10), .clk(clock_1_out), .Q(r10_q), .clr(CLR));
  Register #(.width(16)) r11 (.D(DATA_IN), .en(demultiplexer_1_out11), .clk(clock_1_out), .Q(r11_q), .clr(CLR));
  Register #(.width(16)) r12 (.D(DATA_IN), .en(demultiplexer_1_out12), .clk(clock_1_out), .Q(r12_q), .clr(CLR));
  Register #(.width(16)) r13 (.D(DATA_IN), .en(demultiplexer_1_out13), .clk(clock_1_out), .Q(r13_q), .clr(CLR));
  Register #(.width(16)) r14 (.D(DATA_IN), .en(demultiplexer_1_out14), .clk(clock_1_out), .Q(r14_q), .clr(CLR));
  Register #(.width(16)) r15 (.D(multiplexer_1_out), .en(or_2_out), .clk(clock_1_out), .Q(r15_q), .clr(CLR));
  Multiplexer #(.enable("false"), .select(4), .width(16)) multiplexer_2 (
    .in0(r0_q), .in1(r1_q), .in2(r2_q), .in3(r3_q), .in4(r4_q), .in5(r5_q), .in6(r6_q), .in7(r7_q),
    .in8(r8_q), .in9(r9_q), .in10(r10_q), .in11(r11_q), .in12(r12_q), .in13(r13_q), .in14(r14_q),
    .in15(r15_q), .out(Y_OUT), .sel(YOP));
  Multiplexer #(.enable("false"), .select(4), .width(16)) multiplexer_3 (
    .in0(r0_q), .in1(r1_q), .in2(r2_q), .in3(r3_q), .in4(r4_q), .in5(r5_q), .in6(r6_q), .in7(r7_q),
    .in8(r8_q), .in9(r9_q), .in10(r10_q), .in11(r11_q), .in12(r12_q), .in13(r13_q), .in14(r14_q),
    .in15(r15_q), .out(X_OUT), .sel(XOP));
  assign bit_extender_2_out = {{15{RE}}, RE};  // Bit_Extender bit_extender_2
  assign DATA_OUT = bit_extender_2_out & X_OUT;  // AND_Gate and_1, 16 bits wide

  // Notes on the sheet:
  //   Stack Pointer
endmodule
module Arithmetic_Logic_Unit (
  input  [1:0] FLAGS_READ,
  input  CARRY,
  input  SUB,
  input  NEG,
  input  ABS,
  input  INC,
  input  [15:0] X_OPERAND,
  input  [15:0] Y_OPERAND,
  input  I_FLAGS,
  input  ADD,
  input  SHIFT,
  input  LEFT,
  input  ROTATE,
  input  A_SHIFT,
  input  AND,
  input  OR,
  input  XOR,
  input  NOT,
  input  X_PASS_THROUGH,
  output [15:0] RESULT,
  output [1:0] FLAGS_WRITE
);

  wire adder_1_cout, and_1_out, and_2_out, and_3_out, and_4_out, and_10_out, and_12_out, not_2_out, or_1_out,
       or_3_out, or_4_out, or_7_out, or_8_out, or_9_out, or_10_out, xor_2_out, xor_4_out;
  wire [3:0] bit_extender_8_out;
  wire [15:0] adder_1_out, and_5_out, and_6_out, and_7_out, and_8_out, and_9_out, and_11_out, and_13_out,
       bit_extender_1_out, bit_extender_2_out, bit_extender_3_out, bit_extender_4_out, bit_extender_5_out,
       bit_extender_6_out, bit_extender_7_out, bit_extender_9_out, multiplexer_1_out, multiplexer_2_out,
       multiplexer_3_out, multiplexer_4_out, not_1_out, or_2_out, or_5_out, shifter_1_data_out, xor_1_out,
       xor_3_out;

  assign bit_extender_1_out = {{15{AND}}, AND};  // Bit_Extender bit_extender_1
  assign bit_extender_2_out = {{15{OR}}, OR};  // Bit_Extender bit_extender_2
  assign bit_extender_3_out = {{15{XOR}}, XOR};  // Bit_Extender bit_extender_3
  assign bit_extender_4_out = {{15{NOT}}, NOT};  // Bit_Extender bit_extender_4
  assign bit_extender_5_out = {{15{X_PASS_THROUGH}}, X_PASS_THROUGH};  // Bit_Extender bit_extender_5
  and and_1 (and_1_out, FLAGS_READ[0], CARRY);
  and and_2 (and_2_out, ABS, X_OPERAND[15]);
  or or_1 (or_1_out, NEG, ABS);
  and and_3 (and_3_out, X_OPERAND[15], ~Y_OPERAND[15]);  // AND_Gate
  and and_4 (and_4_out, Y_OPERAND[15], ~X_OPERAND[15]);  // AND_Gate
  assign and_5_out = X_OPERAND & bit_extender_1_out & Y_OPERAND;  // AND_Gate and_5, 16 bits wide
  assign and_6_out = bit_extender_2_out & or_2_out;  // AND_Gate and_6, 16 bits wide
  assign or_2_out = X_OPERAND | Y_OPERAND;  // OR_Gate or_2, 16 bits wide
  assign and_7_out = bit_extender_3_out & xor_1_out;  // AND_Gate and_7, 16 bits wide
  assign xor_1_out = X_OPERAND ^ Y_OPERAND;  // XOR_Gate xor_1, 16 bits wide
  assign and_8_out = bit_extender_4_out & not_1_out;  // AND_Gate and_8, 16 bits wide
  assign not_1_out = ~Y_OPERAND;  // NOT_Gate not_1, 16 bits wide
  assign and_9_out = X_OPERAND & bit_extender_5_out;  // AND_Gate and_9, 16 bits wide
  or or_3 (or_3_out, SUB, NEG, and_2_out);
  Multiplexer #(.enable("false"), .width(16)) multiplexer_1 (
    .in0(Y_OPERAND), .in1(16'h1), .out(multiplexer_1_out), .sel(INC));
  Multiplexer #(.enable("false"), .width(16)) multiplexer_2 (
    .in0(multiplexer_1_out), .in1(X_OPERAND), .out(multiplexer_2_out), .sel(or_1_out));
  or or_4 (or_4_out, and_3_out, and_4_out);
  assign or_5_out = and_5_out | and_6_out | and_7_out | and_8_out;  // OR_Gate or_5, 16 bits wide
  xor xor_2 (xor_2_out, and_1_out, or_3_out);
  assign bit_extender_6_out = {{15{not_2_out}}, not_2_out};  // Bit_Extender bit_extender_6
  not not_2 (not_2_out, or_1_out);
  assign bit_extender_7_out = {{15{or_3_out}}, or_3_out};  // Bit_Extender bit_extender_7
  and and_10 (and_10_out, or_4_out, I_FLAGS, ADD);
  Multiplexer #(.enable("false"), .width(16)) multiplexer_3 (
    .in0(X_OPERAND),
    .in1({X_OPERAND[0], X_OPERAND[1], X_OPERAND[2], X_OPERAND[3], X_OPERAND[4], X_OPERAND[5], X_OPERAND[6], X_OPERAND[7], X_OPERAND[8], X_OPERAND[9], X_OPERAND[10], X_OPERAND[11], X_OPERAND[12], X_OPERAND[13], X_OPERAND[14], X_OPERAND[15]}),
    .out(multiplexer_3_out), .sel(LEFT));
  Bit_Extender #(.in_width(16), .out_width(4), .\type ("zero")) bit_extender_8 (
    .in(Y_OPERAND), .out(bit_extender_8_out));
  assign and_11_out = bit_extender_6_out & X_OPERAND;  // AND_Gate and_11, 16 bits wide
  assign xor_3_out = bit_extender_7_out ^ multiplexer_2_out;  // XOR_Gate xor_3, 16 bits wide
  Shifter shifter_1 (
    .DATA_OUT(shifter_1_data_out), .ROTATE(ROTATE), .SIGNED(A_SHIFT), .SHIFT(bit_extender_8_out),
    .DATA_IN(multiplexer_3_out));
  Adder #(.width(16)) adder_1 (.a(and_11_out), .b(xor_3_out), .out(adder_1_out), .cin(xor_2_out), .cout(adder_1_cout));
  xor xor_4 (xor_4_out, adder_1_cout, or_3_out);
  assign bit_extender_9_out = {{15{ADD}}, ADD};  // Bit_Extender bit_extender_9
  and and_12 (and_12_out, xor_4_out, ADD);
  Multiplexer #(.width(16)) multiplexer_4 (
    .in0(shifter_1_data_out),
    .in1({shifter_1_data_out[0], shifter_1_data_out[1], shifter_1_data_out[2], shifter_1_data_out[3], shifter_1_data_out[4], shifter_1_data_out[5], shifter_1_data_out[6], shifter_1_data_out[7], shifter_1_data_out[8], shifter_1_data_out[9], shifter_1_data_out[10], shifter_1_data_out[11], shifter_1_data_out[12], shifter_1_data_out[13], shifter_1_data_out[14], shifter_1_data_out[15]}),
    .out(multiplexer_4_out), .sel(LEFT), .en(SHIFT));
  assign and_13_out = adder_1_out & bit_extender_9_out;  // AND_Gate and_13, 16 bits wide
  xor xor_5 (FLAGS_WRITE[0], and_12_out, and_10_out);
  assign RESULT = and_13_out | multiplexer_4_out | or_5_out | and_9_out;  // OR_Gate or_6, 16 bits wide
  or or_7 (or_7_out, RESULT[15], RESULT[14], RESULT[13], RESULT[12]);
  or or_8 (or_8_out, RESULT[11], RESULT[10], RESULT[9], RESULT[8]);
  or or_9 (or_9_out, RESULT[7], RESULT[6], RESULT[5], RESULT[4]);
  nor nor_1 (FLAGS_WRITE[1], or_7_out, or_8_out, or_9_out, or_10_out);
  or or_10 (or_10_out, RESULT[3], RESULT[2], RESULT[1], RESULT[0]);
endmodule

module Flags_Register (
  input  [1:0] ALU_OUT,
  input  [15:0] DATA_IN,
  input  LOAD,
  input  WE,
  input  CLR,
  input  RE,
  output [1:0] ALU_IN,
  output [15:0] DATA_OUT
);

  wire clock_1_out;
  wire [1:0] multiplexer_1_out;
  wire [15:0] bit_extender_1_out;

  Clock clock_1 (.out(clock_1_out));
  Multiplexer #(.enable("false"), .width(2)) multiplexer_1 (
    .in0(ALU_OUT), .in1(DATA_IN[1:0]), .out(multiplexer_1_out), .sel(LOAD));
  Register #(.width(2)) flags (.D(multiplexer_1_out), .en(WE), .clk(clock_1_out), .Q(ALU_IN), .clr(CLR));
  assign bit_extender_1_out = {{15{RE}}, RE};  // Bit_Extender bit_extender_1
  assign DATA_OUT = {{14{1'b0}}, ALU_IN} & bit_extender_1_out;  // AND_Gate and_1, 16 bits wide
endmodule

module Immediate_Register (
  input  [15:0] DATA_IN,
  input  WE,
  input  CLR,
  output [15:0] DATA_OUT
);

  wire clock_1_out;

  Register #(.width(16)) IMM (.D(DATA_IN), .en(WE), .clk(clock_1_out), .Q(DATA_OUT), .clr(CLR));
  Clock clock_1 (.out(clock_1_out));
endmodule

module Shifter (
  input  [3:0] SHIFT,
  input  [15:0] DATA_IN,
  input  ROTATE,
  input  SIGNED,
  output [15:0] DATA_OUT
);

  wire rotate_bit_1_q0, rotate_bit_1_q1, rotate_bit_1_q2, rotate_bit_1_q3, rotate_bit_1_q4, rotate_bit_1_q5,
       rotate_bit_1_q6, rotate_bit_1_q7, rotate_bit_1_q8, rotate_bit_1_q9, rotate_bit_1_q10,
       rotate_bit_1_q11, rotate_bit_1_q12, rotate_bit_1_q13, rotate_bit_1_q14;
  wire [3:0] not_1_out;

  ROTATE_BIT rotate_bit_1 (
    .Q0(rotate_bit_1_q0), .Q1(rotate_bit_1_q1), .Q2(rotate_bit_1_q2), .Q3(rotate_bit_1_q3),
    .Q4(rotate_bit_1_q4), .Q5(rotate_bit_1_q5), .Q6(rotate_bit_1_q6), .Q7(rotate_bit_1_q7),
    .Q8(rotate_bit_1_q8), .Q9(rotate_bit_1_q9), .Q10(rotate_bit_1_q10), .Q11(rotate_bit_1_q11),
    .Q12(rotate_bit_1_q12), .Q13(rotate_bit_1_q13), .Q14(rotate_bit_1_q14), .ROTATE(ROTATE), .D0(DATA_IN[0]),
    .D1(DATA_IN[1]), .D2(DATA_IN[2]), .D3(DATA_IN[3]), .D4(DATA_IN[4]), .D5(DATA_IN[5]), .D6(DATA_IN[6]),
    .D7(DATA_IN[7]), .D8(DATA_IN[8]), .D9(DATA_IN[9]), .D10(DATA_IN[10]), .D11(DATA_IN[11]),
    .D12(DATA_IN[12]), .D13(DATA_IN[13]), .D14(DATA_IN[14]), .D15(DATA_IN[15]), .SIGNED(SIGNED));
  assign not_1_out = ~SHIFT;  // NOT_Gate not_1, 4 bits wide
  SHIFT_BIT shift_bit_1 (
    .BIT_OUT(DATA_OUT[0]), .SHIFT_N(not_1_out), .SHIFT_P(SHIFT), .D13(DATA_IN[13]), .D14(DATA_IN[14]),
    .D15(DATA_IN[15]), .D0(DATA_IN[0]), .D1(DATA_IN[1]), .D2(DATA_IN[2]), .D3(DATA_IN[3]), .D4(DATA_IN[4]),
    .D5(DATA_IN[5]), .D6(DATA_IN[6]), .D7(DATA_IN[7]), .D8(DATA_IN[8]), .D9(DATA_IN[9]), .D10(DATA_IN[10]),
    .D11(DATA_IN[11]), .D12(DATA_IN[12]));
  SHIFT_BIT shift_bit_2 (
    .BIT_OUT(DATA_OUT[1]), .SHIFT_N(not_1_out), .SHIFT_P(SHIFT), .D13(DATA_IN[14]), .D14(DATA_IN[15]),
    .D15(rotate_bit_1_q0), .D0(DATA_IN[1]), .D1(DATA_IN[2]), .D2(DATA_IN[3]), .D3(DATA_IN[4]),
    .D4(DATA_IN[5]), .D5(DATA_IN[6]), .D6(DATA_IN[7]), .D7(DATA_IN[8]), .D8(DATA_IN[9]), .D9(DATA_IN[10]),
    .D10(DATA_IN[11]), .D11(DATA_IN[12]), .D12(DATA_IN[13]));
  SHIFT_BIT shift_bit_3 (
    .BIT_OUT(DATA_OUT[2]), .SHIFT_N(not_1_out), .SHIFT_P(SHIFT), .D13(DATA_IN[15]), .D14(rotate_bit_1_q0),
    .D15(rotate_bit_1_q1), .D0(DATA_IN[2]), .D1(DATA_IN[3]), .D2(DATA_IN[4]), .D3(DATA_IN[5]),
    .D4(DATA_IN[6]), .D5(DATA_IN[7]), .D6(DATA_IN[8]), .D7(DATA_IN[9]), .D8(DATA_IN[10]), .D9(DATA_IN[11]),
    .D10(DATA_IN[12]), .D11(DATA_IN[13]), .D12(DATA_IN[14]));
  SHIFT_BIT shift_bit_4 (
    .BIT_OUT(DATA_OUT[3]), .SHIFT_N(not_1_out), .SHIFT_P(SHIFT), .D13(rotate_bit_1_q0),
    .D14(rotate_bit_1_q1), .D15(rotate_bit_1_q2), .D0(DATA_IN[3]), .D1(DATA_IN[4]), .D2(DATA_IN[5]),
    .D3(DATA_IN[6]), .D4(DATA_IN[7]), .D5(DATA_IN[8]), .D6(DATA_IN[9]), .D7(DATA_IN[10]), .D8(DATA_IN[11]),
    .D9(DATA_IN[12]), .D10(DATA_IN[13]), .D11(DATA_IN[14]), .D12(DATA_IN[15]));
  SHIFT_BIT shift_bit_5 (
    .BIT_OUT(DATA_OUT[4]), .SHIFT_N(not_1_out), .SHIFT_P(SHIFT), .D13(rotate_bit_1_q1),
    .D14(rotate_bit_1_q2), .D15(rotate_bit_1_q3), .D0(DATA_IN[4]), .D1(DATA_IN[5]), .D2(DATA_IN[6]),
    .D3(DATA_IN[7]), .D4(DATA_IN[8]), .D5(DATA_IN[9]), .D6(DATA_IN[10]), .D7(DATA_IN[11]), .D8(DATA_IN[12]),
    .D9(DATA_IN[13]), .D10(DATA_IN[14]), .D11(DATA_IN[15]), .D12(rotate_bit_1_q0));
  SHIFT_BIT shift_bit_6 (
    .BIT_OUT(DATA_OUT[5]), .SHIFT_N(not_1_out), .SHIFT_P(SHIFT), .D13(rotate_bit_1_q2),
    .D14(rotate_bit_1_q3), .D15(rotate_bit_1_q4), .D0(DATA_IN[5]), .D1(DATA_IN[6]), .D2(DATA_IN[7]),
    .D3(DATA_IN[8]), .D4(DATA_IN[9]), .D5(DATA_IN[10]), .D6(DATA_IN[11]), .D7(DATA_IN[12]), .D8(DATA_IN[13]),
    .D9(DATA_IN[14]), .D10(DATA_IN[15]), .D11(rotate_bit_1_q0), .D12(rotate_bit_1_q1));
  SHIFT_BIT shift_bit_7 (
    .BIT_OUT(DATA_OUT[6]), .SHIFT_N(not_1_out), .SHIFT_P(SHIFT), .D13(rotate_bit_1_q3),
    .D14(rotate_bit_1_q4), .D15(rotate_bit_1_q5), .D0(DATA_IN[6]), .D1(DATA_IN[7]), .D2(DATA_IN[8]),
    .D3(DATA_IN[9]), .D4(DATA_IN[10]), .D5(DATA_IN[11]), .D6(DATA_IN[12]), .D7(DATA_IN[13]),
    .D8(DATA_IN[14]), .D9(DATA_IN[15]), .D10(rotate_bit_1_q0), .D11(rotate_bit_1_q1), .D12(rotate_bit_1_q2));
  SHIFT_BIT shift_bit_8 (
    .BIT_OUT(DATA_OUT[7]), .SHIFT_N(not_1_out), .SHIFT_P(SHIFT), .D13(rotate_bit_1_q4),
    .D14(rotate_bit_1_q5), .D15(rotate_bit_1_q6), .D0(DATA_IN[7]), .D1(DATA_IN[8]), .D2(DATA_IN[9]),
    .D3(DATA_IN[10]), .D4(DATA_IN[11]), .D5(DATA_IN[12]), .D6(DATA_IN[13]), .D7(DATA_IN[14]),
    .D8(DATA_IN[15]), .D9(rotate_bit_1_q0), .D10(rotate_bit_1_q1), .D11(rotate_bit_1_q2),
    .D12(rotate_bit_1_q3));
  SHIFT_BIT shift_bit_9 (
    .BIT_OUT(DATA_OUT[8]), .SHIFT_N(not_1_out), .SHIFT_P(SHIFT), .D13(rotate_bit_1_q5),
    .D14(rotate_bit_1_q6), .D15(rotate_bit_1_q7), .D0(DATA_IN[8]), .D1(DATA_IN[9]), .D2(DATA_IN[10]),
    .D3(DATA_IN[11]), .D4(DATA_IN[12]), .D5(DATA_IN[13]), .D6(DATA_IN[14]), .D7(DATA_IN[15]),
    .D8(rotate_bit_1_q0), .D9(rotate_bit_1_q1), .D10(rotate_bit_1_q2), .D11(rotate_bit_1_q3),
    .D12(rotate_bit_1_q4));
  SHIFT_BIT shift_bit_10 (
    .BIT_OUT(DATA_OUT[9]), .SHIFT_N(not_1_out), .SHIFT_P(SHIFT), .D13(rotate_bit_1_q6),
    .D14(rotate_bit_1_q7), .D15(rotate_bit_1_q8), .D0(DATA_IN[9]), .D1(DATA_IN[10]), .D2(DATA_IN[11]),
    .D3(DATA_IN[12]), .D4(DATA_IN[13]), .D5(DATA_IN[14]), .D6(DATA_IN[15]), .D7(rotate_bit_1_q0),
    .D8(rotate_bit_1_q1), .D9(rotate_bit_1_q2), .D10(rotate_bit_1_q3), .D11(rotate_bit_1_q4),
    .D12(rotate_bit_1_q5));
  SHIFT_BIT shift_bit_11 (
    .BIT_OUT(DATA_OUT[10]), .SHIFT_N(not_1_out), .SHIFT_P(SHIFT), .D13(rotate_bit_1_q7),
    .D14(rotate_bit_1_q8), .D15(rotate_bit_1_q9), .D0(DATA_IN[10]), .D1(DATA_IN[11]), .D2(DATA_IN[12]),
    .D3(DATA_IN[13]), .D4(DATA_IN[14]), .D5(DATA_IN[15]), .D6(rotate_bit_1_q0), .D7(rotate_bit_1_q1),
    .D8(rotate_bit_1_q2), .D9(rotate_bit_1_q3), .D10(rotate_bit_1_q4), .D11(rotate_bit_1_q5),
    .D12(rotate_bit_1_q6));
  // SHIFT_BIT shift_bit_12: pin names not known; wires that end beside it: not_1_out, SHIFT, DATA_IN[11], DATA_IN[12], DATA_IN[13], DATA_IN[14], DATA_IN[15], rotate_bit_1_q0, rotate_bit_1_q1, rotate_bit_1_q2, rotate_bit_1_q3, rotate_bit_1_q4, rotate_bit_1_q5, rotate_bit_1_q6, rotate_bit_1_q7, rotate_bit_1_q8, rotate_bit_1_q9, rotate_bit_1_q10, DATA_OUT[11]
  SHIFT_BIT shift_bit_13 (
    .BIT_OUT(DATA_OUT[12]), .SHIFT_N(not_1_out), .SHIFT_P(SHIFT), .D13(rotate_bit_1_q9),
    .D14(rotate_bit_1_q10), .D15(rotate_bit_1_q11), .D0(DATA_IN[12]), .D1(DATA_IN[13]), .D2(DATA_IN[14]),
    .D3(DATA_IN[15]), .D4(rotate_bit_1_q0), .D5(rotate_bit_1_q1), .D6(rotate_bit_1_q2), .D7(rotate_bit_1_q3),
    .D8(rotate_bit_1_q4), .D9(rotate_bit_1_q5), .D10(rotate_bit_1_q6), .D11(rotate_bit_1_q7),
    .D12(rotate_bit_1_q8));
  SHIFT_BIT shift_bit_14 (
    .BIT_OUT(DATA_OUT[13]), .SHIFT_N(not_1_out), .SHIFT_P(SHIFT), .D13(rotate_bit_1_q10),
    .D14(rotate_bit_1_q11), .D15(rotate_bit_1_q12), .D0(DATA_IN[13]), .D1(DATA_IN[14]), .D2(DATA_IN[15]),
    .D3(rotate_bit_1_q0), .D4(rotate_bit_1_q1), .D5(rotate_bit_1_q2), .D6(rotate_bit_1_q3),
    .D7(rotate_bit_1_q4), .D8(rotate_bit_1_q5), .D9(rotate_bit_1_q6), .D10(rotate_bit_1_q7),
    .D11(rotate_bit_1_q8), .D12(rotate_bit_1_q9));
  SHIFT_BIT shift_bit_15 (
    .BIT_OUT(DATA_OUT[14]), .SHIFT_N(not_1_out), .SHIFT_P(SHIFT), .D13(rotate_bit_1_q11),
    .D14(rotate_bit_1_q12), .D15(rotate_bit_1_q13), .D0(DATA_IN[14]), .D1(DATA_IN[15]), .D2(rotate_bit_1_q0),
    .D3(rotate_bit_1_q1), .D4(rotate_bit_1_q2), .D5(rotate_bit_1_q3), .D6(rotate_bit_1_q4),
    .D7(rotate_bit_1_q5), .D8(rotate_bit_1_q6), .D9(rotate_bit_1_q7), .D10(rotate_bit_1_q8),
    .D11(rotate_bit_1_q9), .D12(rotate_bit_1_q10));
  SHIFT_BIT shift_bit_16 (
    .BIT_OUT(DATA_OUT[15]), .SHIFT_N(not_1_out), .SHIFT_P(SHIFT), .D13(rotate_bit_1_q12),
    .D14(rotate_bit_1_q13), .D15(rotate_bit_1_q14), .D0(DATA_IN[15]), .D1(rotate_bit_1_q0),
    .D2(rotate_bit_1_q1), .D3(rotate_bit_1_q2), .D4(rotate_bit_1_q3), .D5(rotate_bit_1_q4),
    .D6(rotate_bit_1_q5), .D7(rotate_bit_1_q6), .D8(rotate_bit_1_q7), .D9(rotate_bit_1_q8),
    .D10(rotate_bit_1_q9), .D11(rotate_bit_1_q10), .D12(rotate_bit_1_q11));

  // Notes on the sheet:
  //    592 Logic Blocks for Shifting/Rotating
  //     15 Logic Blocks for Operation Select
  //      4 Logic Blocks for Negating Shift Amount
  //    611 Logic Blocks Total
  //   1780 Logic Blocks Without Optimization
endmodule

module SHIFT_BIT (
  input  [3:0] SHIFT_N,
  input  [3:0] SHIFT_P,
  input  D0,
  input  D1,
  input  D2,
  input  D3,
  input  D4,
  input  D5,
  input  D6,
  input  D7,
  input  D8,
  input  D9,
  input  D10,
  input  D11,
  input  D12,
  input  D13,
  input  D14,
  input  D15,
  output BIT_OUT
);

  wire and_1_out, and_2_out, and_3_out, and_4_out, and_5_out, and_6_out, and_7_out, and_8_out, and_9_out,
       and_10_out, and_11_out, and_12_out, and_13_out, and_14_out, and_15_out, and_16_out, and_17_out,
       and_18_out, and_19_out, and_20_out, and_21_out, and_22_out, and_23_out, and_24_out, and_25_out,
       and_26_out, and_27_out, and_28_out, and_29_out, and_30_out, and_31_out, and_32_out, or_1_out,
       or_2_out, or_3_out, or_4_out;

  and and_1 (and_1_out, SHIFT_N[0], SHIFT_N[1], SHIFT_N[2], SHIFT_N[3]);
  and and_2 (and_2_out, SHIFT_P[0], SHIFT_N[1], SHIFT_N[2], SHIFT_N[3]);
  and and_3 (and_3_out, SHIFT_N[0], SHIFT_P[1], SHIFT_N[2], SHIFT_N[3]);
  and and_4 (and_4_out, SHIFT_P[0], SHIFT_P[1], SHIFT_N[2], SHIFT_N[3]);
  and and_5 (and_5_out, SHIFT_N[0], SHIFT_N[1], SHIFT_P[2], SHIFT_N[3]);
  and and_6 (and_6_out, SHIFT_P[0], SHIFT_N[1], SHIFT_P[2], SHIFT_N[3]);
  and and_7 (and_7_out, SHIFT_N[0], SHIFT_P[1], SHIFT_P[2], SHIFT_N[3]);
  and and_8 (and_8_out, SHIFT_P[0], SHIFT_P[1], SHIFT_P[2], SHIFT_N[3]);
  and and_9 (and_9_out, SHIFT_N[0], SHIFT_N[1], SHIFT_N[2], SHIFT_P[3]);
  and and_10 (and_10_out, SHIFT_P[0], SHIFT_N[1], SHIFT_N[2], SHIFT_P[3]);
  and and_11 (and_11_out, SHIFT_N[0], SHIFT_P[1], SHIFT_N[2], SHIFT_P[3]);
  and and_12 (and_12_out, SHIFT_P[0], SHIFT_P[1], SHIFT_N[2], SHIFT_P[3]);
  and and_13 (and_13_out, SHIFT_N[0], SHIFT_N[1], SHIFT_P[2], SHIFT_P[3]);
  and and_14 (and_14_out, SHIFT_P[0], SHIFT_N[1], SHIFT_P[2], SHIFT_P[3]);
  and and_15 (and_15_out, SHIFT_N[0], SHIFT_P[1], SHIFT_P[2], SHIFT_P[3]);
  and and_16 (and_16_out, SHIFT_P[0], SHIFT_P[1], SHIFT_P[2], SHIFT_P[3]);
  and and_17 (and_17_out, and_1_out, D0);
  and and_18 (and_18_out, and_2_out, D1);
  or or_1 (or_1_out, and_17_out, and_18_out, and_19_out, and_20_out);
  and and_19 (and_19_out, and_3_out, D2);
  and and_20 (and_20_out, and_4_out, D3);
  and and_21 (and_21_out, and_5_out, D4);
  and and_22 (and_22_out, and_6_out, D5);
  or or_2 (or_2_out, and_21_out, and_22_out, and_23_out, and_24_out);
  and and_23 (and_23_out, and_7_out, D6);
  and and_24 (and_24_out, and_8_out, D7);
  and and_25 (and_25_out, and_9_out, D8);
  and and_26 (and_26_out, and_10_out, D9);
  or or_3 (or_3_out, and_25_out, and_26_out, and_27_out, and_28_out);
  and and_27 (and_27_out, and_11_out, D10);
  and and_28 (and_28_out, and_12_out, D11);
  and and_29 (and_29_out, and_13_out, D12);
  and and_30 (and_30_out, and_14_out, D13);
  or or_4 (or_4_out, and_29_out, and_30_out, and_31_out, and_32_out);
  and and_31 (and_31_out, and_15_out, D14);
  and and_32 (and_32_out, and_16_out, D15);
  or or_5 (BIT_OUT, or_1_out, or_2_out, or_3_out, or_4_out);
endmodule

module ROTATE_BIT (
  input  ROTATE,
  input  D0,
  input  D1,
  input  D2,
  input  D3,
  input  D4,
  input  D5,
  input  D6,
  input  D7,
  input  D8,
  input  D9,
  input  D10,
  input  D11,
  input  D12,
  input  D13,
  input  D14,
  input  D15,
  input  SIGNED,
  output Q0,
  output Q1,
  output Q2,
  output Q3,
  output Q4,
  output Q5,
  output Q6,
  output Q7,
  output Q8,
  output Q9,
  output Q10,
  output Q11,
  output Q12,
  output Q13,
  output Q14
);

  wire and_1_out, and_2_out, and_3_out, and_4_out, and_5_out, and_6_out, and_7_out, and_8_out, and_9_out,
       and_10_out, and_11_out, and_12_out, and_13_out, and_14_out, and_15_out, and_16_out;

  and and_1 (and_1_out, ROTATE, D0);
  and and_2 (and_2_out, ROTATE, D1);
  and and_3 (and_3_out, ROTATE, D2);
  and and_4 (and_4_out, ROTATE, D3);
  and and_5 (and_5_out, ROTATE, D4);
  and and_6 (and_6_out, ROTATE, D5);
  and and_7 (and_7_out, ROTATE, D6);
  and and_8 (and_8_out, ROTATE, D7);
  and and_9 (and_9_out, ROTATE, D8);
  and and_10 (and_10_out, ROTATE, D9);
  and and_11 (and_11_out, ROTATE, D10);
  and and_12 (and_12_out, ROTATE, D11);
  and and_13 (and_13_out, ROTATE, D12);
  and and_14 (and_14_out, ROTATE, D13);
  and and_15 (and_15_out, ROTATE, D14);
  and and_16 (and_16_out, D15, SIGNED);
  or or_1 (Q0, and_1_out, and_16_out);
  or or_2 (Q1, and_2_out, and_16_out);
  or or_3 (Q2, and_3_out, and_16_out);
  or or_4 (Q3, and_4_out, and_16_out);
  or or_5 (Q4, and_5_out, and_16_out);
  or or_6 (Q5, and_6_out, and_16_out);
  or or_7 (Q6, and_7_out, and_16_out);
  or or_8 (Q7, and_8_out, and_16_out);
  or or_9 (Q8, and_9_out, and_16_out);
  or or_10 (Q9, and_10_out, and_16_out);
  or or_11 (Q10, and_11_out, and_16_out);
  or or_12 (Q11, and_12_out, and_16_out);
  or or_13 (Q12, and_13_out, and_16_out);
  or or_14 (Q13, and_14_out, and_16_out);
  or or_15 (Q14, and_15_out, and_16_out);
endmodule
