// Logisim project CPU Test.circ as structural Verilog: 8 circuits, main circuit main
module main (
);

  wire address_mapper_1_re_out, address_mapper_3_re_out, address_mapper_4_we_out, address_mapper_5_re_out,
       address_mapper_5_we_out, address_mapper_6_we_out, address_mapper_7_re_out, address_mapper_7_we_out,
       address_mapper_8_re_out, clock_2_out, clock_3_out, clock_4_out, clock_5_out, clock_6_out, DBG_RESUME,
       demultiplexer_1_out1, demultiplexer_1_out2, demultiplexer_2_out0, demultiplexer_2_out1,
       demultiplexer_2_out2, INT_BUTTON, INT_JOYSTICK, INT_KEYBOARD, INTERRUPT, not_1_out, RE, RESET,
       rgb_video_1_p2, rgb_video_1_p3, WE;
  wire [2:0] bit_extender_3_out;
  wire [7:0] bit_extender_1_out, keyboard_1_data;
  wire [12:0] bit_extender_4_out, JOY_DATA;
  wire [15:0] ADDR, bit_extender_2_out, DATA, HEX_OUT, PAGE, rom_1_data;
  wire [19:0] BCD_OUT;

  Joystick #(.bits(5)) joystick_1 (.x(JOY_DATA[4:0]), .y(JOY_DATA[12:8]));
  _7_Segment_Display u_7_segment_display_1 ();  // open: g, f, a, b, e, d, c, dp
  // Hex_to_7_Segment_decoder hex_to_7_segment_decoder_1: pin names not known
  DotMatrix #(.dotshape("circle"), .matrixcols(16), .matrixrows(1)) dotmatrix_1 (
    .col0(HEX_OUT[15]), .col1(HEX_OUT[14]), .col2(HEX_OUT[13]), .col3(HEX_OUT[12]), .col4(HEX_OUT[11]),
    .col5(HEX_OUT[10]), .col6(HEX_OUT[9]), .col7(HEX_OUT[8]), .col8(HEX_OUT[7]), .col9(HEX_OUT[6]),
    .col10(HEX_OUT[5]), .col11(HEX_OUT[4]), .col12(HEX_OUT[3]), .col13(HEX_OUT[2]), .col14(HEX_OUT[1]),
    .col15(HEX_OUT[0]));
  _7_Segment_Display u_7_segment_display_2 ();  // open: g, f, a, b, e, d, c, dp
  _7_Segment_Display u_7_segment_display_3 ();  // open: g, f, a, b, e, d, c, dp
  // Hex_to_7_Segment_decoder hex_to_7_segment_decoder_2: pin names not known
  // Hex_to_7_Segment_decoder hex_to_7_segment_decoder_3: pin names not known
  // RGB_Video #(.cursor("No Cursor"), .fixed("0#565 RGB (16 bit)")) rgb_video_1: pin names not known; wires that end beside it: RESET, rgb_video_1_p2, rgb_video_1_p3, ADDR[6:0], ADDR[13:7], DATA
  Clock clock_1 (.out(rgb_video_1_p2));
  Address_Mapper address_mapper_1 (
    .RE_OUT(address_mapper_1_re_out), .Base({16{1'b0}}), .Mask({16{1'b1}}), .Address(PAGE), .RE_IN(RE));  // open: WE_OUT, WE_IN
  _7_Segment_Display u_7_segment_display_4 ();  // open: g, f, a, b, e, d, c, dp
  // Hex_to_7_Segment_decoder hex_to_7_segment_decoder_4: pin names not known
  Button u_interrupt (.out(INT_BUTTON));
  Button debug_resume (.out(DBG_RESUME));
  Button u_reset (.out(RESET));
  _7_Segment_Display u_7_segment_display_5 ();  // open: g, f, a, b, e, d, c, dp
  _7_Segment_Display u_7_segment_display_6 ();  // open: g, f, a, b, e, d, c, dp
  // BCD_to_7_Segment_decoder bcd_to_7_segment_decoder_1: pin names not known
  // BCD_to_7_Segment_decoder bcd_to_7_segment_decoder_2: pin names not known
  Address_Mapper address_mapper_2 (
    .RE_OUT(rgb_video_1_p3), .Base(16'h8000), .Mask(16'hc000), .Address(ADDR), .RE_IN(address_mapper_1_re_out));  // open: WE_OUT, WE_IN
  _7_Segment_Display u_7_segment_display_7 ();  // open: g, f, a, b, e, d, c, dp
  // BCD_to_7_Segment_decoder bcd_to_7_segment_decoder_3: pin names not known
  _7_Segment_Display u_7_segment_display_8 ();  // open: g, f, a, b, e, d, c, dp
  _7_Segment_Display u_7_segment_display_9 ();  // open: g, f, a, b, e, d, c, dp
  // BCD_to_7_Segment_decoder bcd_to_7_segment_decoder_4: pin names not known
  // BCD_to_7_Segment_decoder bcd_to_7_segment_decoder_5: pin names not known
  Bit_Extender #(.in_width(16), .out_width(8), .\type ("zero")) bit_extender_1 (.in(DATA), .out(bit_extender_1_out));
  TTY #(.asciiwidth(8), .cols(120), .rows(32)) tty_1 (
    .data(bit_extender_1_out[6:0]), .clk(clock_2_out), .we(address_mapper_4_we_out), .clr(RESET));
  Clock clock_2 (.out(clock_2_out));
  Clock clock_3 (.out(clock_3_out));
  Keyboard #(.asciiwidth(8)) keyboard_1 (
    .clk(clock_3_out), .re(address_mapper_3_re_out), .clr(RESET), .avail(INT_KEYBOARD),
    .data(keyboard_1_data[6:0]));
  Address_Mapper address_mapper_3 (
    .RE_OUT(address_mapper_3_re_out), .Base(16'h7f01), .Mask({16{1'b1}}), .Address(ADDR), .WE_IN(WE),
    .RE_IN(RE));  // open: WE_OUT
  Address_Mapper address_mapper_4 (
    .WE_OUT(address_mapper_4_we_out), .Base(16'h7f00), .Mask({16{1'b1}}), .Address(ADDR), .WE_IN(WE),
    .RE_IN(RE));  // open: RE_OUT
  assign bit_extender_2_out = {{8{1'b0}}, keyboard_1_data};  // Bit_Extender bit_extender_2
  assign DATA = address_mapper_3_re_out ? bit_extender_2_out : 16'bz;  // Controlled_Buffer controlled_buffer_1
  Bit_Extender #(.in_width(16), .out_width(3), .\type ("zero")) bit_extender_3 (.in(ADDR), .out(bit_extender_3_out));
  Address_Mapper address_mapper_5 (
    .WE_OUT(address_mapper_5_we_out), .RE_OUT(address_mapper_5_re_out), .Base(16'h7ff0), .Mask(16'hfff8),
    .Address(ADDR), .WE_IN(WE), .RE_IN(RE));
  CH016M01 ch016m01_1 (
    .TO_ADDR(ADDR), .TO_RAM(DATA), .RAM_WE(WE), .RAM_RE(RE), .FROM_RAM(DATA), .INT(INTERRUPT),
    .resume(DBG_RESUME), .CLR(RESET));  // open: STEP_1, STEP_2, STEP_3, STEP_4
  Interrupt_Manager interrupt_manager_1 (
    .Data_Out(DATA), .Interrupt(INTERRUPT), .Data_In(DATA), .RE(address_mapper_5_re_out),
    .WE(address_mapper_5_we_out), .Register_Select(bit_extender_3_out), .Reset(RESET), .Source_1(INT_BUTTON),
    .Source_2(INT_JOYSTICK), .Source_3(INT_KEYBOARD), .Source_4(1'b0), .Source_5(1'b0), .Source_6(1'b0),
    .Source_7(1'b0), .Source_8(1'b0), .Source_9(1'b0), .Source_10(1'b0), .Source_11(1'b0), .Source_12(1'b0),
    .Source_13(1'b0), .Source_14(1'b0), .Source_15(1'b0));
  Clock clock_4 (.out(clock_4_out));
  not not_1 (not_1_out, ADDR[15]);
  Demultiplexer #(.select(2)) demultiplexer_1 (
    .out1(demultiplexer_1_out1), .out2(demultiplexer_1_out2), .in(WE), .sel(ADDR[14:13]), .en(not_1_out));  // open: out0, out3
  Demultiplexer #(.select(2)) demultiplexer_2 (
    .out0(demultiplexer_2_out0), .out1(demultiplexer_2_out1), .out2(demultiplexer_2_out2), .in(RE),
    .sel(ADDR[14:13]), .en(not_1_out));  // open: out3
  Register #(.width(16)) register_1 (
    .D(DATA), .en(address_mapper_6_we_out), .clk(clock_4_out), .Q(HEX_OUT), .clr(RESET));
  ROM #(.addrWidth(13), .dataWidth(16)) rom_1 (.addr(bit_extender_4_out), .data(rom_1_data));
  Bit_Extender #(.in_width(16), .out_width(13), .\type ("zero")) bit_extender_4 (.in(ADDR), .out(bit_extender_4_out));
  RAM #(.addrWidth(13), .dataWidth(16), .databus("bidir")) ram_1 (
    .addr(bit_extender_4_out), .data(DATA));  // open: we, oe, clk
  RAM #(.addrWidth(13), .dataWidth(16), .databus("bidir")) ram_2 (
    .addr(bit_extender_4_out), .data(DATA));  // open: we, oe, clk
  Clock clock_5 (.out(clock_5_out));
  Address_Mapper address_mapper_6 (
    .WE_OUT(address_mapper_6_we_out), .Base(16'h7ffe), .Mask({16{1'b1}}), .Address(ADDR), .WE_IN(WE),
    .RE_IN(RE));  // open: RE_OUT
  Binary_to_BCD binary_to_bcd_1 (
    .Input(DATA), .Load_Start(address_mapper_6_we_out), .Reset(RESET), ._10_000s(BCD_OUT[19:16]),
    ._1_000s(BCD_OUT[15:12]), ._100s(BCD_OUT[11:8]), ._10s(BCD_OUT[7:4]), ._1s(BCD_OUT[3:0]));
  assign DATA = demultiplexer_2_out0 ? rom_1_data : 16'bz;  // Controlled_Buffer controlled_buffer_2
  Address_Mapper address_mapper_7 (
    .WE_OUT(address_mapper_7_we_out), .RE_OUT(address_mapper_7_re_out), .Base(16'h7fff), .Mask({16{1'b1}}),
    .Address(ADDR), .WE_IN(WE), .RE_IN(RE));
  Clock clock_6 (.out(clock_6_out));
  Address_Mapper address_mapper_8 (
    .RE_OUT(address_mapper_8_re_out), .Base(16'h7f02), .Mask({16{1'b1}}), .Address(ADDR), .RE_IN(RE));  // open: WE_OUT, WE_IN
  Register #(.width(16)) register_2 (.D(DATA), .en(address_mapper_7_we_out), .clk(clock_6_out), .Q(PAGE), .clr(RESET));
  Joystick_Processor joystick_processor_1 (
    .Data_Out(DATA), .Interrupt(INT_JOYSTICK), .Data_In({3'b000, JOY_DATA[12:8], 3'b000, JOY_DATA[4:0]}),
    .Reset(RESET), .RE(address_mapper_8_re_out));
  assign DATA = address_mapper_7_re_out ? PAGE : 16'bz;  // Controlled_Buffer controlled_buffer_3
  // Pins of 7 and 8 bits meet at bit_extender_1_out
  // Pins of 7 and 8 bits meet at keyboard_1_data

  // Notes on the sheet:
  //   Joystick
  //   RGB Display
  //   Misc. Inputs
  //   Output Register Display
  //   Keyboard
  //   Terminal Display
  //   Interrupt Manager
  //   Central Processing Unit
  //   Output Register
  //   contents of rom_1 (hex, n*v repeats v):
  //   1200 24f bf1 1 802 ff00 a10 1603 3423 1210 19 2d83 d03 7f00 1603 2d82 3423 1210 19 d03 7f00 2982
  //   2201 1200 6 500 1000 1001 1002 1003 900 7ff0 d00 2001 b21 2a 800 f 3802 1250 3a 1301 3f 23c 240
  //   13*3a 3600 d00 7ff1 1200 246 900 2000 b00 59 1000 400 2 220f 900 2000 801 10 3810 1220 54 800 1 d00
  //   7ff2 1200 246 2200 d00 2000 1200 246 6a 73 84 92 bc d2 f5 106 122 15a 190 1ac 1d5 1e3 1f8 216 22d
  //   4865 6c6c 6f2c 2059 6f75 5475 6265 210a 0 5072 696e 7469 6e67 2073 7472 696e 6773 2074 616b 6573
  //   2066 6f72 6576 6572 2e0a 0 506c 6561 7365 2072 6174 6520 616e 6420 7375 6273 6372 6962 6521 a00 486f
  //   7720 616d 2049 2073 7570 706f 7365 6420 746f 2063 616c 6375 6c61 7465 2074 6865 2066 6962 6f6e 6163
  //   6369 2073 6571 7565 6e63 6520 6966 2079 6f75 206b 6565 7020 696e 7465 7272 7570 7469 6e67 206d 653f
  //   a00 5468 6520 696e 7465 7272 7570 7420 6861 6e64 6c65 7220 6a75 7374 2070 7269 6e74 7320 7374 7269
  //   6e67 732e a00 4f6b 6179 2c20 6974 2061 6c73 6f20 696e 6372 656d 656e 7473 2061 2063 6f75 6e74 6572
  //   2065 7665 7279 2074 696d 6520 796f 7520 7075 7368 2074 6861 7420 6275 7474 6f6e 2e0a 0 5374 6f70
  //   2070 7573 6869 6e67 2074 6861 7420 6275 7474 6f6e 2070 6c65 6173 652e a00 4927 6d20 6173 6b69 6e67
  //   206e 6963 656c 792e 2020 506c 6561 7365 2073 746f 7020 7072 6573 7369 6e67 2074 6861 7420 6275 7474
  //   6f6e 2e0a 0 4966 2079 6f75 2772 6520 6c6f 6f6b 696e 6720 666f 7220 616e 2045 6173 7465 7220 4567
  //   6720 6f72 2073 6f6d 6574 6869 6e67 2069 6e20 7468 6520 696e 7465 7272 7570 7420 6861 6e64 6c65 722c
  //   2079 6f75 2772 6520 676f 696e 6720 746f 2062 6520 7761 6974 696e 6720 6120 7768 696c 652e a00 4920
  //   776f 6e64 6572 2068 6f77 206c 6f6e 6720 7468 6973 2066 756e 6374 696f 6e20 776f 756c 6420 7461 6b65
  //   2069 6620 4920 666f 7267 6574 2074 6f20 6164 6420 6120 6e75 6c6c 2074 6572 6d69 6e61 746f 7220 746f
  //   206f 6e65 206f 6620 7468 6573 6520 7374 7269 6e67 732e 2e2e a00 4920 616c 736f 2077 6f6e 6465 7220
  //   686f 7720 7468 6174 2077 6f75 6c64 206c 6f6f 6b20 6f6e 2074 6865 2054 5459 2064 6973 706c 6179 2e0a
  //   0 4e6f 7420 7468 6174 2049 2764 2066 6f72 6765 7420 7468 6174 206e 756c 6c20 7465 726d 696e 6174
  //   6f72 206f 6e20 7075 7270 6f73 6520 6f72 2061 6e79 7468 696e 672e 2020 4f72 2077 6f75 6c64 2049 2e2e
  //   2e0a 0 5374 6f70 2070 7573 6869 6e67 2074 6861 7420 6275 7474 6f6e 210a 0 5768 6174 2070 6172 7420
  //   6f66 2073 746f 7020 646f 2079 6f75 206e 6f74 2075 6e64 6572 7374 616e 643f a00 4927 6d20 7761 726e
  //   696e 6720 796f 753a 2020 444f 2e20 204e 4f54 2e20 2050 5553 482e 2020 5448 4154 2e20 2042 5554 544f
  //   4e2e 2020 4147 4149 4e2e a00 5075 7368 2074 6861 7420 6275 7474 6f6e 206f 6e65 206d 6f72 6520 7469
  //   6d65 2e20 4920 6461 7265 2079 6f75 210a 0 5468 6520 6275 7474 6f6e 2069 7320 6e6f 7720 6469 7361
  //   626c 6564 2e0a 0 900 7f02 1200 246 900 7f01 d00 7f00 1200 246 900 2001 d00 7ff0 1103 1102 1101 1100
  //   510 3600 d00 2000 80f 3fff 2200 d00 7ff1 100 1a 210 3600 801 1 d00 7ffe 2010 1230 25a 3610 3601 3610
  //   d01 7ffe 10*0 1200 25f 3600 ff00
  //   Main Memory
  //   Page Register
  //   Joystick Handler
endmodule

module Address_Mapper (
  input  [15:0] Base,
  input  [15:0] Mask,
  input  [15:0] Address,
  input  WE_IN,
  input  RE_IN,
  output WE_OUT,
  output RE_OUT
);

  wire comparator_1_eq;
  wire [15:0] and_1_out;

  assign and_1_out = Mask & Address;  // AND_Gate and_1, 16 bits wide
  Comparator #(.mode("unsigned"), .width(16)) comparator_1 (
    .a(Base), .b(and_1_out), .eq(comparator_1_eq));  // open: gt, lt
  and and_2 (WE_OUT, comparator_1_eq, WE_IN);
  and and_3 (RE_OUT, comparator_1_eq, RE_IN);
endmodule

module Binary_to_BCD (
  input  [15:0] Input,
  input  Load_Start,
  input  Reset,
  output [3:0] _10_000s,
  output [3:0] _1_000s,
  output [3:0] _100s,
  output [3:0] _10s,
  output [3:0] _1s
);

  wire binary_to_bcd_segment_2_out_5, binary_to_bcd_segment_3_out_5, binary_to_bcd_segment_4_out_5,
       binary_to_bcd_segment_5_out_5, clock_1_out, not_1_out, or_1_out, or_2_out, or_4_out,
       shift_register_1_p1, shift_register_1_p6;
  wire [4:0] multiplexer_1_out, register_1_q, subtractor_1_out;

  Clock clock_1 (.out(clock_1_out));
  not not_1 (not_1_out, Load_Start);
  Binary_to_BCD_Segment binary_to_bcd_segment_1 (
    .out_6(_10_000s), .in_1(binary_to_bcd_segment_2_out_5), ._CLR(not_1_out), .WE(shift_register_1_p1),
    .RESET(Reset));  // open: out_5
  Binary_to_BCD_Segment binary_to_bcd_segment_2 (
    .out_5(binary_to_bcd_segment_2_out_5), .out_6(_1_000s), .in_1(binary_to_bcd_segment_3_out_5),
    ._CLR(not_1_out), .WE(shift_register_1_p1), .RESET(Reset));
  Binary_to_BCD_Segment binary_to_bcd_segment_3 (
    .out_5(binary_to_bcd_segment_3_out_5), .out_6(_100s), .in_1(binary_to_bcd_segment_4_out_5),
    ._CLR(not_1_out), .WE(shift_register_1_p1), .RESET(Reset));
  Binary_to_BCD_Segment binary_to_bcd_segment_4 (
    .out_5(binary_to_bcd_segment_4_out_5), .out_6(_10s), .in_1(binary_to_bcd_segment_5_out_5),
    ._CLR(not_1_out), .WE(shift_register_1_p1), .RESET(Reset));
  Binary_to_BCD_Segment binary_to_bcd_segment_5 (
    .out_5(binary_to_bcd_segment_5_out_5), .out_6(_1s), .in_1(shift_register_1_p6), ._CLR(not_1_out),
    .WE(shift_register_1_p1), .RESET(Reset));
  // Shift_Register #(.length(16)) shift_register_1: pin names not known; wires that end beside it: shift_register_1_p1, 1'b0, clock_1_out, Load_Start, Reset, shift_register_1_p6
  Subtractor #(.width(5)) subtractor_1 (.a(register_1_q), .b(5'b00001), .out(subtractor_1_out));  // open: bin, bout
  Multiplexer #(.enable("false"), .width(5)) multiplexer_1 (
    .in0(subtractor_1_out), .in1(5'b10000), .out(multiplexer_1_out), .sel(Load_Start));
  or or_1 (or_1_out, Load_Start, shift_register_1_p1);
  Register #(.width(5)) register_1 (
    .D(multiplexer_1_out), .en(or_1_out), .clk(clock_1_out), .Q(register_1_q), .clr(Reset));
  or or_2 (or_2_out, register_1_q[0], register_1_q[1]);
  or or_3 (shift_register_1_p1, or_2_out, or_4_out);
  or or_4 (or_4_out, register_1_q[2], register_1_q[3], register_1_q[4]);
endmodule

module Binary_to_BCD_Segment (
  input  in_1,
  input  _CLR,
  input  WE,
  input  RESET,
  output out_5,
  output [3:0] out_6
);

  wire and_2_out, clock_1_out, not_1_out, or_1_out, or_2_out;
  wire [1:1] or_3_out;
  wire [2:0] adder_1_out;
  wire [3:0] and_1_out, bit_extender_1_out, register_1_q;

  assign and_1_out = {adder_1_out, in_1} & bit_extender_1_out;  // AND_Gate and_1, 4 bits wide
  assign bit_extender_1_out = {{3{_CLR}}, _CLR};  // Bit_Extender bit_extender_1
  not not_1 (not_1_out, _CLR);
  or or_1 (or_1_out, not_1_out, WE);
  Register #(.width(4)) register_1 (.D(and_1_out), .en(or_1_out), .clk(clock_1_out), .Q(register_1_q), .clr(RESET));
  Clock clock_1 (.out(clock_1_out));
  Register #(.trigger("falling"), .width(4)) register_2 (.D(register_1_q), .en(1'b1), .clk(WE), .Q(out_6), .clr(RESET));
  or or_2 (or_2_out, register_1_q[0], register_1_q[1]);
  and and_2 (and_2_out, or_2_out, register_1_q[2]);
  or or_3 (or_3_out[1], and_2_out, register_1_q[3]);
  Adder #(.width(4)) adder_1 (
    .a(register_1_q), .b({2'b00, {2{or_3_out[1]}}}), .out({out_5, adder_1_out}));  // open: cin, cout
endmodule

module Joystick_Processor (
  input  [15:0] Data_In,
  input  Reset,
  input  RE,
  output [15:0] Data_Out,
  output Interrupt
);

  wire clock_1_out, comparator_1_eq;
  wire [15:0] register_1_q, register_2_q;

  Clock clock_1 (.out(clock_1_out));
  Register #(.width(16)) register_1 (.D(Data_In), .en(1'b1), .clk(clock_1_out), .Q(register_1_q), .clr(Reset));
  Register #(.\initial ('h1010), .width(16)) register_2 (
    .D(register_1_q), .en(RE), .clk(clock_1_out), .Q(register_2_q), .clr(Reset));
  assign Data_Out = RE ? register_1_q : 16'bz;  // Controlled_Buffer controlled_buffer_1
  Comparator #(.mode("unsigned"), .width(16)) comparator_1 (
    .a(register_1_q), .b(register_2_q), .eq(comparator_1_eq));  // open: gt, lt
  not not_1 (Interrupt, comparator_1_eq);
endmodule

module Interrupt_Manager (
  input  Source_1,
  input  Source_2,
  input  Source_3,
  input  Source_4,
  input  Source_5,
  input  WE,
  input  [2:0] Register_Select,
  input  Source_6,
  input  RE,
  input  Source_7,
  input  Source_8,
  input  Source_9,
  input  Reset,
  input  Source_10,
  input  [15:0] Data_In,
  input  Source_11,
  input  Source_12,
  input  Source_13,
  input  Source_14,
  input  Source_15,
  output Interrupt,
  output [15:0] Data_Out
);

  wire and_4_out, clock_1_out, clock_2_out, clock_3_out, comparator_1_eq, d_ff_1_q, demultiplexer_1_out0,
       demultiplexer_1_out1, demultiplexer_1_out2, demultiplexer_1_out3, demultiplexer_1_out4,
       demultiplexer_1_out5, demultiplexer_1_out6, demultiplexer_1_out7, demultiplexer_1_out8,
       demultiplexer_1_out9, demultiplexer_1_out10, demultiplexer_1_out11, demultiplexer_1_out12,
       demultiplexer_1_out13, demultiplexer_1_out14, interrupt_latch_1_output, interrupt_latch_2_output,
       interrupt_latch_3_output, interrupt_latch_4_output, interrupt_latch_5_output,
       interrupt_latch_6_output, interrupt_latch_7_output, interrupt_latch_8_output,
       interrupt_latch_9_output, interrupt_latch_10_output, interrupt_latch_11_output,
       interrupt_latch_12_output, interrupt_latch_13_output, interrupt_latch_14_output,
       interrupt_latch_15_output, interrupt_latch_16_output, not_1_out, not_2_out, or_1_out, RE1, RE2, RE3,
       RE4, RE5, RE6, RE7, TC_RESET, TIMER_ZERO, WE0, WE1, WE2, WE3, WE4, WE5;
  wire [3:0] and_3_out, bit_extender_1_out, bit_extender_4_out, priority_encoder_1_out;
  wire [15:0] adder_1_out, and_1_out, and_2_out, and_5_out, bit_extender_2_out, bit_extender_3_out,
       bit_extender_6_out, INT_SOURCE, TC_OUT, TICKS_HI, TICKS_LO, TIMER_HI, TIMER_LO;

  Bit_Extender #(.in_width(16), .out_width(4), .\type ("zero")) bit_extender_1 (.in(Data_In), .out(bit_extender_1_out));
  D_Flip_Flop d_ff_1 (.D(WE0), .clk(clock_1_out), .Q(d_ff_1_q));  // open: Qn, preset, reset
  Clock clock_1 (.out(clock_1_out));
  Demultiplexer #(.enable("false"), .select(4)) demultiplexer_1 (
    .out0(demultiplexer_1_out0), .out1(demultiplexer_1_out1), .out2(demultiplexer_1_out2),
    .out3(demultiplexer_1_out3), .out4(demultiplexer_1_out4), .out5(demultiplexer_1_out5),
    .out6(demultiplexer_1_out6), .out7(demultiplexer_1_out7), .out8(demultiplexer_1_out8),
    .out9(demultiplexer_1_out9), .out10(demultiplexer_1_out10), .out11(demultiplexer_1_out11),
    .out12(demultiplexer_1_out12), .out13(demultiplexer_1_out13), .out14(demultiplexer_1_out14),
    .out15(TC_RESET), .in(d_ff_1_q), .sel(bit_extender_1_out));
  assign and_1_out = Data_In & bit_extender_3_out;  // AND_Gate and_1, 16 bits wide
  assign and_2_out = Data_In & bit_extender_2_out;  // AND_Gate and_2, 16 bits wide
  assign bit_extender_2_out = {{15{WE1}}, WE1};  // Bit_Extender bit_extender_2
  assign bit_extender_3_out = {{15{WE2}}, WE2};  // Bit_Extender bit_extender_3
  Interrupt_Latch interrupt_latch_1 (
    .Source(Source_1), .Reset(demultiplexer_1_out0), .Pin_Reset(Reset), .Enable_Source(and_2_out[0]),
    .Disable_Source(and_1_out[0]), .Output(interrupt_latch_1_output));
  Interrupt_Latch interrupt_latch_2 (
    .Source(Source_2), .Reset(demultiplexer_1_out1), .Pin_Reset(Reset), .Enable_Source(and_2_out[1]),
    .Disable_Source(and_1_out[1]), .Output(interrupt_latch_2_output));
  Interrupt_Latch interrupt_latch_3 (
    .Source(Source_3), .Reset(demultiplexer_1_out2), .Pin_Reset(Reset), .Enable_Source(and_2_out[2]),
    .Disable_Source(and_1_out[2]), .Output(interrupt_latch_3_output));
  Interrupt_Latch interrupt_latch_4 (
    .Source(Source_4), .Reset(demultiplexer_1_out3), .Pin_Reset(Reset), .Enable_Source(and_2_out[3]),
    .Disable_Source(and_1_out[3]), .Output(interrupt_latch_4_output));
  Interrupt_Latch interrupt_latch_5 (
    .Source(Source_5), .Reset(demultiplexer_1_out4), .Pin_Reset(Reset), .Enable_Source(and_2_out[4]),
    .Disable_Source(and_1_out[4]), .Output(interrupt_latch_5_output));
  Interrupt_Latch interrupt_latch_6 (
    .Source(Source_6), .Reset(demultiplexer_1_out5), .Pin_Reset(Reset), .Enable_Source(and_2_out[5]),
    .Disable_Source(and_1_out[5]), .Output(interrupt_latch_6_output));
  Interrupt_Latch interrupt_latch_7 (
    .Source(Source_7), .Reset(demultiplexer_1_out6), .Pin_Reset(Reset), .Enable_Source(and_2_out[6]),
    .Disable_Source(and_1_out[6]), .Output(interrupt_latch_7_output));
  Interrupt_Latch interrupt_latch_8 (
    .Source(Source_8), .Reset(demultiplexer_1_out7), .Pin_Reset(Reset), .Enable_Source(and_2_out[7]),
    .Disable_Source(and_1_out[7]), .Output(interrupt_latch_8_output));
  Interrupt_Latch interrupt_latch_9 (
    .Source(Source_9), .Reset(demultiplexer_1_out8), .Pin_Reset(Reset), .Enable_Source(and_2_out[8]),
    .Disable_Source(and_1_out[8]), .Output(interrupt_latch_9_output));
  Interrupt_Latch interrupt_latch_10 (
    .Source(Source_10), .Reset(demultiplexer_1_out9), .Pin_Reset(Reset), .Enable_Source(and_2_out[9]),
    .Disable_Source(and_1_out[9]), .Output(interrupt_latch_10_output));
  Interrupt_Latch interrupt_latch_11 (
    .Source(Source_11), .Reset(demultiplexer_1_out10), .Pin_Reset(Reset), .Enable_Source(and_2_out[10]),
    .Disable_Source(and_1_out[10]), .Output(interrupt_latch_11_output));
  Interrupt_Latch interrupt_latch_12 (
    .Source(Source_12), .Reset(demultiplexer_1_out11), .Pin_Reset(Reset), .Enable_Source(and_2_out[11]),
    .Disable_Source(and_1_out[11]), .Output(interrupt_latch_12_output));
  Interrupt_Latch interrupt_latch_13 (
    .Source(Source_13), .Reset(demultiplexer_1_out12), .Pin_Reset(Reset), .Enable_Source(and_2_out[12]),
    .Disable_Source(and_1_out[12]), .Output(interrupt_latch_13_output));
  Interrupt_Latch interrupt_latch_14 (
    .Source(Source_14), .Reset(demultiplexer_1_out13), .Pin_Reset(Reset), .Enable_Source(and_2_out[13]),
    .Disable_Source(and_1_out[13]), .Output(interrupt_latch_14_output));
  Interrupt_Latch interrupt_latch_15 (
    .Source(Source_15), .Reset(demultiplexer_1_out14), .Pin_Reset(Reset), .Enable_Source(and_2_out[14]),
    .Disable_Source(and_1_out[14]), .Output(interrupt_latch_15_output));
  Interrupt_Latch interrupt_latch_16 (
    .Source(and_4_out), .Reset(TC_RESET), .Pin_Reset(Reset), .Enable_Source(and_2_out[15]),
    .Disable_Source(and_1_out[15]), .Output(interrupt_latch_16_output));
  Priority_Encoder #(.select(4)) priority_encoder_1 (
    .in0(interrupt_latch_1_output), .in1(interrupt_latch_2_output), .in2(interrupt_latch_3_output),
    .in3(interrupt_latch_4_output), .in4(interrupt_latch_5_output), .in5(interrupt_latch_6_output),
    .in6(interrupt_latch_7_output), .in7(interrupt_latch_8_output), .in8(interrupt_latch_9_output),
    .in9(interrupt_latch_10_output), .in10(interrupt_latch_11_output), .in11(interrupt_latch_12_output),
    .in12(interrupt_latch_13_output), .in13(interrupt_latch_14_output), .in14(interrupt_latch_15_output),
    .in15(interrupt_latch_16_output), .out(priority_encoder_1_out), .gs(Interrupt));  // open: en_out, en_in
  Clock clock_2 (.out(clock_2_out));
  assign bit_extender_4_out = {{3{Interrupt}}, Interrupt};  // Bit_Extender bit_extender_4
  Register #(.width(16)) register_1 (.D(Data_In), .en(WE4), .clk(clock_2_out), .Q(TIMER_LO), .clr(Reset));
  Register #(.width(16)) register_2 (.D(Data_In), .en(WE5), .clk(clock_2_out), .Q(TIMER_HI), .clr(Reset));
  assign and_3_out = priority_encoder_1_out & bit_extender_4_out;  // AND_Gate and_3, 4 bits wide
  assign INT_SOURCE = {{11{1'b0}}, {Interrupt, and_3_out}};  // Bit_Extender bit_extender_5
  not not_1 (not_1_out, comparator_1_eq);
  Comparator #(.mode("unsigned"), .width(32)) comparator_1 (
    .a({TIMER_HI, TIMER_LO}), .b({32{1'b0}}), .eq(comparator_1_eq));  // open: gt, lt
  Interrupt_Counter Timer (
    .DEC(1'b1), .Reset_Value({TIMER_HI, TIMER_LO}), .WE(not_1_out), .RE_Low(1'b0), .RE_High(1'b0),
    .Reset(Reset), .Zero(TIMER_ZERO));  // open: Output_Low, Output_High
  and and_4 (and_4_out, not_1_out, TIMER_ZERO);
  Interrupt_Counter Ticks (
    .DEC(1'b0), .Reset_Value({32{1'b0}}), .WE(TIMER_ZERO), .RE_Low(RE6), .RE_High(RE7), .Reset(Reset),
    .Output_Low(TICKS_LO), .Output_High(TICKS_HI));  // open: Zero
  not not_2 (not_2_out, TC_RESET);
  Adder #(.width(16)) adder_1 (.a(TC_OUT), .b({16{1'b0}}), .out(adder_1_out), .cin(1'b1));  // open: cout
  assign bit_extender_6_out = {{15{not_2_out}}, not_2_out};  // Bit_Extender bit_extender_6
  or or_1 (or_1_out, TC_RESET, TIMER_ZERO);
  Demultiplexer #(.enable("false"), .select(3)) demultiplexer_2 (
    .out0(WE0), .out1(WE1), .out2(WE2), .out3(WE3), .out4(WE4), .out5(WE5), .in(WE), .sel(Register_Select));  // open: out6, out7
  Demultiplexer #(.enable("false"), .select(3)) demultiplexer_3 (
    .out1(RE1), .out2(RE2), .out3(RE3), .out4(RE4), .out5(RE5), .out6(RE6), .out7(RE7), .in(RE),
    .sel(Register_Select));  // open: out0
  Register #(.width(16)) register_3 (.D(and_5_out), .en(or_1_out), .clk(clock_3_out), .Q(TC_OUT), .clr(Reset));
  assign and_5_out = adder_1_out & bit_extender_6_out;  // AND_Gate and_5, 16 bits wide
  Clock clock_3 (.out(clock_3_out));
  Multiplexer #(.disabled("Z"), .select(3), .width(16)) multiplexer_1 (
    .in0(INT_SOURCE), .in3(TC_OUT), .in4(TIMER_LO), .in5(TIMER_HI), .in6(TICKS_LO), .in7(TICKS_HI),
    .out(Data_Out), .sel(Register_Select), .en(RE));  // open: in1, in2

  // Other names for the same wires on the sheet: DATA_EN[15:0] = Data_In; PIN_RESET = Reset;
  //   RS[2:0] = Register_Select

  // Notes on the sheet:
  //   Registers:
  //   	0:	Source Index (R/W)
  //   	1:	Enable Source (W)
  //   	2:	Disable Source (W)
  //   	3:	Missed Ticks (R)
  //   	4:	Timer Low (R/W)
  //   	5:	Timer High (R/W)
  //   	6:	Ticks Low (R)
  //   	7:	Ticks High (R)
  //   Write Response:
  //   	0:	Clear Selected Interrupt
  //   Read Response:
  //   	0:	Read Source Index
endmodule

module Interrupt_Latch (
  input  Source,
  input  Reset,
  input  Pin_Reset,
  input  Enable_Source,
  input  Disable_Source,
  output Output
);

  wire and_1_out, clock_1_out, d_ff_1_qn, d_ff_2_q, d_ff_2_qn, multiplexer_1_out, multiplexer_2_out,
       or_1_out, or_2_out, or_3_out;

  and and_1 (and_1_out, d_ff_2_q, d_ff_1_qn);
  or or_1 (or_1_out, Reset, Pin_Reset);
  or or_2 (or_2_out, Enable_Source, Disable_Source);
  D_Flip_Flop d_ff_1 (
    .D(multiplexer_1_out), .clk(clock_1_out), .Q(Output), .Qn(d_ff_1_qn), .reset(or_3_out));  // open: preset
  Multiplexer #(.enable("false")) multiplexer_1 (.in0(Output), .in1(Source), .out(multiplexer_1_out), .sel(and_1_out));
  Clock clock_1 (.out(clock_1_out));
  or or_3 (or_3_out, or_1_out, d_ff_2_qn);
  D_Flip_Flop d_ff_2 (
    .D(multiplexer_2_out), .clk(clock_1_out), .Q(d_ff_2_q), .Qn(d_ff_2_qn), .reset(Pin_Reset));  // open: preset
  Multiplexer #(.enable("false")) multiplexer_2 (
    .in0(d_ff_2_q), .in1(Enable_Source), .out(multiplexer_2_out), .sel(or_2_out));
endmodule

module Interrupt_Counter (
  input  DEC,
  input  [31:0] Reset_Value,
  input  WE,
  input  RE_Low,
  input  RE_High,
  input  Reset,
  output Zero,
  output [15:0] Output_Low,
  output [15:0] Output_High
);

  wire adder_1_cout, and_1_out, and_2_out, and_3_out, and_4_out, and_5_out, clock_1_out, clock_2_out,
       d_ff_1_q, d_ff_1_qn, d_ff_2_q, d_ff_2_qn, nor_1_out, not_1_out, not_2_out, or_1_out, or_2_out,
       xnor_1_out;
  wire [31:0] adder_1_out, bit_extender_1_out, multiplexer_1_out, register_1_q;

  and and_1 (and_1_out, RE_Low, not_1_out);
  Clock clock_1 (.out(clock_1_out));
  not not_1 (not_1_out, and_3_out);
  and and_2 (and_2_out, not_1_out, RE_High);
  D_Flip_Flop #(.enable("true")) d_ff_1 (
    .D(and_1_out), .clk(clock_1_out), .Q(d_ff_1_q), .Qn(d_ff_1_qn));  // open: preset, reset
  or or_1 (or_1_out, and_3_out, d_ff_1_qn);
  D_Flip_Flop #(.enable("true")) d_ff_2 (
    .D(and_2_out), .clk(clock_1_out), .Q(d_ff_2_q), .Qn(d_ff_2_qn));  // open: preset, reset
  or or_2 (or_2_out, and_3_out, d_ff_2_qn);
  nor nor_1 (nor_1_out, RE_Low, RE_High);
  and and_3 (and_3_out, d_ff_2_q, d_ff_1_q);
  assign bit_extender_1_out = {{31{DEC}}, DEC};  // Bit_Extender bit_extender_1
  xnor xnor_1 (xnor_1_out, d_ff_1_q, d_ff_2_q);
  and and_4 (and_4_out, xnor_1_out, nor_1_out);
  and and_5 (and_5_out, xnor_1_out, nor_1_out);
  not not_2 (not_2_out, DEC);
  Adder #(.width(32)) adder_1 (
    .a(register_1_q), .b(bit_extender_1_out), .out(adder_1_out), .cin(not_2_out), .cout(adder_1_cout));
  Comparator #(.mode("unsigned"), .width(32)) comparator_1 (
    .a(adder_1_out), .b({32{1'b0}}), .eq(Zero));  // open: gt, lt
  Multiplexer #(.enable("false"), .width(32)) multiplexer_1 (
    .in0(Reset_Value), .in1(adder_1_out), .out(multiplexer_1_out), .sel(adder_1_cout));
  Clock clock_2 (.out(clock_2_out));
  Register #(.width(32)) register_1 (.D(multiplexer_1_out), .en(WE), .clk(clock_2_out), .Q(register_1_q), .clr(Reset));
  Register #(.width(16)) register_2 (
    .D(adder_1_out[15:0]), .en(and_4_out), .clk(clock_2_out), .Q(Output_Low), .clr(Reset));
  Register #(.width(16)) register_3 (
    .D(adder_1_out[31:16]), .en(and_5_out), .clk(clock_2_out), .Q(Output_High), .clr(Reset));
endmodule
